// Logisim project cpu21-riscv.circ as structural Verilog: 23 circuits, main circuit ◇单周期RISC-V
module \单周期RISC_V  (
  input  IR1,
  input  IR2,
  input  IR3,
  output RegWrite,
  output MemWrite,
  output [31:0] PC,
  output [31:0] IR,
  output [31:0] RDin,
  output [31:0] MDin,
  output [31:0] LedData
);

  wire AluSrcB, and_1_out, and_2_out, and_3_out, and_4_out, and_5_out, Beq, Bge, Bne, Branch, CLK,
       clock_1_out, comparator_1_eq, comparator_2_eq, comparator_2_lt, d_ff_2_q, ecall, Equal, Ge, Go, halt,
       IR1_t, IR2_t, IR3_t, IRA, IRB, IRC, JAL, JALR, Less, Lh, MemToReg, nand_1_out, not_1_out, not_2_out,
       not_3_out, or_5_out, RST, S_type, URET, W1, W2, W3;
  wire [1:0] priority_encoder_1_out;
  wire [3:0] AluOP;
  wire [4:0] multiplexer_2_out, multiplexer_3_out;
  wire [12:0] CNT_num;
  wire [15:0] multiplexer_7_out, \总周期数 ;
  wire [31:0] adder_2_out, adder_3_out, AluResult, bit_extender_1_out, bit_extender_2_out,
       bit_extender_3_out, bit_extender_4_out, HalfMemData, MemData, multiplexer_1_out, multiplexer_4_out,
       multiplexer_5_out, multiplexer_6_out, multiplexer_8_out, PC_4, R1Data, shifter_1_out, shifter_2_out;

  Button \u_继续运行  (.out(Go));
  Button _1 (.out(IRA));
  Button _2 (.out(IRB));
  Button _3 (.out(IRC));
  Button \u_总复位  (.out(RST));
  LED #(.active("true")) led_1 (.in(W1));
  LED #(.active("true")) led_2 (.in(W2));
  LED #(.active("true")) led_3 (.in(W3));
  Hex_Digit_Display hex_digit_display_1 (.value(LedData[31:28]));  // open: dp
  and and_1 (and_1_out, Beq, Equal);
  and and_2 (and_2_out, ~Equal, Bne);  // AND_Gate
  and and_3 (and_3_out, Bge, Ge);
  Priority_Encoder #(.select(2), .disabled("Z")) priority_encoder_1 (
    .in0(1'b1), .in1(JALR), .in2(JAL), .in3(Branch), .out(priority_encoder_1_out));  // open: gs, en_out, en_in
  Multiplexer #(.select(2), .width(32), .disabled("Z"), .enable("false")) multiplexer_1 (
    .in0(PC_4), .in1(AluResult), .in2(adder_3_out), .in3(adder_2_out), .out(multiplexer_1_out),
    .sel(priority_encoder_1_out));
  not not_1 (not_1_out, halt);
  Hex_Digit_Display hex_digit_display_2 (.value(LedData[23:20]));  // open: dp
  Hex_Digit_Display hex_digit_display_3 (.value(LedData[27:24]));  // open: dp
  or or_1 (Branch, and_1_out, and_2_out, and_3_out);
  Register #(.width(32), .trigger("rising"), .Select("low")) u_PC (
    .D(multiplexer_1_out), .en(not_1_out), .Q(PC), .clk(CLK), .clr(RST));
  Hex_Digit_Display hex_digit_display_4 (.value(LedData[15:12]));  // open: dp
  Hex_Digit_Display hex_digit_display_5 (.value(LedData[19:16]));  // open: dp
  Hex_Digit_Display hex_digit_display_6 (.value(LedData[7:4]));  // open: dp
  Hex_Digit_Display hex_digit_display_7 (.value(LedData[11:8]));  // open: dp
  // Probe on \总周期数 
  // RiscV_Probe riscv_probe_1: pin names not known; wires that end beside it: IR
  ROM #(.addrWidth(10), .dataWidth(32), .Select("high")) rom_1 (.addr(PC[11:2]), .data(IR));
  Adder #(.width(32)) adder_1 (.a(PC), .b(32'h4), .out(PC_4));  // open: cin, cout
  Hex_Digit_Display hex_digit_display_8 (.value(LedData[3:0]));  // open: dp
  \单周期硬布线控制器  \u_单周期硬布线控制器_1  (
    .Funct({IR[30], IR[25], IR[14:12]}), .OP(IR[6:2]), .ALU_OP(AluOP), .MemToReg(MemToReg),
    .MemWrite(MemWrite), .ALU_SRC(AluSrcB), .RegWrite(RegWrite), .ecall(ecall), .S_type(S_type), .Jalr(JALR),
    .Beq(Beq), .JAL(JAL), .Bne(Bne), .in_3(IR[21]), .uret(URET), .Lh(Lh), .Bge(Bge));  // open: RS1Used, RS2Used, CSR
  Multiplexer #(.select(1), .width(5), .disabled("Z"), .enable("false")) multiplexer_2 (
    .in0(IR[19:15]), .in1(5'b10001), .out(multiplexer_2_out), .sel(ecall));
  Multiplexer #(.select(1), .width(5), .disabled("Z"), .enable("false")) multiplexer_3 (
    .in0(IR[24:20]), .in1(5'b01010), .out(multiplexer_3_out), .sel(ecall));
  or or_2 (IR1_t, IR1, IRA);
  assign bit_extender_1_out = {{20{IR[31]}}, IR[31:20]};  // Bit_Extender bit_extender_1
  assign bit_extender_2_out = {{20{IR[31]}}, {IR[31:25], IR[11:7]}};  // Bit_Extender bit_extender_2
  assign bit_extender_3_out = {{20{IR[31]}}, {IR[31], IR[7], IR[30:25], IR[11:8]}};  // Bit_Extender bit_extender_3
  assign bit_extender_4_out = {{12{IR[31]}}, {IR[31], IR[19:12], IR[20], IR[30:21]}};  // Bit_Extender bit_extender_4
  or or_3 (IR2_t, IR2, IRB);
  Multiplexer #(.select(1), .width(32), .disabled("Z"), .enable("false")) multiplexer_4 (
    .in0(bit_extender_1_out), .in1(bit_extender_2_out), .out(multiplexer_4_out), .sel(S_type));
  Shifter #(.width(32), .shift("ll")) shifter_1 (.in(bit_extender_3_out), .\dist (5'b00001), .out(shifter_1_out));
  Shifter #(.width(32), .shift("ll")) shifter_2 (.in(bit_extender_4_out), .\dist (5'b00001), .out(shifter_2_out));
  Regifile regifile_1 (
    .Din(RDin), .Clk(CLK), .R1(R1Data), .R2(MDin), .WE(RegWrite), .W_num(IR[11:7]),
    .R1_num(multiplexer_2_out), .R2_num(multiplexer_3_out));
  or or_4 (IR3_t, IR3, IRC);
  Multiplexer #(.select(1), .width(32), .disabled("Z"), .enable("false")) multiplexer_5 (
    .in0(MDin), .in1(multiplexer_4_out), .out(multiplexer_5_out), .sel(AluSrcB));
  Adder #(.width(32)) adder_2 (.a(shifter_1_out), .b(PC), .out(adder_2_out));  // open: cin, cout
  Adder #(.width(32)) adder_3 (.a(shifter_2_out), .b(PC), .out(adder_3_out));  // open: cin, cout
  not not_2 (not_2_out, halt);
  Counter #(.width(16), .max('hffff), .ongoal("wrap"), .trigger("rising"), .behavior("new")) counter_1 (
    .count(not_2_out), .Q(\总周期数 ), .clk(CLK), .clr(RST));  // open: load, D, carry, preset, down
  ALU alu_1 (
    .X(R1Data), .Y(multiplexer_5_out), .AluOP(AluOP), .Equal(Equal), .Result(AluResult), .out_4(Ge),
    .out_6(Less));  // open: Result_2
  Comparator #(.width(32), .mode("twosComplement")) comparator_1 (
    .a(R1Data), .b(32'h22), .eq(comparator_1_eq));  // open: gt, lt
  and and_4 (and_4_out, ecall, ~comparator_1_eq);  // AND_Gate
  and and_5 (and_5_out, comparator_1_eq, ecall);
  D_Flip_Flop #(.trigger("falling"), .Pre_Clr_Positions("ABOVE_BELOW"), .NegatePresetClear("false"), .enable("true"), .NewFFLayout("true")) d_ff_1 (
    .clk(CLK), .D(and_4_out), .Q(halt), .en(ecall), .reset(Go));  // open: Qn, preset
  Register #(.width(32), .trigger("rising"), .Select("low")) register_1 (
    .D(MDin), .en(and_5_out), .Q(LedData), .clk(CLK), .clr(RST));
  not not_3 (not_3_out, MemWrite);
  RAM #(.addrWidth(10), .dataWidth(32), .bus("separate"), .Select("high")) ram_1 (
    .addr(AluResult[11:2]), .din(MDin), .data(MemData), .str(MemWrite), .clk(CLK), .ld(not_3_out));  // open: sel, clr
  D_Flip_Flop #(.trigger("high"), .Pre_Clr_Positions("LEGACY"), .NegatePresetClear("false"), .enable("true"), .NewFFLayout("false")) d_ff_2 (.Q(d_ff_2_q));  // open: clk, D, Qn, preset, en, reset
  // Probe on 13'ha
  Multiplexer #(.select(1), .width(32), .disabled("Z"), .enable("false")) multiplexer_6 (
    .in0(MemData), .in1(HalfMemData), .out(multiplexer_6_out), .sel(Lh));
  Multiplexer #(.select(1), .width(16), .disabled("Z"), .enable("false")) multiplexer_7 (
    .in0(MemData[15:0]), .in1(MemData[31:16]), .out(multiplexer_7_out), .sel(AluResult[1]));
  Comparator #(.width(13), .mode("twosComplement")) comparator_2 (
    .a(CNT_num), .b(13'ha), .eq(comparator_2_eq), .lt(comparator_2_lt));  // open: gt
  Clock #(.highDuration(1), .lowDuration(1)) clock_1 (.out(clock_1_out));
  Multiplexer #(.select(1), .width(32), .disabled("Z"), .enable("false")) multiplexer_8 (
    .in0(AluResult), .in1(multiplexer_6_out), .out(multiplexer_8_out), .sel(MemToReg));
  assign HalfMemData = {{16{multiplexer_7_out[15]}}, multiplexer_7_out};  // Bit_Extender bit_extender_5
  Counter #(.width(13), .max('h1fff), .ongoal("stay"), .trigger("rising"), .behavior("old")) counter_2 (
    .count(comparator_2_lt), .Q(CNT_num), .clk(clock_1_out));  // open: load, D, carry, clr, preset
  or or_5 (or_5_out, JAL, JALR);
  nand nand_1 (nand_1_out, d_ff_2_q, comparator_2_eq);
  Multiplexer #(.select(1), .width(32), .disabled("Z"), .enable("false")) multiplexer_9 (
    .in0(multiplexer_8_out), .in1(PC_4), .out(RDin), .sel(or_5_out));
  assign CLK = nand_1_out ? clock_1_out : 1'bz;  // Controlled_Buffer controlled_buffer_1
  Pull_Resistor #(.pull(1)) pull_resistor_1 (.node(CLK));

  // Other names for the same wires on the sheet: BitSel[1:0] = AluResult[1:0]

  // Notes on the sheet:
  //   中断源
  //   中断等待指示
  //   数码管输出应该用寄存器锁存，否则显示数据只能一闪而过
  //   数码管输出
  //   指令探针
  //   指令存储器
  //   contents of rom_1 (hex, n*v repeats v):
  //   100493 100006f 100493 200913 300993 100006f 100493 200913 300993 100006f 100493 200913 300993
  //   100006f 100493 200913 300993 3c8000ef 100413 100493 1f49493 900533 2200893 73 24d493 48463 fedff06f
  //   900533 2200893 73 100493 249493 900533 2200893 73 48463 fedff06f 100493 1f49493 900533 2200893 73
  //   4034d493 900533 2200893 73 4044d493 900533 2200893 73 4044d493 900533 2200893 73 4044d493 900533
  //   2200893 73 4044d493 900533 2200893 73 4044d493 900533 2200893 73 4044d493 900533 2200893 73 4044d493
  //   900533 2200893 73 100413 1f41993 41f9d993 433 c00913 300b13 140413 f47413 800293 100313 499993
  //   89e9b3 1300533 2200893 73 406282b3 fe0294e3 140413 f00f93 1f47433 1c41413 800293 100313 49d993
  //   89e9b3 1300533 2200893 73 406282b3 fe0294e3 1c45413 406b0b33 b0463 f95ff06f 2b3 fff2c293 829293
  //   ff2e293 500533 2200893 73 fff00413 493 84a023 140413 448493 84a023 140413 448493 84a023 140413
  //   448493 84a023 140413 448493 84a023 140413 448493 84a023 140413 448493 84a023 140413 448493 84a023
  //   140413 448493 84a023 140413 448493 84a023 140413 448493 84a023 140413 448493 84a023 140413 448493
  //   84a023 140413 448493 84a023 140413 448493 84a023 140413 448493 84a023 140413 448493 140413 433
  //   3c00493 42983 4aa03 149a2b3 28663 134a023 1442023 ffc48493 fe9412e3 800533 2200893 73 440413 3c00493
  //   fc9416e3 a00893 73 100293 300313 800493 849493 7648493 1449493 900533 2200893 73 800e13 4054d4b3
  //   4064d4b3 900533 2200893 73 fffe0e13 fe0e14e3 a00893 73 fff00293 7700493 849493 7748493 900533
  //   2200893 73 1000e13 54c4b3 900533 2200893 73 fffe0e13 fe0e16e3 a00893 73 313 1000e13 8400493 849493
  //   8348493 400913 891913 490913 849493 8248493 849493 8148493 891913 490913 891913 490913 932023
  //   12484b3 430313 fffe0e13 fe0e18e3 2000e13 313 31483 900533 2200893 73 230313 fffe0e13 fe0e14e3 a00893
  //   73 f00493 900533 2200893 73 fff48493 fe04d8e3 a00893 73 413 140413 800533 2200893 73 240413 800533
  //   2200893 73 340413 800533 2200893 73 440413 800533 2200893 73 540413 800533 2200893 73 640413 800533
  //   2200893 73 740413 800533 2200893 73 840413 800533 2200893 2200893 73 8067
  //   指令字
  //   JAL
  //   JALR
  //   URET
  //   ecall
  //   I型指令立即数 
  //   S型指令立即数 
  //   B型指令立即数 
  //   J型指令立即数 
  //   Bne
  //   MemToReg
  //   MemWrite
  //   AluOP
  //   AluSrcB
  //   RegWrite
  //   S_type
  //   为方便自动评测，需要输出PC，IR，寄存器堆写如数据RDin
  //   RAM写使能MemWrite、RAM写入数据MDin等信号
  //   数据存储器
  //   控制位
  //   暂停节拍，不能为0
  //   戳工具置1进入计数暂停模式，ctrl+k时钟自动运行到对应节拍暂停
  //   ctrl+k关闭时钟连续运行，将控制位置零，进入单步调试模式调试
  //   用这个时钟源需要去掉电路中的其他时钟源
  //   可计数暂停的时钟源
endmodule

// 单周期硬布线控制器
module \单周期硬布线控制器  (
  input  [4:0] OP,
  input  [4:0] Funct,
  input  in_3,
  output [3:0] ALU_OP,
  output uret,
  output MemToReg,
  output ecall,
  output MemWrite,
  output ALU_SRC,
  output RegWrite,
  output S_type,
  output Beq,
  output Bne,
  output Jalr,
  output JAL,
  output Lh,
  output Bge,
  output RS2Used,
  output RS1Used,
  output CSR
);

  wire \控制信号自动生成_1_ecall ;

  \运算控制器自动生成  \u_运算控制器自动生成_1  (
    .OP2(OP[0]), .OP3(OP[1]), .OP4(OP[2]), .OP5(OP[3]), .OP6(OP[4]), .F12(Funct[0]), .F13(Funct[1]),
    .F14(Funct[2]), .F25(Funct[3]), .F30(Funct[4]), .S0(ALU_OP[0]), .S1(ALU_OP[1]), .S2(ALU_OP[2]),
    .S3(ALU_OP[3]));
  \控制信号自动生成  \u_控制信号自动生成_1  (
    .OP2(OP[0]), .OP3(OP[1]), .OP4(OP[2]), .OP5(OP[3]), .OP6(OP[4]), .MemToReg(MemToReg), .F12(Funct[0]),
    .F13(Funct[1]), .F14(Funct[2]), .F25(Funct[3]), .F30(Funct[4]), .MemWrite(MemWrite), .ALU_SRC(ALU_SRC),
    .RegWrite(RegWrite), .ecall(\控制信号自动生成_1_ecall ), .S_Type(S_type), .BEQ(Beq), .BNE(Bne), .JALR(Jalr),
    .JAL(JAL), .LH(Lh), .BGE(Bge), .RS1Used(RS1Used), .RS2Used(RS2Used), .CSR(CSR));
  and and_1 (uret, in_3, \控制信号自动生成_1_ecall );
  and and_2 (ecall, ~in_3, \控制信号自动生成_1_ecall );  // AND_Gate

  // Other names for the same wires on the sheet: IR21 = in_3; OP_CODE[4:0] = OP

  // Notes on the sheet:
  //   运算器控制器，根据指令生成运算器功能选择信号
  //   控制信号生成，产生数据通路需要的其他控制信号
endmodule

// 运算器控制器
module \运算控制器自动生成  (
  input  OP2,
  input  OP3,
  input  OP4,
  input  OP5,
  input  OP6,
  input  F12,
  input  F13,
  input  F14,
  input  F25,
  input  F30,
  output S0,
  output S1,
  output S2,
  output S3
);

  wire and_1_out, and_2_out, and_3_out, and_4_out, and_5_out, and_6_out, and_7_out, and_8_out, and_9_out,
       and_10_out, and_11_out, and_12_out, and_13_out, and_14_out, and_15_out, and_16_out, and_17_out,
       and_18_out, and_19_out, and_20_out, and_21_out, and_22_out, and_23_out, and_24_out, and_25_out,
       and_26_out, and_27_out, and_28_out, and_29_out, and_30_out, and_31_out, and_32_out, and_33_out,
       and_34_out, and_35_out, and_36_out, and_37_out, and_38_out, and_39_out, and_40_out, and_41_out,
       and_42_out, and_43_out, and_44_out, not_1_out, not_2_out, not_3_out, not_4_out, not_5_out, not_6_out,
       not_7_out, not_8_out, not_9_out, not_10_out, not_11_out, not_12_out, not_13_out, not_14_out,
       not_15_out, not_16_out, not_17_out, not_18_out, not_19_out, not_20_out, not_21_out, not_22_out,
       not_23_out, not_24_out, not_25_out, not_26_out, not_27_out, not_28_out, not_29_out, not_30_out,
       not_31_out, not_32_out, not_33_out, not_34_out, not_35_out, not_36_out, not_37_out, not_38_out,
       not_39_out, not_40_out, not_41_out, not_42_out, not_43_out, not_44_out, not_45_out, not_46_out,
       not_47_out, not_48_out, not_49_out, not_50_out, not_51_out, not_52_out, not_53_out, not_54_out,
       not_55_out, not_56_out, not_57_out, not_58_out, not_59_out, not_60_out, not_61_out, not_62_out,
       not_63_out, not_64_out, not_65_out, not_66_out, not_67_out, not_68_out, not_69_out, not_70_out,
       not_71_out, not_72_out, not_73_out, not_74_out, not_75_out, not_76_out, not_77_out, not_78_out,
       not_79_out, not_80_out, not_81_out, not_82_out, not_83_out, not_84_out, not_85_out, not_86_out,
       not_87_out, not_88_out, not_89_out, not_90_out, not_91_out, not_92_out, not_93_out, not_94_out,
       not_95_out, not_96_out, not_97_out, not_98_out, not_99_out, not_100_out, not_101_out, not_102_out,
       not_103_out, not_104_out, not_105_out, not_106_out, not_107_out, not_108_out, not_109_out,
       not_110_out, not_111_out, not_112_out, not_113_out, not_114_out, not_115_out, not_116_out,
       not_117_out, not_118_out, not_119_out, not_120_out, not_121_out, not_122_out, not_123_out,
       not_124_out, not_125_out, not_126_out, not_127_out, not_128_out, not_129_out, not_130_out,
       not_131_out, not_132_out, not_133_out, not_134_out, not_135_out, not_136_out, not_137_out,
       not_138_out, not_139_out, not_140_out, not_141_out, not_142_out, not_143_out, not_144_out,
       not_145_out, not_146_out, not_147_out, not_148_out, not_149_out, not_150_out, not_151_out,
       not_152_out, not_153_out, not_154_out, not_155_out, not_156_out, not_157_out, not_158_out,
       not_159_out, not_160_out, not_161_out, not_162_out, not_163_out, not_164_out, not_165_out,
       not_166_out, not_167_out, not_168_out, not_169_out, not_170_out, not_171_out, not_172_out,
       not_173_out, not_174_out, not_175_out, not_176_out, not_177_out, not_178_out, not_179_out,
       not_180_out, not_181_out, not_182_out, not_183_out, not_184_out, not_185_out, not_186_out,
       not_187_out, not_188_out, not_189_out, not_190_out, not_191_out, not_192_out, not_193_out,
       not_194_out, not_195_out, not_196_out, not_197_out, not_198_out, not_199_out, not_200_out,
       not_201_out, not_202_out, not_203_out, not_204_out, not_205_out, not_206_out, not_207_out,
       not_208_out, not_209_out, not_210_out, not_211_out, not_212_out, not_213_out, not_214_out,
       not_215_out, not_216_out, not_217_out, not_218_out, not_219_out, not_220_out, not_221_out,
       not_222_out, not_223_out, not_224_out, not_225_out, not_226_out, not_227_out, not_228_out,
       not_229_out, not_230_out, not_231_out, not_232_out, not_233_out, not_234_out, not_235_out,
       not_236_out, not_237_out, not_238_out, not_239_out, not_240_out, not_241_out, not_242_out,
       not_243_out, not_244_out, not_245_out, not_246_out, not_247_out, not_248_out, not_249_out,
       not_250_out, not_251_out, not_252_out, not_253_out, not_254_out, not_255_out, not_256_out,
       not_257_out, not_258_out, not_259_out, not_260_out, not_261_out;

  not not_1 (not_1_out, F30);
  not not_2 (not_2_out, F25);
  not not_3 (not_3_out, F14);
  not not_4 (not_4_out, F13);
  not not_5 (not_5_out, F12);
  not not_6 (not_6_out, OP6);
  not not_7 (not_7_out, OP3);
  not not_8 (not_8_out, OP2);
  not not_9 (not_9_out, F30);
  not not_10 (not_10_out, F25);
  not not_11 (not_11_out, OP6);
  not not_12 (not_12_out, OP3);
  not not_13 (not_13_out, OP2);
  not not_14 (not_14_out, F30);
  not not_15 (not_15_out, F25);
  not not_16 (not_16_out, F14);
  not not_17 (not_17_out, F12);
  not not_18 (not_18_out, OP6);
  not not_19 (not_19_out, OP3);
  not not_20 (not_20_out, OP2);
  not not_21 (not_21_out, F14);
  not not_22 (not_22_out, F13);
  not not_23 (not_23_out, F12);
  not not_24 (not_24_out, OP6);
  not not_25 (not_25_out, OP5);
  not not_26 (not_26_out, OP3);
  not not_27 (not_27_out, OP2);
  not not_28 (not_28_out, OP6);
  not not_29 (not_29_out, OP5);
  not not_30 (not_30_out, OP3);
  not not_31 (not_31_out, OP2);
  not not_32 (not_32_out, F13);
  not not_33 (not_33_out, F12);
  not not_34 (not_34_out, OP6);
  not not_35 (not_35_out, OP5);
  not not_36 (not_36_out, OP3);
  not not_37 (not_37_out, OP2);
  not not_38 (not_38_out, F14);
  not not_39 (not_39_out, F12);
  not not_40 (not_40_out, OP6);
  not not_41 (not_41_out, OP5);
  not not_42 (not_42_out, OP3);
  not not_43 (not_43_out, OP2);
  not not_44 (not_44_out, F25);
  not not_45 (not_45_out, F13);
  not not_46 (not_46_out, OP6);
  not not_47 (not_47_out, OP5);
  not not_48 (not_48_out, OP3);
  not not_49 (not_49_out, OP2);
  not not_50 (not_50_out, F14);
  not not_51 (not_51_out, F12);
  not not_52 (not_52_out, OP6);
  not not_53 (not_53_out, OP5);
  not not_54 (not_54_out, OP4);
  not not_55 (not_55_out, OP3);
  not not_56 (not_56_out, OP2);
  not not_57 (not_57_out, F14);
  not not_58 (not_58_out, F12);
  not not_59 (not_59_out, OP6);
  not not_60 (not_60_out, OP4);
  not not_61 (not_61_out, OP3);
  not not_62 (not_62_out, OP2);
  not not_63 (not_63_out, F14);
  not not_64 (not_64_out, F13);
  not not_65 (not_65_out, F12);
  not not_66 (not_66_out, OP4);
  not not_67 (not_67_out, OP3);
  not not_68 (not_68_out, F25);
  not not_69 (not_69_out, F13);
  not not_70 (not_70_out, OP6);
  not not_71 (not_71_out, OP3);
  not not_72 (not_72_out, OP2);
  not not_73 (not_73_out, F30);
  not not_74 (not_74_out, F25);
  not not_75 (not_75_out, F13);
  not not_76 (not_76_out, F12);
  not not_77 (not_77_out, OP6);
  not not_78 (not_78_out, OP3);
  not not_79 (not_79_out, OP2);
  not not_80 (not_80_out, F14);
  not not_81 (not_81_out, F13);
  not not_82 (not_82_out, OP6);
  not not_83 (not_83_out, OP5);
  not not_84 (not_84_out, OP4);
  not not_85 (not_85_out, OP3);
  not not_86 (not_86_out, OP2);
  not not_87 (not_87_out, F13);
  not not_88 (not_88_out, OP4);
  not not_89 (not_89_out, OP3);
  not not_90 (not_90_out, OP2);
  not not_91 (not_91_out, F25);
  not not_92 (not_92_out, F14);
  not not_93 (not_93_out, F13);
  not not_94 (not_94_out, F12);
  not not_95 (not_95_out, OP6);
  not not_96 (not_96_out, OP3);
  not not_97 (not_97_out, OP2);
  not not_98 (not_98_out, F30);
  not not_99 (not_99_out, F25);
  not not_100 (not_100_out, OP6);
  not not_101 (not_101_out, OP3);
  not not_102 (not_102_out, OP2);
  not not_103 (not_103_out, F30);
  not not_104 (not_104_out, F25);
  not not_105 (not_105_out, F14);
  not not_106 (not_106_out, F12);
  not not_107 (not_107_out, OP6);
  not not_108 (not_108_out, OP3);
  not not_109 (not_109_out, OP2);
  not not_110 (not_110_out, OP6);
  not not_111 (not_111_out, OP5);
  not not_112 (not_112_out, OP3);
  not not_113 (not_113_out, OP2);
  not not_114 (not_114_out, F14);
  not not_115 (not_115_out, F12);
  not not_116 (not_116_out, OP6);
  not not_117 (not_117_out, OP5);
  not not_118 (not_118_out, OP3);
  not not_119 (not_119_out, OP2);
  not not_120 (not_120_out, F30);
  not not_121 (not_121_out, F25);
  not not_122 (not_122_out, F13);
  not not_123 (not_123_out, OP6);
  not not_124 (not_124_out, OP5);
  not not_125 (not_125_out, OP3);
  not not_126 (not_126_out, OP2);
  not not_127 (not_127_out, F14);
  not not_128 (not_128_out, F13);
  not not_129 (not_129_out, F12);
  not not_130 (not_130_out, OP4);
  not not_131 (not_131_out, OP3);
  not not_132 (not_132_out, OP2);
  not not_133 (not_133_out, F14);
  not not_134 (not_134_out, F13);
  not not_135 (not_135_out, OP4);
  not not_136 (not_136_out, OP3);
  not not_137 (not_137_out, OP2);
  not not_138 (not_138_out, F13);
  not not_139 (not_139_out, OP4);
  not not_140 (not_140_out, OP3);
  not not_141 (not_141_out, OP2);
  not not_142 (not_142_out, F30);
  not not_143 (not_143_out, F25);
  not not_144 (not_144_out, F14);
  not not_145 (not_145_out, F13);
  not not_146 (not_146_out, F12);
  not not_147 (not_147_out, OP6);
  not not_148 (not_148_out, OP3);
  not not_149 (not_149_out, OP2);
  not not_150 (not_150_out, F25);
  not not_151 (not_151_out, F14);
  not not_152 (not_152_out, F13);
  not not_153 (not_153_out, F12);
  not not_154 (not_154_out, OP6);
  not not_155 (not_155_out, OP3);
  not not_156 (not_156_out, OP2);
  not not_157 (not_157_out, F30);
  not not_158 (not_158_out, F25);
  not not_159 (not_159_out, OP6);
  not not_160 (not_160_out, OP3);
  not not_161 (not_161_out, OP2);
  not not_162 (not_162_out, F30);
  not not_163 (not_163_out, F25);
  not not_164 (not_164_out, F14);
  not not_165 (not_165_out, OP6);
  not not_166 (not_166_out, OP3);
  not not_167 (not_167_out, OP2);
  not not_168 (not_168_out, F14);
  not not_169 (not_169_out, F13);
  not not_170 (not_170_out, F12);
  not not_171 (not_171_out, OP6);
  not not_172 (not_172_out, OP5);
  not not_173 (not_173_out, OP3);
  not not_174 (not_174_out, OP2);
  not not_175 (not_175_out, OP6);
  not not_176 (not_176_out, OP5);
  not not_177 (not_177_out, OP3);
  not not_178 (not_178_out, OP2);
  not not_179 (not_179_out, F14);
  not not_180 (not_180_out, F12);
  not not_181 (not_181_out, OP6);
  not not_182 (not_182_out, OP5);
  not not_183 (not_183_out, OP4);
  not not_184 (not_184_out, OP3);
  not not_185 (not_185_out, OP2);
  not not_186 (not_186_out, F14);
  not not_187 (not_187_out, F12);
  not not_188 (not_188_out, OP6);
  not not_189 (not_189_out, OP4);
  not not_190 (not_190_out, OP3);
  not not_191 (not_191_out, OP2);
  not not_192 (not_192_out, F14);
  not not_193 (not_193_out, F13);
  not not_194 (not_194_out, F12);
  not not_195 (not_195_out, OP4);
  not not_196 (not_196_out, OP3);
  not not_197 (not_197_out, OP2);
  not not_198 (not_198_out, F14);
  not not_199 (not_199_out, F13);
  not not_200 (not_200_out, OP4);
  not not_201 (not_201_out, OP3);
  not not_202 (not_202_out, OP2);
  not not_203 (not_203_out, F14);
  not not_204 (not_204_out, F13);
  not not_205 (not_205_out, F12);
  not not_206 (not_206_out, OP4);
  not not_207 (not_207_out, OP3);
  not not_208 (not_208_out, F14);
  not not_209 (not_209_out, F13);
  not not_210 (not_210_out, OP6);
  not not_211 (not_211_out, OP5);
  not not_212 (not_212_out, OP4);
  not not_213 (not_213_out, OP3);
  not not_214 (not_214_out, OP2);
  not not_215 (not_215_out, F30);
  not not_216 (not_216_out, F25);
  not not_217 (not_217_out, F12);
  not not_218 (not_218_out, OP6);
  not not_219 (not_219_out, OP3);
  not not_220 (not_220_out, OP2);
  not not_221 (not_221_out, F30);
  not not_222 (not_222_out, F25);
  not not_223 (not_223_out, F14);
  not not_224 (not_224_out, F12);
  not not_225 (not_225_out, OP6);
  not not_226 (not_226_out, OP3);
  not not_227 (not_227_out, OP2);
  not not_228 (not_228_out, F30);
  not not_229 (not_229_out, F25);
  not not_230 (not_230_out, F14);
  not not_231 (not_231_out, OP6);
  not not_232 (not_232_out, OP3);
  not not_233 (not_233_out, OP2);
  not not_234 (not_234_out, F12);
  not not_235 (not_235_out, OP6);
  not not_236 (not_236_out, OP5);
  not not_237 (not_237_out, OP3);
  not not_238 (not_238_out, OP2);
  not not_239 (not_239_out, F13);
  not not_240 (not_240_out, F12);
  not not_241 (not_241_out, OP6);
  not not_242 (not_242_out, OP5);
  not not_243 (not_243_out, OP3);
  not not_244 (not_244_out, OP2);
  not not_245 (not_245_out, F14);
  not not_246 (not_246_out, F12);
  not not_247 (not_247_out, OP6);
  not not_248 (not_248_out, OP5);
  not not_249 (not_249_out, OP3);
  not not_250 (not_250_out, OP2);
  not not_251 (not_251_out, F30);
  not not_252 (not_252_out, F25);
  not not_253 (not_253_out, F13);
  not not_254 (not_254_out, F12);
  not not_255 (not_255_out, OP6);
  not not_256 (not_256_out, OP3);
  not not_257 (not_257_out, OP2);
  not not_258 (not_258_out, F13);
  not not_259 (not_259_out, OP4);
  not not_260 (not_260_out, OP3);
  not not_261 (not_261_out, OP2);
  and and_1 (and_1_out, not_1_out, not_2_out, not_3_out, not_4_out, not_5_out, not_6_out, OP5, OP4, not_7_out, not_8_out);
  and and_2 (and_2_out, not_9_out, not_10_out, F14, F13, F12, not_11_out, OP5, OP4, not_12_out, not_13_out);
  and and_3 (and_3_out, not_14_out, not_15_out, not_16_out, F13, not_17_out, not_18_out, OP5, OP4, not_19_out, not_20_out);
  and and_4 (and_4_out, not_21_out, not_22_out, not_23_out, not_24_out, not_25_out, OP4, not_26_out, not_27_out);
  and and_5 (and_5_out, F14, F13, F12, not_28_out, not_29_out, OP4, not_30_out, not_31_out);
  and and_6 (and_6_out, F14, not_32_out, not_33_out, not_34_out, not_35_out, OP4, not_36_out, not_37_out);
  and and_7 (and_7_out, not_38_out, F13, not_39_out, not_40_out, not_41_out, OP4, not_42_out, not_43_out);
  and and_8 (and_8_out, F30, not_44_out, F14, not_45_out, F12, not_46_out, not_47_out, OP4, not_48_out, not_49_out);
  and and_9 (and_9_out, not_50_out, F13, not_51_out, not_52_out, not_53_out, not_54_out, not_55_out, not_56_out);
  and and_10 (and_10_out, not_57_out, F13, not_58_out, not_59_out, OP5, not_60_out, not_61_out, not_62_out);
  and and_11 (and_11_out, not_63_out, not_64_out, not_65_out, OP6, OP5, not_66_out, not_67_out, OP2);
  and and_12 (and_12_out, F30, not_68_out, F14, not_69_out, F12, not_70_out, OP5, OP4, not_71_out, not_72_out);
  and and_13 (and_13_out, not_73_out, not_74_out, F14, not_75_out, not_76_out, not_77_out, OP5, OP4, not_78_out, not_79_out);
  and and_14 (and_14_out, not_80_out, not_81_out, F12, not_82_out, not_83_out, not_84_out, not_85_out, not_86_out);
  and and_15 (and_15_out, F14, not_87_out, F12, OP6, OP5, not_88_out, not_89_out, not_90_out);
  and and_16 (and_16_out, F30, not_91_out, not_92_out, not_93_out, not_94_out, not_95_out, OP5, OP4, not_96_out, not_97_out);
  and and_17 (and_17_out, not_98_out, not_99_out, F14, F13, F12, not_100_out, OP5, OP4, not_101_out, not_102_out);
  and and_18 (and_18_out, not_103_out, not_104_out, not_105_out, F13, not_106_out, not_107_out, OP5, OP4, not_108_out, not_109_out);
  and and_19 (and_19_out, F14, F13, F12, not_110_out, not_111_out, OP4, not_112_out, not_113_out);
  and and_20 (and_20_out, not_114_out, F13, not_115_out, not_116_out, not_117_out, OP4, not_118_out, not_119_out);
  and and_21 (and_21_out, not_120_out, not_121_out, F14, not_122_out, F12, not_123_out, not_124_out, OP4, not_125_out, not_126_out);
  and and_22 (and_22_out, not_127_out, not_128_out, not_129_out, OP6, OP5, not_130_out, not_131_out, not_132_out);
  and and_23 (and_23_out, not_133_out, not_134_out, F12, OP6, OP5, not_135_out, not_136_out, not_137_out);
  and and_24 (and_24_out, F14, not_138_out, F12, OP6, OP5, not_139_out, not_140_out, not_141_out);
  and and_25 (and_25_out, not_142_out, not_143_out, not_144_out, not_145_out, not_146_out, not_147_out, OP5, OP4, not_148_out, not_149_out);
  and and_26 (and_26_out, F30, not_150_out, not_151_out, not_152_out, not_153_out, not_154_out, OP5, OP4, not_155_out, not_156_out);
  and and_27 (and_27_out, not_157_out, not_158_out, F14, F13, F12, not_159_out, OP5, OP4, not_160_out, not_161_out);
  and and_28 (and_28_out, not_162_out, not_163_out, not_164_out, F13, F12, not_165_out, OP5, OP4, not_166_out, not_167_out);
  and and_29 (and_29_out, not_168_out, not_169_out, not_170_out, not_171_out, not_172_out, OP4, not_173_out, not_174_out);
  and and_30 (and_30_out, F14, F13, F12, not_175_out, not_176_out, OP4, not_177_out, not_178_out);
  and and_31 (and_31_out, not_179_out, F13, not_180_out, not_181_out, not_182_out, not_183_out, not_184_out, not_185_out);
  and and_32 (and_32_out, not_186_out, F13, not_187_out, not_188_out, OP5, not_189_out, not_190_out, not_191_out);
  and and_33 (and_33_out, not_192_out, not_193_out, not_194_out, OP6, OP5, not_195_out, not_196_out, not_197_out);
  and and_34 (and_34_out, not_198_out, not_199_out, F12, OP6, OP5, not_200_out, not_201_out, not_202_out);
  and and_35 (and_35_out, not_203_out, not_204_out, not_205_out, OP6, OP5, not_206_out, not_207_out, OP2);
  and and_36 (and_36_out, not_208_out, not_209_out, F12, not_210_out, not_211_out, not_212_out, not_213_out, not_214_out);
  and and_37 (and_37_out, not_215_out, not_216_out, F14, F13, not_217_out, not_218_out, OP5, OP4, not_219_out, not_220_out);
  and and_38 (and_38_out, not_221_out, not_222_out, not_223_out, F13, not_224_out, not_225_out, OP5, OP4, not_226_out, not_227_out);
  and and_39 (and_39_out, not_228_out, not_229_out, not_230_out, F13, F12, not_231_out, OP5, OP4, not_232_out, not_233_out);
  and and_40 (and_40_out, F14, F13, not_234_out, not_235_out, not_236_out, OP4, not_237_out, not_238_out);
  and and_41 (and_41_out, F14, not_239_out, not_240_out, not_241_out, not_242_out, OP4, not_243_out, not_244_out);
  and and_42 (and_42_out, not_245_out, F13, not_246_out, not_247_out, not_248_out, OP4, not_249_out, not_250_out);
  and and_43 (and_43_out, not_251_out, not_252_out, F14, not_253_out, not_254_out, not_255_out, OP5, OP4, not_256_out, not_257_out);
  and and_44 (and_44_out, F14, not_258_out, F12, OP6, OP5, not_259_out, not_260_out, not_261_out);
  or or_1 (S0, and_1_out, and_2_out, and_3_out, and_4_out, and_5_out, and_6_out, and_7_out, and_8_out, and_9_out, and_10_out, and_11_out, and_12_out, and_13_out, and_14_out, and_15_out);
  or or_2 (S1, and_16_out, and_17_out, and_18_out, and_19_out, and_20_out, and_21_out, and_22_out, and_23_out, and_24_out);
  or or_3 (S2, and_25_out, and_26_out, and_27_out, and_28_out, and_29_out, and_30_out, and_31_out, and_32_out, and_33_out, and_34_out, and_35_out, and_36_out);
  or or_4 (S3, and_37_out, and_38_out, and_39_out, and_40_out, and_41_out, and_42_out, and_43_out, and_44_out);
endmodule

// 控制信号生成
module \控制信号自动生成  (
  input  OP2,
  input  OP3,
  input  OP4,
  input  OP5,
  input  OP6,
  input  F12,
  input  F13,
  input  F14,
  input  F25,
  input  F30,
  output MemToReg,
  output MemWrite,
  output ALU_SRC,
  output RegWrite,
  output ecall,
  output S_Type,
  output BEQ,
  output BNE,
  output JALR,
  output JAL,
  output LH,
  output BGE,
  output RS1Used,
  output RS2Used,
  output CSR
);

  wire and_1_out, and_2_out, and_4_out, and_5_out, and_6_out, and_7_out, and_8_out, and_9_out, and_10_out,
       and_11_out, and_12_out, and_13_out, and_14_out, and_15_out, and_16_out, and_17_out, and_18_out,
       and_19_out, and_20_out, and_21_out, and_30_out, and_31_out, and_32_out, and_33_out, and_34_out,
       and_35_out, and_36_out, and_37_out, and_38_out, and_39_out, and_40_out, and_41_out, and_42_out,
       and_43_out, and_44_out, and_45_out, and_46_out, and_47_out, and_48_out, and_49_out, not_1_out,
       not_2_out, not_3_out, not_4_out, not_5_out, not_6_out, not_7_out, not_8_out, not_9_out, not_10_out,
       not_11_out, not_12_out, not_13_out, not_14_out, not_15_out, not_16_out, not_17_out, not_18_out,
       not_19_out, not_20_out, not_21_out, not_22_out, not_23_out, not_24_out, not_25_out, not_26_out,
       not_27_out, not_28_out, not_29_out, not_30_out, not_31_out, not_32_out, not_33_out, not_34_out,
       not_35_out, not_36_out, not_37_out, not_38_out, not_39_out, not_40_out, not_41_out, not_42_out,
       not_43_out, not_44_out, not_45_out, not_46_out, not_47_out, not_48_out, not_49_out, not_50_out,
       not_51_out, not_52_out, not_53_out, not_54_out, not_55_out, not_56_out, not_57_out, not_58_out,
       not_59_out, not_60_out, not_61_out, not_62_out, not_63_out, not_64_out, not_65_out, not_66_out,
       not_67_out, not_68_out, not_69_out, not_70_out, not_71_out, not_72_out, not_73_out, not_74_out,
       not_75_out, not_76_out, not_77_out, not_78_out, not_79_out, not_80_out, not_81_out, not_82_out,
       not_83_out, not_84_out, not_85_out, not_86_out, not_87_out, not_88_out, not_89_out, not_90_out,
       not_91_out, not_92_out, not_93_out, not_94_out, not_95_out, not_96_out, not_97_out, not_98_out,
       not_99_out, not_100_out, not_101_out, not_102_out, not_103_out, not_104_out, not_105_out, not_106_out,
       not_107_out, not_108_out, not_109_out, not_110_out, not_111_out, not_112_out, not_113_out,
       not_114_out, not_115_out, not_116_out, not_117_out, not_118_out, not_119_out, not_120_out,
       not_121_out, not_122_out, not_123_out, not_124_out, not_125_out, not_126_out, not_127_out,
       not_128_out, not_129_out, not_130_out, not_131_out, not_132_out, not_133_out, not_134_out,
       not_135_out, not_136_out, not_137_out, not_138_out, not_139_out, not_140_out, not_141_out,
       not_142_out, not_143_out, not_144_out, not_145_out, not_146_out, not_147_out, not_148_out,
       not_149_out, not_150_out, not_151_out, not_152_out, not_153_out, not_154_out, not_155_out,
       not_156_out, not_157_out, not_158_out, not_159_out, not_160_out, not_161_out, not_162_out,
       not_163_out, not_164_out, not_165_out, not_166_out, not_167_out, not_168_out, not_169_out,
       not_170_out, not_171_out, not_172_out, not_173_out, not_174_out, not_175_out, not_176_out,
       not_177_out, not_178_out, not_179_out, not_180_out, not_181_out, not_182_out, not_183_out,
       not_184_out, not_185_out, not_186_out, not_187_out, not_188_out, not_189_out, not_190_out,
       not_191_out, not_192_out, not_193_out, not_194_out, not_195_out, not_196_out, not_197_out,
       not_198_out, not_199_out, not_200_out, not_201_out, not_202_out, not_203_out, not_204_out,
       not_205_out, not_206_out, not_207_out, not_208_out, not_209_out, not_210_out, not_211_out,
       not_212_out, not_213_out, not_214_out, not_215_out, not_216_out, not_217_out, not_218_out,
       not_219_out, not_220_out, not_221_out, not_222_out, not_223_out, not_224_out, not_225_out,
       not_226_out, not_227_out, not_228_out, not_229_out, not_230_out, not_231_out, not_232_out,
       not_233_out, not_234_out, not_235_out, not_236_out, not_237_out, not_238_out, not_239_out,
       not_240_out, not_241_out, not_242_out, not_243_out, not_244_out, not_245_out, not_246_out,
       not_247_out, not_248_out, not_249_out, not_250_out, not_251_out, not_252_out, not_253_out,
       not_254_out, not_255_out, not_256_out, not_257_out, not_258_out, not_259_out, not_260_out, not_261_out;

  not not_1 (not_1_out, OP2);
  not not_2 (not_2_out, OP3);
  not not_3 (not_3_out, OP4);
  not not_4 (not_4_out, OP5);
  not not_5 (not_5_out, OP6);
  not not_6 (not_6_out, F12);
  not not_7 (not_7_out, F14);
  not not_8 (not_8_out, OP2);
  not not_9 (not_9_out, OP3);
  not not_10 (not_10_out, OP4);
  not not_11 (not_11_out, OP5);
  not not_12 (not_12_out, OP6);
  not not_13 (not_13_out, F13);
  not not_14 (not_14_out, F14);
  not not_15 (not_15_out, OP2);
  not not_16 (not_16_out, OP3);
  not not_17 (not_17_out, OP4);
  not not_18 (not_18_out, OP6);
  not not_19 (not_19_out, F12);
  not not_20 (not_20_out, F14);
  not not_21 (not_21_out, OP2);
  not not_22 (not_22_out, OP3);
  not not_23 (not_23_out, OP4);
  not not_24 (not_24_out, OP6);
  not not_25 (not_25_out, F12);
  not not_26 (not_26_out, F14);
  not not_27 (not_27_out, OP2);
  not not_28 (not_28_out, OP3);
  not not_29 (not_29_out, OP4);
  not not_30 (not_30_out, OP5);
  not not_31 (not_31_out, OP6);
  not not_32 (not_32_out, F13);
  not not_33 (not_33_out, F14);
  not not_34 (not_34_out, OP2);
  not not_35 (not_35_out, OP3);
  not not_36 (not_36_out, OP5);
  not not_37 (not_37_out, OP6);
  not not_38 (not_38_out, F12);
  not not_39 (not_39_out, OP2);
  not not_40 (not_40_out, OP3);
  not not_41 (not_41_out, OP5);
  not not_42 (not_42_out, OP6);
  not not_43 (not_43_out, F13);
  not not_44 (not_44_out, F25);
  not not_45 (not_45_out, F30);
  not not_46 (not_46_out, OP2);
  not not_47 (not_47_out, OP3);
  not not_48 (not_48_out, OP5);
  not not_49 (not_49_out, OP6);
  not not_50 (not_50_out, F25);
  not not_51 (not_51_out, OP2);
  not not_52 (not_52_out, OP3);
  not not_53 (not_53_out, OP5);
  not not_54 (not_54_out, OP6);
  not not_55 (not_55_out, OP3);
  not not_56 (not_56_out, OP4);
  not not_57 (not_57_out, F12);
  not not_58 (not_58_out, F13);
  not not_59 (not_59_out, F14);
  not not_60 (not_60_out, OP2);
  not not_61 (not_61_out, OP3);
  not not_62 (not_62_out, OP5);
  not not_63 (not_63_out, OP6);
  not not_64 (not_64_out, F12);
  not not_65 (not_65_out, F14);
  not not_66 (not_66_out, OP2);
  not not_67 (not_67_out, OP3);
  not not_68 (not_68_out, OP4);
  not not_69 (not_69_out, OP5);
  not not_70 (not_70_out, OP6);
  not not_71 (not_71_out, F13);
  not not_72 (not_72_out, F14);
  not not_73 (not_73_out, OP2);
  not not_74 (not_74_out, OP3);
  not not_75 (not_75_out, OP5);
  not not_76 (not_76_out, OP6);
  not not_77 (not_77_out, F12);
  not not_78 (not_78_out, OP2);
  not not_79 (not_79_out, OP3);
  not not_80 (not_80_out, OP5);
  not not_81 (not_81_out, OP6);
  not not_82 (not_82_out, F13);
  not not_83 (not_83_out, F25);
  not not_84 (not_84_out, F30);
  not not_85 (not_85_out, OP2);
  not not_86 (not_86_out, OP3);
  not not_87 (not_87_out, OP6);
  not not_88 (not_88_out, F12);
  not not_89 (not_89_out, F13);
  not not_90 (not_90_out, F14);
  not not_91 (not_91_out, F25);
  not not_92 (not_92_out, OP2);
  not not_93 (not_93_out, OP3);
  not not_94 (not_94_out, OP6);
  not not_95 (not_95_out, F12);
  not not_96 (not_96_out, F25);
  not not_97 (not_97_out, F30);
  not not_98 (not_98_out, OP2);
  not not_99 (not_99_out, OP3);
  not not_100 (not_100_out, OP5);
  not not_101 (not_101_out, OP6);
  not not_102 (not_102_out, OP2);
  not not_103 (not_103_out, OP3);
  not not_104 (not_104_out, OP6);
  not not_105 (not_105_out, F13);
  not not_106 (not_106_out, F25);
  not not_107 (not_107_out, OP2);
  not not_108 (not_108_out, OP3);
  not not_109 (not_109_out, OP6);
  not not_110 (not_110_out, F25);
  not not_111 (not_111_out, F30);
  not not_112 (not_112_out, OP4);
  not not_113 (not_113_out, F12);
  not not_114 (not_114_out, F13);
  not not_115 (not_115_out, F14);
  not not_116 (not_116_out, OP4);
  not not_117 (not_117_out, OP2);
  not not_118 (not_118_out, OP3);
  not not_119 (not_119_out, F12);
  not not_120 (not_120_out, F13);
  not not_121 (not_121_out, F14);
  not not_122 (not_122_out, F25);
  not not_123 (not_123_out, F30);
  not not_124 (not_124_out, OP2);
  not not_125 (not_125_out, OP3);
  not not_126 (not_126_out, OP4);
  not not_127 (not_127_out, OP6);
  not not_128 (not_128_out, F12);
  not not_129 (not_129_out, F14);
  not not_130 (not_130_out, OP2);
  not not_131 (not_131_out, OP3);
  not not_132 (not_132_out, OP4);
  not not_133 (not_133_out, F12);
  not not_134 (not_134_out, F13);
  not not_135 (not_135_out, F14);
  not not_136 (not_136_out, OP2);
  not not_137 (not_137_out, OP3);
  not not_138 (not_138_out, OP4);
  not not_139 (not_139_out, F13);
  not not_140 (not_140_out, F14);
  not not_141 (not_141_out, OP3);
  not not_142 (not_142_out, OP4);
  not not_143 (not_143_out, F12);
  not not_144 (not_144_out, F13);
  not not_145 (not_145_out, F14);
  not not_146 (not_146_out, OP4);
  not not_147 (not_147_out, OP2);
  not not_148 (not_148_out, OP3);
  not not_149 (not_149_out, OP4);
  not not_150 (not_150_out, OP5);
  not not_151 (not_151_out, OP6);
  not not_152 (not_152_out, F13);
  not not_153 (not_153_out, F14);
  not not_154 (not_154_out, OP2);
  not not_155 (not_155_out, OP3);
  not not_156 (not_156_out, OP4);
  not not_157 (not_157_out, F13);
  not not_158 (not_158_out, OP2);
  not not_159 (not_159_out, OP3);
  not not_160 (not_160_out, OP4);
  not not_161 (not_161_out, OP6);
  not not_162 (not_162_out, F12);
  not not_163 (not_163_out, F14);
  not not_164 (not_164_out, OP2);
  not not_165 (not_165_out, OP3);
  not not_166 (not_166_out, OP4);
  not not_167 (not_167_out, OP5);
  not not_168 (not_168_out, OP6);
  not not_169 (not_169_out, F13);
  not not_170 (not_170_out, F14);
  not not_171 (not_171_out, OP3);
  not not_172 (not_172_out, OP4);
  not not_173 (not_173_out, F12);
  not not_174 (not_174_out, F13);
  not not_175 (not_175_out, F14);
  not not_176 (not_176_out, OP2);
  not not_177 (not_177_out, OP3);
  not not_178 (not_178_out, OP4);
  not not_179 (not_179_out, F13);
  not not_180 (not_180_out, OP2);
  not not_181 (not_181_out, OP3);
  not not_182 (not_182_out, OP5);
  not not_183 (not_183_out, OP6);
  not not_184 (not_184_out, F12);
  not not_185 (not_185_out, OP2);
  not not_186 (not_186_out, OP3);
  not not_187 (not_187_out, OP5);
  not not_188 (not_188_out, OP6);
  not not_189 (not_189_out, F13);
  not not_190 (not_190_out, F25);
  not not_191 (not_191_out, F30);
  not not_192 (not_192_out, OP2);
  not not_193 (not_193_out, OP3);
  not not_194 (not_194_out, OP6);
  not not_195 (not_195_out, F12);
  not not_196 (not_196_out, F13);
  not not_197 (not_197_out, F14);
  not not_198 (not_198_out, F25);
  not not_199 (not_199_out, OP2);
  not not_200 (not_200_out, OP3);
  not not_201 (not_201_out, OP6);
  not not_202 (not_202_out, F12);
  not not_203 (not_203_out, F25);
  not not_204 (not_204_out, F30);
  not not_205 (not_205_out, OP2);
  not not_206 (not_206_out, OP3);
  not not_207 (not_207_out, OP5);
  not not_208 (not_208_out, OP6);
  not not_209 (not_209_out, OP2);
  not not_210 (not_210_out, OP3);
  not not_211 (not_211_out, OP6);
  not not_212 (not_212_out, F13);
  not not_213 (not_213_out, F25);
  not not_214 (not_214_out, OP2);
  not not_215 (not_215_out, OP3);
  not not_216 (not_216_out, OP6);
  not not_217 (not_217_out, F25);
  not not_218 (not_218_out, F30);
  not not_219 (not_219_out, OP2);
  not not_220 (not_220_out, OP3);
  not not_221 (not_221_out, OP4);
  not not_222 (not_222_out, OP6);
  not not_223 (not_223_out, F12);
  not not_224 (not_224_out, F14);
  not not_225 (not_225_out, OP2);
  not not_226 (not_226_out, OP3);
  not not_227 (not_227_out, OP4);
  not not_228 (not_228_out, F13);
  not not_229 (not_229_out, F14);
  not not_230 (not_230_out, OP2);
  not not_231 (not_231_out, OP3);
  not not_232 (not_232_out, OP4);
  not not_233 (not_233_out, F13);
  not not_234 (not_234_out, OP2);
  not not_235 (not_235_out, OP3);
  not not_236 (not_236_out, OP6);
  not not_237 (not_237_out, F12);
  not not_238 (not_238_out, F13);
  not not_239 (not_239_out, F14);
  not not_240 (not_240_out, F25);
  not not_241 (not_241_out, OP2);
  not not_242 (not_242_out, OP3);
  not not_243 (not_243_out, OP6);
  not not_244 (not_244_out, F12);
  not not_245 (not_245_out, F25);
  not not_246 (not_246_out, F30);
  not not_247 (not_247_out, OP2);
  not not_248 (not_248_out, OP3);
  not not_249 (not_249_out, OP6);
  not not_250 (not_250_out, F25);
  not not_251 (not_251_out, F30);
  not not_252 (not_252_out, OP2);
  not not_253 (not_253_out, OP3);
  not not_254 (not_254_out, OP6);
  not not_255 (not_255_out, F13);
  not not_256 (not_256_out, F25);
  not not_257 (not_257_out, F12);
  not not_258 (not_258_out, OP3);
  not not_259 (not_259_out, OP2);
  not not_260 (not_260_out, OP3);
  not not_261 (not_261_out, OP2);
  and and_1 (and_1_out, not_1_out, not_2_out, not_3_out, not_4_out, not_5_out, not_6_out, F13, not_7_out);
  and and_2 (and_2_out, not_8_out, not_9_out, not_10_out, not_11_out, not_12_out, F12, not_13_out, not_14_out);
  and and_3 (MemWrite, not_15_out, not_16_out, not_17_out, OP5, not_18_out, not_19_out, F13, not_20_out);
  and and_4 (and_4_out, not_21_out, not_22_out, not_23_out, not_24_out, not_25_out, F13, not_26_out);
  and and_5 (and_5_out, not_27_out, not_28_out, not_29_out, not_30_out, not_31_out, F12, not_32_out, not_33_out);
  and and_6 (and_6_out, not_34_out, not_35_out, OP4, not_36_out, not_37_out, not_38_out);
  and and_7 (and_7_out, not_39_out, not_40_out, OP4, not_41_out, not_42_out, not_43_out, not_44_out, not_45_out);
  and and_8 (and_8_out, not_46_out, not_47_out, OP4, not_48_out, not_49_out, F14, not_50_out);
  and and_9 (and_9_out, not_51_out, not_52_out, OP4, not_53_out, not_54_out, F13, F14);
  and and_10 (and_10_out, OP2, not_55_out, not_56_out, OP5, OP6, not_57_out, not_58_out, not_59_out);
  and and_11 (and_11_out, not_60_out, not_61_out, not_62_out, not_63_out, not_64_out, F13, not_65_out);
  and and_12 (and_12_out, not_66_out, not_67_out, not_68_out, not_69_out, not_70_out, F12, not_71_out, not_72_out);
  and and_13 (and_13_out, not_73_out, not_74_out, OP4, not_75_out, not_76_out, not_77_out);
  and and_14 (and_14_out, not_78_out, not_79_out, OP4, not_80_out, not_81_out, not_82_out, not_83_out, not_84_out);
  and and_15 (and_15_out, not_85_out, not_86_out, OP4, not_87_out, not_88_out, not_89_out, not_90_out, not_91_out);
  and and_16 (and_16_out, not_92_out, not_93_out, OP4, not_94_out, not_95_out, not_96_out, not_97_out);
  and and_17 (and_17_out, not_98_out, not_99_out, OP4, not_100_out, not_101_out, F13, F14);
  and and_18 (and_18_out, not_102_out, not_103_out, OP4, not_104_out, F12, not_105_out, F14, not_106_out, F30);
  and and_19 (and_19_out, not_107_out, not_108_out, OP4, OP5, not_109_out, F13, not_110_out, not_111_out);
  and and_20 (and_20_out, OP2, not_112_out, OP5, OP6, not_113_out, not_114_out, not_115_out);
  and and_21 (and_21_out, OP2, OP3, not_116_out, OP5, OP6);
  and and_22 (ecall, not_117_out, not_118_out, OP4, OP5, OP6, not_119_out, not_120_out, not_121_out, not_122_out, not_123_out);
  and and_23 (S_Type, not_124_out, not_125_out, not_126_out, OP5, not_127_out, not_128_out, F13, not_129_out);
  and and_24 (BEQ, not_130_out, not_131_out, not_132_out, OP5, OP6, not_133_out, not_134_out, not_135_out);
  and and_25 (BNE, not_136_out, not_137_out, not_138_out, OP5, OP6, F12, not_139_out, not_140_out);
  and and_26 (JALR, OP2, not_141_out, not_142_out, OP5, OP6, not_143_out, not_144_out, not_145_out);
  and and_27 (JAL, OP2, OP3, not_146_out, OP5, OP6);
  and and_28 (LH, not_147_out, not_148_out, not_149_out, not_150_out, not_151_out, F12, not_152_out, not_153_out);
  and and_29 (BGE, not_154_out, not_155_out, not_156_out, OP5, OP6, F12, not_157_out, F14);
  and and_30 (and_30_out, not_158_out, not_159_out, not_160_out, not_161_out, not_162_out, F13, not_163_out);
  and and_31 (and_31_out, not_164_out, not_165_out, not_166_out, not_167_out, not_168_out, F12, not_169_out, not_170_out);
  and and_32 (and_32_out, not_171_out, not_172_out, OP5, OP6, not_173_out, not_174_out, not_175_out);
  and and_33 (and_33_out, not_176_out, not_177_out, not_178_out, OP5, OP6, F12, not_179_out);
  and and_34 (and_34_out, not_180_out, not_181_out, OP4, not_182_out, not_183_out, not_184_out);
  and and_35 (and_35_out, not_185_out, not_186_out, OP4, not_187_out, not_188_out, not_189_out, not_190_out, not_191_out);
  and and_36 (and_36_out, not_192_out, not_193_out, OP4, not_194_out, not_195_out, not_196_out, not_197_out, not_198_out);
  and and_37 (and_37_out, not_199_out, not_200_out, OP4, not_201_out, not_202_out, not_203_out, not_204_out);
  and and_38 (and_38_out, not_205_out, not_206_out, OP4, not_207_out, not_208_out, F13, F14);
  and and_39 (and_39_out, not_209_out, not_210_out, OP4, not_211_out, F12, not_212_out, F14, not_213_out, F30);
  and and_40 (and_40_out, not_214_out, not_215_out, OP4, OP5, not_216_out, F13, not_217_out, not_218_out);
  and and_41 (and_41_out, not_219_out, not_220_out, not_221_out, OP5, not_222_out, not_223_out, F13, not_224_out);
  and and_42 (and_42_out, not_225_out, not_226_out, not_227_out, OP5, OP6, not_228_out, not_229_out);
  and and_43 (and_43_out, not_230_out, not_231_out, not_232_out, OP5, OP6, F12, not_233_out);
  and and_44 (and_44_out, not_234_out, not_235_out, OP4, OP5, not_236_out, not_237_out, not_238_out, not_239_out, not_240_out);
  and and_45 (and_45_out, not_241_out, not_242_out, OP4, OP5, not_243_out, not_244_out, not_245_out, not_246_out);
  and and_46 (and_46_out, not_247_out, not_248_out, OP4, OP5, not_249_out, F13, not_250_out, not_251_out);
  and and_47 (and_47_out, not_252_out, not_253_out, OP4, OP5, not_254_out, F12, not_255_out, F14, not_256_out, F30);
  and and_48 (and_48_out, F14, F13, not_257_out, OP6, OP5, OP4, not_258_out, not_259_out);
  and and_49 (and_49_out, F14, F13, F12, OP6, OP5, OP4, not_260_out, not_261_out);
  or or_1 (MemToReg, and_1_out, and_2_out);
  or or_2 (ALU_SRC, and_4_out, and_5_out, and_6_out, and_7_out, and_8_out, and_9_out, and_10_out);
  or or_3 (CSR, and_48_out, and_49_out);
  or or_4 (RegWrite, and_11_out, and_12_out, and_13_out, and_14_out, and_15_out, and_16_out, and_17_out, and_18_out, and_19_out, and_20_out, and_21_out);
  or or_5 (RS1Used, and_30_out, and_31_out, and_32_out, and_33_out, and_34_out, and_35_out, and_36_out, and_37_out, and_38_out, and_39_out, and_40_out);
  or or_6 (RS2Used, and_41_out, and_42_out, and_43_out, and_44_out, and_45_out, and_46_out, and_47_out);
endmodule

// ALU
module ALU (
  input  [31:0] X,
  input  [31:0] Y,
  input  [3:0] AluOP,
  output out_4,
  output Equal,
  output out_6,
  output [31:0] Result,
  output [31:0] Result_2
);

  wire [0:0] comparator_1_lt, comparator_2_lt;
  wire [31:0] adder_1_out, AND_out, divider_1_out, divider_1_rem, multiplier_1_cout, multiplier_1_out,
       NOR_out, OR_out, shifter_1_out, shifter_2_out, shifter_3_out, subtractor_1_out, XOR_out;

  assign AND_out = X & Y;  // AND_Gate AND, 32 bits wide
  assign OR_out = X | Y;  // OR_Gate OR, 32 bits wide
  Shifter #(.width(32), .shift("ll")) shifter_1 (.in(X), .\dist (Y[4:0]), .out(shifter_1_out));
  Shifter #(.width(32), .shift("ar")) shifter_2 (.in(X), .\dist (Y[4:0]), .out(shifter_2_out));
  Shifter #(.width(32), .shift("lr")) shifter_3 (.in(X), .\dist (Y[4:0]), .out(shifter_3_out));
  Multiplier #(.width(32)) multiplier_1 (.a(X), .b(Y), .out(multiplier_1_out), .cout(multiplier_1_cout));  // open: cin
  Divider #(.width(32)) divider_1 (.a(X), .b(Y), .out(divider_1_out), .rem(divider_1_rem));  // open: upper
  Adder #(.width(32)) adder_1 (.a(X), .b(Y), .out(adder_1_out));  // open: cin, cout
  Subtractor #(.width(32)) subtractor_1 (.a(X), .b(Y), .out(subtractor_1_out));  // open: bin, bout
  assign XOR_out = X ^ Y;  // XOR_Gate XOR, 32 bits wide
  assign NOR_out = ~(X | Y);  // NOR_Gate NOR, 32 bits wide
  Comparator #(.width(32), .mode("twosComplement")) comparator_1 (
    .a(X), .b(Y), .eq(Equal), .lt(comparator_1_lt[0]));  // open: gt
  Comparator #(.width(32), .mode("unsigned")) comparator_2 (.a(X), .b(Y), .lt(comparator_2_lt[0]));  // open: gt, eq
  Multiplexer #(.select(4), .width(32), .disabled("Z"), .enable("false")) multiplexer_1 (
    .in0(shifter_1_out), .in1(shifter_2_out), .in2(shifter_3_out), .in3(multiplier_1_out),
    .in4(divider_1_out), .in5(adder_1_out), .in6(subtractor_1_out), .in7(AND_out), .in8(OR_out),
    .in9(XOR_out), .in10(NOR_out), .in11({{31{1'b0}}, comparator_1_lt[0]}),
    .in12({{31{1'b0}}, comparator_2_lt[0]}), .in13({32{1'b0}}), .in14({32{1'b0}}), .in15({32{1'b0}}),
    .out(Result), .sel(AluOP));
  Multiplexer #(.select(4), .width(32), .disabled("Z"), .enable("false")) multiplexer_2 (
    .in0({32{1'b0}}), .in1({32{1'b0}}), .in2({32{1'b0}}), .in3(multiplier_1_cout), .in4(divider_1_rem),
    .in5({32{1'b0}}), .in6({32{1'b0}}), .in7({32{1'b0}}), .in8({32{1'b0}}), .in9({32{1'b0}}),
    .in10({32{1'b0}}), .in11({32{1'b0}}), .in12({32{1'b0}}), .in13({32{1'b0}}), .in14({32{1'b0}}),
    .in15({32{1'b0}}), .out(Result_2), .sel(AluOP));
  Multiplexer #(.select(4), .width(1), .disabled("Z"), .enable("false")) multiplexer_3 (
    .in0(1'b0), .in1(1'b0), .in2(1'b0), .in3(1'b0), .in4(1'b0), .in5(1'b0), .in6(1'b0), .in7(1'b0),
    .in8(1'b0), .in9(1'b0), .in10(1'b0), .in11(comparator_1_lt[0]), .in12(comparator_2_lt[0]), .in13(1'b0),
    .in14(1'b0), .in15(1'b0), .out(out_6), .sel(AluOP));
  not not_1 (out_4, out_6);

  // Other names for the same wires on the sheet: Result2[31:0] = Result_2; S[3:0] = AluOP; tunnel = out_6;
  //   tunnel_t = out_4

  // Notes on the sheet:
  //   不要改变此引脚区域内容，也不要改变ALU封装形式
  //   输入引脚
  //   输出引脚
endmodule

module Regifile (
  input  [31:0] Din,
  input  Clk,
  input  WE,
  input  [4:0] R1_num,
  input  [4:0] W_num,
  input  [4:0] R2_num,
  output [31:0] R1,
  output [31:0] R2
);

  // RegisterFile registerfile_1: pin names not known; wires that end beside it: Din, Clk, WE, W_num, R1_num, R2_num, R1, R2
endmodule

module \理想流水线  (
  output RegWrite,
  output MemWrite,
  output [31:0] IF_PC,
  output [31:0] ID_PC,
  output [31:0] EX_PC,
  output [31:0] M_PC,
  output [31:0] WB_PC,
  output [31:0] RDin,
  output [31:0] MDin,
  output [31:0] LedData
);

  wire and_1_out, and_2_out, and_3_out, and_4_out, and_5_out, CLK, clock_1_out, comparator_1_eq,
       comparator_1_lt, comparator_2_eq, d_ff_1_q, Equal, EX_JAL, EX_JALR, ex_mem_1_halt_2, ex_mem_1_jal_2,
       ex_mem_1_jalr_2, ex_mem_1_lh_2, ex_mem_1_memtoreg_2, ex_mem_1_regwrite_2, Ge, Go, halt,
       id_ex_1_alusrcb_2, id_ex_1_beq_2, id_ex_1_bge_2, id_ex_1_bne_2, id_ex_1_ecall_2, id_ex_1_lh_2,
       id_ex_1_memtoreg_2, id_ex_1_memwrite_2, id_ex_1_regwrite_2, ID_JAL, IR1, IR2, IR3, Less,
       mem_wb_1_halt_2, mem_wb_1_jal_2, mem_wb_1_jalr_2, mem_wb_1_memtoreg_2, nand_1_out, not_1_out,
       not_2_out, not_3_out, or_1_out, or_3_out, RST, S_type, W1, W2, W3, \单周期硬布线控制器_1_alu_src ,
       \单周期硬布线控制器_1_beq , \单周期硬布线控制器_1_bge , \单周期硬布线控制器_1_bne , \单周期硬布线控制器_1_ecall , \单周期硬布线控制器_1_jalr ,
       \单周期硬布线控制器_1_lh , \单周期硬布线控制器_1_memtoreg , \单周期硬布线控制器_1_memwrite , \单周期硬布线控制器_1_regwrite ,
       \单周期硬布线控制器_1_uret ;
  wire [1:0] BitSel;
  wire [1:1] or_2_out;
  wire [3:0] id_ex_1_aluop_2, \单周期硬布线控制器_1_alu_op ;
  wire [4:0] ex_mem_1_rd_2, id_ex_1_rd_2, multiplexer_2_out, multiplexer_3_out, WB_Rd;
  wire [12:0] CNT_num;
  wire [15:0] \LoadUse次数 , multiplexer_7_out, \总周期数 , \插入气泡数 , \无条件分支数 , \条件分支成功数 ;
  wire [31:0] adder_2_out, bit_extender_1_out, bit_extender_2_out, bit_extender_3_out, bit_extender_4_out,
       EX_AluResult, EX_IR, ex_mem_1_pc_4_2, HalfMemData, id_ex_1_imm1_2, id_ex_1_imm2_2, id_ex_1_pc_4_2,
       id_ex_1_r1_2, id_ex_1_r2_2, ID_IR, if_id_1_pc_4_2, IF_IR, IF_PC_4, MEM_IR, mem_wb_1_aluresult_2,
       mem_wb_1_pc_4_2, mem_wb_1_readdata_2, MemData, multiplexer_1_out, multiplexer_4_out,
       multiplexer_5_out, multiplexer_6_out, multiplexer_8_out, multiplexer_9_out, regifile_1_r1,
       regifile_1_r2, shifter_1_out, WB_IR;
  wire [31:2] ex_mem_1_aluresult_2;

  Button \u_总复位  (.out(RST));
  Button _1 (.out(IR1));
  Button _2 (.out(IR2));
  Button _3 (.out(IR3));
  // Probe on \总周期数 
  // Probe on \总周期数 
  Button \u_继续运行  (.out(Go));
  LED #(.active("true")) led_1 (.in(W1));
  LED #(.active("true")) led_2 (.in(W2));
  LED #(.active("true")) led_3 (.in(W3));
  Hex_Digit_Display hex_digit_display_1 (.value(LedData[31:28]));  // open: dp
  // Probe on IF_PC[19:0]
  // RiscV_Probe riscv_probe_1: pin names not known; wires that end beside it: IF_IR
  Hex_Digit_Display hex_digit_display_2 (.value(LedData[27:24]));  // open: dp
  Hex_Digit_Display hex_digit_display_3 (.value(LedData[23:20]));  // open: dp
  // Probe on ID_PC[19:0]
  // RiscV_Probe riscv_probe_2: pin names not known; wires that end beside it: ID_IR
  Multiplexer #(.select(2), .width(32), .disabled("Z"), .enable("false")) multiplexer_1 (
    .in0(IF_PC_4), .in1(EX_AluResult), .in2(adder_2_out), .out(multiplexer_1_out),
    .sel({or_2_out[1], EX_JALR}));  // open: in3
  not not_1 (not_1_out, halt);
  Hex_Digit_Display hex_digit_display_4 (.value(LedData[15:12]));  // open: dp
  Hex_Digit_Display hex_digit_display_5 (.value(LedData[19:16]));  // open: dp
  Register #(.width(32), .trigger("rising"), .Select("low")) PC (
    .D(multiplexer_1_out), .en(not_1_out), .Q(IF_PC), .clk(CLK), .clr(RST));
  Hex_Digit_Display hex_digit_display_6 (.value(LedData[7:4]));  // open: dp
  Hex_Digit_Display hex_digit_display_7 (.value(LedData[11:8]));  // open: dp
  // Probe on EX_PC[19:0]
  // RiscV_Probe riscv_probe_3: pin names not known; wires that end beside it: EX_IR
  not not_2 (not_2_out, halt);
  Counter #(.width(16), .max('hffff), .ongoal("wrap"), .trigger("rising"), .behavior("new")) counter_1 (
    .count(not_2_out), .Q(\总周期数 ), .clk(CLK), .clr(RST));  // open: load, D, carry, preset, down
  Hex_Digit_Display hex_digit_display_8 (.value(LedData[3:0]));  // open: dp
  ROM #(.addrWidth(10), .dataWidth(32), .Select("high")) rom_1 (.addr(IF_PC[11:2]), .data(IF_IR));
  Adder #(.width(32)) adder_1 (.a(IF_PC), .b(32'h4), .out(IF_PC_4));  // open: cin, cout
  // Probe on \总周期数 
  // Probe on M_PC[19:0]
  // RiscV_Probe riscv_probe_4: pin names not known; wires that end beside it: MEM_IR
  // RiscV_Probe riscv_probe_5: pin names not known; wires that end beside it: IF_IR
  // Probe on \总周期数 
  // Probe on \无条件分支数 
  // Probe on \条件分支成功数 
  // Probe on \插入气泡数 
  // Probe on \LoadUse次数 
  or or_1 (or_1_out, or_2_out[1], EX_JALR);
  IF_ID if_id_1 (
    .IR(IF_IR), .IR_2(ID_IR), .PC_2(ID_PC), .reset(RST), .en(1'b1), .CLK(CLK), .PC_4(IF_PC_4),
    .PC_4_2(if_id_1_pc_4_2), .PC(IF_PC), .flush(or_1_out));  // open: PredictJump, PredictJump_2
  // Probe on IF_PC[11:0]
  // Probe on WB_PC[19:0]
  // RiscV_Probe riscv_probe_6: pin names not known; wires that end beside it: WB_IR
  // Probe on EX_PC[11:0]
  // Probe on ID_PC[11:0]
  \单周期硬布线控制器  \u_单周期硬布线控制器_1  (
    .Funct({ID_IR[30], ID_IR[25], ID_IR[14:12]}), .OP(ID_IR[6:2]), .ALU_OP(\单周期硬布线控制器_1_alu_op ),
    .MemToReg(\单周期硬布线控制器_1_memtoreg ), .MemWrite(\单周期硬布线控制器_1_memwrite ), .ALU_SRC(\单周期硬布线控制器_1_alu_src ),
    .RegWrite(\单周期硬布线控制器_1_regwrite ), .ecall(\单周期硬布线控制器_1_ecall ), .S_type(S_type),
    .Jalr(\单周期硬布线控制器_1_jalr ), .Beq(\单周期硬布线控制器_1_beq ), .JAL(ID_JAL), .Bne(\单周期硬布线控制器_1_bne ),
    .in_3(ID_IR[21]), .uret(\单周期硬布线控制器_1_uret ), .Lh(\单周期硬布线控制器_1_lh ), .Bge(\单周期硬布线控制器_1_bge ));  // open: RS1Used, RS2Used, CSR
  Multiplexer #(.select(1), .width(5), .disabled("Z"), .enable("false")) multiplexer_2 (
    .in0(ID_IR[19:15]), .in1(5'b10001), .out(multiplexer_2_out), .sel(\单周期硬布线控制器_1_ecall ));
  Multiplexer #(.select(1), .width(5), .disabled("Z"), .enable("false")) multiplexer_3 (
    .in0(ID_IR[24:20]), .in1(5'b01010), .out(multiplexer_3_out), .sel(\单周期硬布线控制器_1_ecall ));
  // Probe on M_PC[11:0]
  D_Flip_Flop #(.trigger("high"), .Pre_Clr_Positions("LEGACY"), .NegatePresetClear("false"), .enable("true"), .NewFFLayout("false")) d_ff_1 (.Q(d_ff_1_q));  // open: clk, D, Qn, preset, en, reset
  // Probe on 13'hc
  assign bit_extender_1_out = {{20{ID_IR[31]}}, ID_IR[31:20]};  // Bit_Extender bit_extender_1
  assign bit_extender_2_out = {{20{ID_IR[31]}}, {ID_IR[31:25], ID_IR[11:7]}};  // Bit_Extender bit_extender_2
  assign bit_extender_3_out = {{20{ID_IR[31]}}, {ID_IR[31], ID_IR[7], ID_IR[30:25], ID_IR[11:8]}};  // Bit_Extender bit_extender_3
  assign bit_extender_4_out = {{12{ID_IR[31]}}, {ID_IR[31], ID_IR[19:12], ID_IR[20], ID_IR[30:21]}};  // Bit_Extender bit_extender_4
  // Probe on WB_PC[11:0]
  Comparator #(.width(13), .mode("twosComplement")) comparator_1 (
    .a(CNT_num), .b(13'hc), .eq(comparator_1_eq), .lt(comparator_1_lt));  // open: gt
  Clock #(.highDuration(1), .lowDuration(1)) clock_1 (.out(clock_1_out));
  Multiplexer #(.select(1), .width(32), .disabled("Z"), .enable("false")) multiplexer_4 (
    .in0(bit_extender_1_out), .in1(bit_extender_2_out), .out(multiplexer_4_out), .sel(S_type));
  Multiplexer #(.select(1), .width(32), .disabled("Z"), .enable("false")) multiplexer_5 (
    .in0(bit_extender_3_out), .in1(bit_extender_4_out), .out(multiplexer_5_out), .sel(ID_JAL));
  nand nand_1 (nand_1_out, d_ff_1_q, comparator_1_eq);
  Counter #(.width(13), .max('h1fff), .ongoal("stay"), .trigger("rising"), .behavior("old")) counter_2 (
    .count(comparator_1_lt), .Q(CNT_num), .clk(clock_1_out));  // open: load, D, carry, clr, preset
  Regifile regifile_1 (
    .Din(RDin), .Clk(CLK), .R1(regifile_1_r1), .R2(regifile_1_r2), .WE(RegWrite), .W_num(WB_Rd),
    .R1_num(multiplexer_2_out), .R2_num(multiplexer_3_out));
  assign CLK = nand_1_out ? clock_1_out : 1'bz;  // Controlled_Buffer controlled_buffer_1
  ID_EX id_ex_1 (
    .Bge(\单周期硬布线控制器_1_bge ), .Lh(\单周期硬布线控制器_1_lh ), .URET(\单周期硬布线控制器_1_uret ), .JALR(\单周期硬布线控制器_1_jalr ),
    .JAL(ID_JAL), .Beq(\单周期硬布线控制器_1_beq ), .Bne(\单周期硬布线控制器_1_bne ), .MemToReg(\单周期硬布线控制器_1_memtoreg ),
    .MemWrite(\单周期硬布线控制器_1_memwrite ), .AluOP(\单周期硬布线控制器_1_alu_op ), .AluSrcB(\单周期硬布线控制器_1_alu_src ),
    .RegWrite(\单周期硬布线控制器_1_regwrite ), .Bge_2(id_ex_1_bge_2), .Lh_2(id_ex_1_lh_2), .JALR_2(EX_JALR),
    .JAL_2(EX_JAL), .Beq_2(id_ex_1_beq_2), .Bne_2(id_ex_1_bne_2), .MemToReg_2(id_ex_1_memtoreg_2),
    .MemWrite_2(id_ex_1_memwrite_2), .AluOP_2(id_ex_1_aluop_2), .AluSrcB_2(id_ex_1_alusrcb_2),
    .RegWrite_2(id_ex_1_regwrite_2), .reset(RST), .en(1'b1), .CLK(CLK), .ecall(\单周期硬布线控制器_1_ecall ),
    .ecall_2(id_ex_1_ecall_2), .R1_2(id_ex_1_r1_2), .R2(regifile_1_r2), .R2_2(id_ex_1_r2_2),
    .imm1(multiplexer_4_out), .imm1_2(id_ex_1_imm1_2), .imm2(multiplexer_5_out), .imm2_2(id_ex_1_imm2_2),
    .IR(ID_IR), .PC(ID_PC), .PC_2(EX_PC), .PC_4(if_id_1_pc_4_2), .PC_4_2(id_ex_1_pc_4_2), .R1(regifile_1_r1),
    .IR_2(EX_IR), .rd(ID_IR[11:7]), .rd_2(id_ex_1_rd_2), .flush(1'b0));  // open: URET_2, RS1Forward, RS1Forward_2, RS2Forward, RS2Forward_2, PredictJump, PredictJump_2
  Pull_Resistor #(.pull(1)) pull_resistor_1 (.node(CLK));
  and and_1 (and_1_out, Ge, id_ex_1_bge_2);
  Shifter #(.width(32), .shift("ll")) shifter_1 (.in(id_ex_1_imm2_2), .\dist (5'b00001), .out(shifter_1_out));
  or or_2 (or_2_out[1], EX_JAL, and_1_out, and_3_out, and_2_out);
  and and_2 (and_2_out, ~Equal, id_ex_1_bne_2);  // AND_Gate
  and and_3 (and_3_out, id_ex_1_beq_2, Equal);
  Multiplexer #(.select(1), .width(32), .disabled("Z"), .enable("false")) multiplexer_6 (
    .in0(id_ex_1_r2_2), .in1(id_ex_1_imm1_2), .out(multiplexer_6_out), .sel(id_ex_1_alusrcb_2));
  Adder #(.width(32)) adder_2 (.a(shifter_1_out), .b(EX_PC), .out(adder_2_out));  // open: cin, cout
  ALU alu_1 (
    .X(id_ex_1_r1_2), .Y(multiplexer_6_out), .AluOP(id_ex_1_aluop_2), .Equal(Equal), .Result(EX_AluResult),
    .out_4(Ge), .out_6(Less));  // open: Result_2
  Comparator #(.width(32), .mode("twosComplement")) comparator_2 (
    .a(id_ex_1_r1_2), .b(32'h22), .eq(comparator_2_eq));  // open: gt, lt
  and and_4 (and_4_out, id_ex_1_ecall_2, ~comparator_2_eq);  // AND_Gate
  and and_5 (and_5_out, comparator_2_eq, id_ex_1_ecall_2);
  Register #(.width(32), .trigger("rising"), .Select("low")) register_1 (
    .D(id_ex_1_r2_2), .en(and_5_out), .Q(LedData), .clk(CLK), .clr(RST));
  EX_MEM ex_mem_1 (
    .Lh(id_ex_1_lh_2), .JALR(EX_JALR), .JAL(EX_JAL), .MemToReg(id_ex_1_memtoreg_2),
    .MemWrite(id_ex_1_memwrite_2), .RegWrite(id_ex_1_regwrite_2), .halt(and_4_out), .AluResult(EX_AluResult),
    .WriteData(id_ex_1_r2_2), .IR(EX_IR), .PC(EX_PC), .PC_4(id_ex_1_pc_4_2), .rd(id_ex_1_rd_2),
    .Lh_2(ex_mem_1_lh_2), .JALR_2(ex_mem_1_jalr_2), .JAL_2(ex_mem_1_jal_2), .MemToReg_2(ex_mem_1_memtoreg_2),
    .MemWrite_2(MemWrite), .RegWrite_2(ex_mem_1_regwrite_2), .halt_2(ex_mem_1_halt_2),
    .AluResult_2({ex_mem_1_aluresult_2, BitSel}), .WriteData_2(MDin), .IR_2(MEM_IR), .PC_2(M_PC),
    .PC_4_2(ex_mem_1_pc_4_2), .rd_2(ex_mem_1_rd_2), .reset(RST), .en(1'b1), .CLK(CLK));
  not not_3 (not_3_out, MemWrite);
  Multiplexer #(.select(1), .width(16), .disabled("Z"), .enable("false")) multiplexer_7 (
    .in0(MemData[15:0]), .in1(MemData[31:16]), .out(multiplexer_7_out), .sel(BitSel[1]));
  RAM #(.addrWidth(10), .dataWidth(32), .bus("separate"), .Select("high")) ram_1 (
    .addr(ex_mem_1_aluresult_2[11:2]), .din(MDin), .data(MemData), .str(MemWrite), .clk(CLK), .ld(not_3_out),
    .clr(RST));  // open: sel
  assign HalfMemData = {{16{multiplexer_7_out[15]}}, multiplexer_7_out};  // Bit_Extender bit_extender_5
  Multiplexer #(.select(1), .width(32), .disabled("Z"), .enable("false")) multiplexer_8 (
    .in0(MemData), .in1(HalfMemData), .out(multiplexer_8_out), .sel(ex_mem_1_lh_2));
  MEM_WB mem_wb_1 (
    .JALR(ex_mem_1_jalr_2), .JAL(ex_mem_1_jal_2), .MemToReg(ex_mem_1_memtoreg_2),
    .RegWrite(ex_mem_1_regwrite_2), .halt(ex_mem_1_halt_2), .AluResult({ex_mem_1_aluresult_2, BitSel}),
    .ReadData(multiplexer_8_out), .IR(MEM_IR), .PC(M_PC), .PC_4(ex_mem_1_pc_4_2), .rd(ex_mem_1_rd_2),
    .JALR_2(mem_wb_1_jalr_2), .JAL_2(mem_wb_1_jal_2), .MemToReg_2(mem_wb_1_memtoreg_2),
    .RegWrite_2(RegWrite), .halt_2(mem_wb_1_halt_2), .AluResult_2(mem_wb_1_aluresult_2),
    .ReadData_2(mem_wb_1_readdata_2), .IR_2(WB_IR), .PC_2(WB_PC), .PC_4_2(mem_wb_1_pc_4_2), .rd_2(WB_Rd),
    .reset(RST), .en(1'b1), .CLK(CLK));
  D_Flip_Flop #(.trigger("rising"), .Pre_Clr_Positions("ABOVE_BELOW"), .NegatePresetClear("false"), .enable("true"), .NewFFLayout("true")) d_ff_2 (
    .clk(mem_wb_1_halt_2), .D(1'b1), .Q(halt), .en(1'b1), .reset(Go));  // open: Qn, preset
  Multiplexer #(.select(1), .width(32), .disabled("Z"), .enable("false")) multiplexer_9 (
    .in0(mem_wb_1_aluresult_2), .in1(mem_wb_1_readdata_2), .out(multiplexer_9_out), .sel(mem_wb_1_memtoreg_2));
  or or_3 (or_3_out, mem_wb_1_jal_2, mem_wb_1_jalr_2);
  Multiplexer #(.select(1), .width(32), .disabled("Z"), .enable("false")) multiplexer_10 (
    .in0(multiplexer_9_out), .in1(mem_wb_1_pc_4_2), .out(RDin), .sel(or_3_out));

  // Other names for the same wires on the sheet: MEM_PC[31:0] = M_PC

  // Notes on the sheet:
  //   中断源
  //   时空图监测，可删除
  //   中断等待指示
  //   数码管输出
  //   指令存储器
  //   contents of rom_1 (hex, n*v repeats v):
  //   413 493 913 993 46413 14e493 296913 39e993 842023 942223 1242423 1342623 a00893 493 913 993 73
  //   指令探针
  //   指令字
  //   控制位
  //   JAL
  //   JALR
  //   URET
  //   Lh
  //   Bge
  //   ecall
  //   I型指令立即数 
  //   S型指令立即数 
  //   B型指令立即数 
  //   J型指令立即数 
  //   流水调试日志用
  //   暂停节拍，不能为0
  //   Beq
  //   Bne
  //   MemToReg
  //   MemWrite
  //   AluOP
  //   AluSrcB
  //   RegWrite
  //   S_type
  //   imm1
  //   可计数暂停的时钟源
  //   Bge
  //   Lh
  //   URET
  //   JALR
  //   JAL
  //   Beq
  //   Bne
  //   ecall
  //   imm2
  //   rd 
  //   IR 
  //   PC 
  //   PC+4 
  //   MemToReg
  //   MemWrite
  //   AluOP
  //   AluSrcB
  //   RegWrite
  //   R1
  //   R2
  //   JumpAddr
  //   为方便自动评测，需要输出流水线各段保存的PC值，注意是PC不是PC+4，另外ID段寄存器写入信息，Mem段内存写入信息也要输出
  //   戳工具置1进入计数暂停模式，ctrl+k时钟自动运行到对应节拍暂停
  //   ctrl+k关闭时钟连续运行，将控制位置零，进入单步调试模式调试
  //   用这个时钟源需要去掉电路中的其他时钟源
  //   ecall
  //   AluResult
  //   WriteData
  //   rd 
  //   IR 
  //   PC 
  //   PC+4 
  //   Lh
  //   JALR
  //   JAL
  //   MemToReg
  //   MemWrite
  //   RegWrite
  //   halt
  //   数据存储器
  //   JALR
  //   MemToReg
  //   RegWrite
  //   AluResult
  //   Lh
  //   ReadData
  //   JAL
  //   halt
  //   rd 
  //   IR 
  //   PC 
  //   PC+4 
  //   JAL
  //   JALR
endmodule

module \气泡流水线  (
  output RegWrite,
  output MemWrite,
  output [31:0] IF_PC,
  output [31:0] ID_PC,
  output [31:0] EX_PC,
  output [31:0] M_PC,
  output [31:0] WB_PC,
  output [31:0] RDin,
  output [31:0] MDin,
  output [31:0] LedData
);

  wire and_1_out, and_2_out, and_3_out, and_4_out, and_5_out, and_6_out, and_7_out, and_8_out, and_9_out,
       and_10_out, BranchCount, CLK, clock_1_out, comparator_1_eq, comparator_1_lt, comparator_2_eq,
       d_ff_1_q, Equal, EX_JAL, EX_JALR, ex_mem_1_halt_2, ex_mem_1_jal_2, ex_mem_1_jalr_2, ex_mem_1_lh_2,
       ex_mem_1_memtoreg_2, ex_mem_1_regwrite_2, flush, Ge, Go, halt, id_ex_1_alusrcb_2, id_ex_1_beq_2,
       id_ex_1_bge_2, id_ex_1_bne_2, id_ex_1_ecall_2, id_ex_1_lh_2, id_ex_1_memtoreg_2, id_ex_1_memwrite_2,
       id_ex_1_regwrite_2, ID_JAL, IR1, IR2, IR3, JumpCount, Less, mem_wb_1_halt_2, mem_wb_1_jal_2,
       mem_wb_1_jalr_2, mem_wb_1_memtoreg_2, nand_1_out, not_1_out, not_2_out, not_3_out, not_4_out,
       not_5_out, not_6_out, or_2_out, or_5_out, RST, S_type, stall, W1, W2, W3, \单周期硬布线控制器_1_alu_src ,
       \单周期硬布线控制器_1_beq , \单周期硬布线控制器_1_bge , \单周期硬布线控制器_1_bne , \单周期硬布线控制器_1_ecall , \单周期硬布线控制器_1_jalr ,
       \单周期硬布线控制器_1_lh , \单周期硬布线控制器_1_memtoreg , \单周期硬布线控制器_1_memwrite , \单周期硬布线控制器_1_regwrite ,
       \单周期硬布线控制器_1_rs1used , \单周期硬布线控制器_1_rs2used , \单周期硬布线控制器_1_uret ;
  wire [1:0] BitSel;
  wire [1:1] or_1_out;
  wire [3:0] id_ex_1_aluop_2, \单周期硬布线控制器_1_alu_op ;
  wire [4:0] ex_mem_1_rd_2, id_ex_1_rd_2, multiplexer_2_out, multiplexer_3_out, WB_Rd;
  wire [12:0] CNT_num;
  wire [15:0] \LoadUse次数 , multiplexer_7_out, \总周期数 , \插入气泡数 , \无条件分支数 , \条件分支成功数 ;
  wire [31:0] adder_2_out, bit_extender_1_out, bit_extender_2_out, bit_extender_3_out, bit_extender_4_out,
       EX_AluResult, EX_IR, ex_mem_1_pc_4_2, HalfMemData, id_ex_1_imm1_2, id_ex_1_imm2_2, id_ex_1_pc_4_2,
       id_ex_1_r1_2, id_ex_1_r2_2, ID_IR, if_id_1_pc_4_2, IF_IR, IF_PC_4, MEM_IR, mem_wb_1_aluresult_2,
       mem_wb_1_pc_4_2, mem_wb_1_readdata_2, MemData, multiplexer_1_out, multiplexer_4_out,
       multiplexer_5_out, multiplexer_6_out, multiplexer_8_out, multiplexer_9_out, regifile_1_r1,
       regifile_1_r2, shifter_1_out, WB_IR;
  wire [31:2] ex_mem_1_aluresult_2;

  Button \u_总复位  (.out(RST));
  Button _1 (.out(IR1));
  Button _2 (.out(IR2));
  Button _3 (.out(IR3));
  // Probe on \总周期数 
  // Probe on \总周期数 
  \气泡处理逻辑  \u_气泡处理逻辑_1  (
    .IR(ID_IR), .RS1Used(\单周期硬布线控制器_1_rs1used ), .EX_RegWrite(id_ex_1_regwrite_2), .EX_rd(id_ex_1_rd_2),
    .RS2Used(\单周期硬布线控制器_1_rs2used ), .MEM_RegWrite(ex_mem_1_regwrite_2), .MEM_rd(ex_mem_1_rd_2),
    .BranchTaken(or_2_out), .stall(stall), .flush(flush), .ecall(\单周期硬布线控制器_1_ecall ));
  Button \u_继续运行  (.out(Go));
  LED #(.active("true")) led_1 (.in(W1));
  LED #(.active("true")) led_2 (.in(W2));
  LED #(.active("true")) led_3 (.in(W3));
  Hex_Digit_Display hex_digit_display_1 (.value(LedData[31:28]));  // open: dp
  // Probe on IF_PC[19:0]
  // RiscV_Probe riscv_probe_1: pin names not known; wires that end beside it: IF_IR
  Hex_Digit_Display hex_digit_display_2 (.value(LedData[27:24]));  // open: dp
  Hex_Digit_Display hex_digit_display_3 (.value(LedData[23:20]));  // open: dp
  // Probe on ID_PC[19:0]
  // RiscV_Probe riscv_probe_2: pin names not known; wires that end beside it: ID_IR
  and and_1 (and_1_out, ~stall, ~halt);  // AND_Gate
  Multiplexer #(.select(2), .width(32), .disabled("Z"), .enable("false")) multiplexer_1 (
    .in0(IF_PC_4), .in1(EX_AluResult), .in2(adder_2_out), .out(multiplexer_1_out),
    .sel({or_1_out[1], EX_JALR}));  // open: in3
  Hex_Digit_Display hex_digit_display_4 (.value(LedData[19:16]));  // open: dp
  Hex_Digit_Display hex_digit_display_5 (.value(LedData[15:12]));  // open: dp
  Register #(.width(32), .trigger("rising"), .Select("low")) PC (
    .D(multiplexer_1_out), .en(and_1_out), .Q(IF_PC), .clk(CLK), .clr(RST));
  Hex_Digit_Display hex_digit_display_6 (.value(LedData[11:8]));  // open: dp
  Hex_Digit_Display hex_digit_display_7 (.value(LedData[7:4]));  // open: dp
  // Probe on EX_PC[19:0]
  // RiscV_Probe riscv_probe_3: pin names not known; wires that end beside it: EX_IR
  Hex_Digit_Display hex_digit_display_8 (.value(LedData[3:0]));  // open: dp
  ROM #(.addrWidth(10), .dataWidth(32), .Select("high")) rom_1 (.addr(IF_PC[11:2]), .data(IF_IR));
  Adder #(.width(32)) adder_1 (.a(IF_PC), .b(32'h4), .out(IF_PC_4));  // open: cin, cout
  // Probe on \总周期数 
  // Probe on M_PC[19:0]
  // RiscV_Probe riscv_probe_4: pin names not known; wires that end beside it: MEM_IR
  // RiscV_Probe riscv_probe_5: pin names not known; wires that end beside it: IF_IR
  // Probe on \总周期数 
  // Probe on \无条件分支数 
  // Probe on \条件分支成功数 
  // Probe on \插入气泡数 
  // Probe on \LoadUse次数 
  IF_ID if_id_1 (
    .IR(IF_IR), .IR_2(ID_IR), .PC_2(ID_PC), .reset(RST), .en(and_1_out), .CLK(CLK), .PC_4(IF_PC_4),
    .PC_4_2(if_id_1_pc_4_2), .PC(IF_PC), .flush(or_2_out));  // open: PredictJump, PredictJump_2
  // Probe on IF_PC[11:0]
  // Probe on WB_PC[19:0]
  // RiscV_Probe riscv_probe_6: pin names not known; wires that end beside it: WB_IR
  // Probe on ID_PC[11:0]
  // Probe on EX_PC[11:0]
  \单周期硬布线控制器  \u_单周期硬布线控制器_1  (
    .Funct({ID_IR[30], ID_IR[25], ID_IR[14:12]}), .OP(ID_IR[6:2]), .ALU_OP(\单周期硬布线控制器_1_alu_op ),
    .MemToReg(\单周期硬布线控制器_1_memtoreg ), .MemWrite(\单周期硬布线控制器_1_memwrite ), .ALU_SRC(\单周期硬布线控制器_1_alu_src ),
    .RegWrite(\单周期硬布线控制器_1_regwrite ), .ecall(\单周期硬布线控制器_1_ecall ), .S_type(S_type),
    .Jalr(\单周期硬布线控制器_1_jalr ), .Beq(\单周期硬布线控制器_1_beq ), .JAL(ID_JAL), .Bne(\单周期硬布线控制器_1_bne ),
    .in_3(ID_IR[21]), .uret(\单周期硬布线控制器_1_uret ), .Lh(\单周期硬布线控制器_1_lh ), .Bge(\单周期硬布线控制器_1_bge ),
    .RS1Used(\单周期硬布线控制器_1_rs1used ), .RS2Used(\单周期硬布线控制器_1_rs2used ));  // open: CSR
  Multiplexer #(.select(1), .width(5), .disabled("Z"), .enable("false")) multiplexer_2 (
    .in0(ID_IR[19:15]), .in1(5'b10001), .out(multiplexer_2_out), .sel(\单周期硬布线控制器_1_ecall ));
  Multiplexer #(.select(1), .width(5), .disabled("Z"), .enable("false")) multiplexer_3 (
    .in0(ID_IR[24:20]), .in1(5'b01010), .out(multiplexer_3_out), .sel(\单周期硬布线控制器_1_ecall ));
  // Probe on M_PC[11:0]
  D_Flip_Flop #(.trigger("high"), .Pre_Clr_Positions("LEGACY"), .NegatePresetClear("false"), .enable("true"), .NewFFLayout("false")) d_ff_1 (.Q(d_ff_1_q));  // open: clk, D, Qn, preset, en, reset
  // Probe on 13'hc
  assign bit_extender_1_out = {{20{ID_IR[31]}}, ID_IR[31:20]};  // Bit_Extender bit_extender_1
  assign bit_extender_2_out = {{20{ID_IR[31]}}, {ID_IR[31:25], ID_IR[11:7]}};  // Bit_Extender bit_extender_2
  assign bit_extender_3_out = {{20{ID_IR[31]}}, {ID_IR[31], ID_IR[7], ID_IR[30:25], ID_IR[11:8]}};  // Bit_Extender bit_extender_3
  assign bit_extender_4_out = {{12{ID_IR[31]}}, {ID_IR[31], ID_IR[19:12], ID_IR[20], ID_IR[30:21]}};  // Bit_Extender bit_extender_4
  // Probe on WB_PC[11:0]
  Comparator #(.width(13), .mode("twosComplement")) comparator_1 (
    .a(CNT_num), .b(13'hc), .eq(comparator_1_eq), .lt(comparator_1_lt));  // open: gt
  Clock #(.highDuration(1), .lowDuration(1)) clock_1 (.out(clock_1_out));
  not not_1 (not_1_out, CLK);
  Multiplexer #(.select(1), .width(32), .disabled("Z"), .enable("false")) multiplexer_4 (
    .in0(bit_extender_1_out), .in1(bit_extender_2_out), .out(multiplexer_4_out), .sel(S_type));
  Multiplexer #(.select(1), .width(32), .disabled("Z"), .enable("false")) multiplexer_5 (
    .in0(bit_extender_3_out), .in1(bit_extender_4_out), .out(multiplexer_5_out), .sel(ID_JAL));
  nand nand_1 (nand_1_out, d_ff_1_q, comparator_1_eq);
  Counter #(.width(13), .max('h1fff), .ongoal("stay"), .trigger("rising"), .behavior("old")) counter_1 (
    .count(comparator_1_lt), .Q(CNT_num), .clk(clock_1_out));  // open: load, D, carry, clr, preset
  Regifile regifile_1 (
    .Din(RDin), .Clk(not_1_out), .R1(regifile_1_r1), .R2(regifile_1_r2), .WE(RegWrite), .W_num(WB_Rd),
    .R1_num(multiplexer_2_out), .R2_num(multiplexer_3_out));
  not not_2 (not_2_out, halt);
  assign CLK = nand_1_out ? clock_1_out : 1'bz;  // Controlled_Buffer controlled_buffer_1
  ID_EX id_ex_1 (
    .Bge(\单周期硬布线控制器_1_bge ), .Lh(\单周期硬布线控制器_1_lh ), .URET(\单周期硬布线控制器_1_uret ), .JALR(\单周期硬布线控制器_1_jalr ),
    .JAL(ID_JAL), .Beq(\单周期硬布线控制器_1_beq ), .Bne(\单周期硬布线控制器_1_bne ), .MemToReg(\单周期硬布线控制器_1_memtoreg ),
    .MemWrite(\单周期硬布线控制器_1_memwrite ), .AluOP(\单周期硬布线控制器_1_alu_op ), .AluSrcB(\单周期硬布线控制器_1_alu_src ),
    .RegWrite(\单周期硬布线控制器_1_regwrite ), .Bge_2(id_ex_1_bge_2), .Lh_2(id_ex_1_lh_2), .JALR_2(EX_JALR),
    .JAL_2(EX_JAL), .Beq_2(id_ex_1_beq_2), .Bne_2(id_ex_1_bne_2), .MemToReg_2(id_ex_1_memtoreg_2),
    .MemWrite_2(id_ex_1_memwrite_2), .AluOP_2(id_ex_1_aluop_2), .AluSrcB_2(id_ex_1_alusrcb_2),
    .RegWrite_2(id_ex_1_regwrite_2), .reset(RST), .en(not_2_out), .CLK(CLK), .ecall(\单周期硬布线控制器_1_ecall ),
    .ecall_2(id_ex_1_ecall_2), .R1_2(id_ex_1_r1_2), .R2(regifile_1_r2), .R2_2(id_ex_1_r2_2),
    .imm1(multiplexer_4_out), .imm1_2(id_ex_1_imm1_2), .imm2(multiplexer_5_out), .imm2_2(id_ex_1_imm2_2),
    .IR(ID_IR), .PC(ID_PC), .PC_2(EX_PC), .PC_4(if_id_1_pc_4_2), .PC_4_2(id_ex_1_pc_4_2), .R1(regifile_1_r1),
    .IR_2(EX_IR), .rd(ID_IR[11:7]), .rd_2(id_ex_1_rd_2), .flush(flush));  // open: URET_2, RS1Forward, RS1Forward_2, RS2Forward, RS2Forward_2, PredictJump, PredictJump_2
  Pull_Resistor #(.pull(1)) pull_resistor_1 (.node(CLK));
  or or_1 (or_1_out[1], EX_JAL, and_2_out, and_3_out, and_4_out);
  and and_2 (and_2_out, Ge, id_ex_1_bge_2);
  Shifter #(.width(32), .shift("ll")) shifter_1 (.in(id_ex_1_imm2_2), .\dist (5'b00001), .out(shifter_1_out));
  or or_2 (or_2_out, or_1_out[1], EX_JALR);
  and and_3 (and_3_out, id_ex_1_beq_2, Equal);
  and and_4 (and_4_out, ~Equal, id_ex_1_bne_2);  // AND_Gate
  Multiplexer #(.select(1), .width(32), .disabled("Z"), .enable("false")) multiplexer_6 (
    .in0(id_ex_1_r2_2), .in1(id_ex_1_imm1_2), .out(multiplexer_6_out), .sel(id_ex_1_alusrcb_2));
  Adder #(.width(32)) adder_2 (.a(shifter_1_out), .b(EX_PC), .out(adder_2_out));  // open: cin, cout
  not not_3 (not_3_out, halt);
  Counter #(.width(16), .max('hffff), .ongoal("wrap"), .trigger("rising"), .behavior("new")) counter_2 (
    .count(not_3_out), .Q(\总周期数 ), .clk(CLK), .clr(RST));  // open: load, D, carry, preset, down
  or or_3 (BranchCount, and_2_out, and_4_out, and_3_out);
  or or_4 (JumpCount, EX_JALR, EX_JAL);
  ALU alu_1 (
    .X(id_ex_1_r1_2), .Y(multiplexer_6_out), .AluOP(id_ex_1_aluop_2), .Equal(Equal), .Result(EX_AluResult),
    .out_4(Ge), .out_6(Less));  // open: Result_2
  Comparator #(.width(32), .mode("twosComplement")) comparator_2 (
    .a(id_ex_1_r1_2), .b(32'h22), .eq(comparator_2_eq));  // open: gt, lt
  and and_5 (and_5_out, ~halt, JumpCount);  // AND_Gate
  Counter #(.width(16), .max('hffff), .ongoal("wrap"), .trigger("rising"), .behavior("new")) counter_3 (
    .count(and_5_out), .Q(\无条件分支数 ), .clk(CLK), .clr(RST));  // open: load, D, carry, preset, down
  and and_6 (and_6_out, id_ex_1_ecall_2, ~comparator_2_eq);  // AND_Gate
  and and_7 (and_7_out, comparator_2_eq, id_ex_1_ecall_2);
  Register #(.width(32), .trigger("rising"), .Select("low")) register_1 (
    .D(id_ex_1_r2_2), .en(and_7_out), .Q(LedData), .clk(CLK), .clr(RST));
  not not_4 (not_4_out, halt);
  and and_8 (and_8_out, ~halt, BranchCount);  // AND_Gate
  EX_MEM ex_mem_1 (
    .Lh(id_ex_1_lh_2), .JALR(EX_JALR), .JAL(EX_JAL), .MemToReg(id_ex_1_memtoreg_2),
    .MemWrite(id_ex_1_memwrite_2), .RegWrite(id_ex_1_regwrite_2), .halt(and_6_out), .AluResult(EX_AluResult),
    .WriteData(id_ex_1_r2_2), .IR(EX_IR), .PC(EX_PC), .PC_4(id_ex_1_pc_4_2), .rd(id_ex_1_rd_2),
    .Lh_2(ex_mem_1_lh_2), .JALR_2(ex_mem_1_jalr_2), .JAL_2(ex_mem_1_jal_2), .MemToReg_2(ex_mem_1_memtoreg_2),
    .MemWrite_2(MemWrite), .RegWrite_2(ex_mem_1_regwrite_2), .halt_2(ex_mem_1_halt_2),
    .AluResult_2({ex_mem_1_aluresult_2, BitSel}), .WriteData_2(MDin), .IR_2(MEM_IR), .PC_2(M_PC),
    .PC_4_2(ex_mem_1_pc_4_2), .rd_2(ex_mem_1_rd_2), .reset(RST), .en(not_4_out), .CLK(CLK));
  Counter #(.width(16), .max('hffff), .ongoal("wrap"), .trigger("rising"), .behavior("new")) counter_4 (
    .count(and_8_out), .Q(\条件分支成功数 ), .clk(CLK), .clr(RST));  // open: load, D, carry, preset, down
  Multiplexer #(.select(1), .width(16), .disabled("Z"), .enable("false")) multiplexer_7 (
    .in0(MemData[15:0]), .in1(MemData[31:16]), .out(multiplexer_7_out), .sel(BitSel[1]));
  and and_9 (and_9_out, ~halt, flush);  // AND_Gate
  RAM #(.addrWidth(10), .dataWidth(32), .bus("separate"), .Select("high")) ram_1 (
    .addr(ex_mem_1_aluresult_2[11:2]), .din(MDin), .data(MemData), .str(MemWrite), .clk(CLK), .ld(not_5_out),
    .clr(RST));  // open: sel
  not not_5 (not_5_out, MemWrite);
  assign HalfMemData = {{16{multiplexer_7_out[15]}}, multiplexer_7_out};  // Bit_Extender bit_extender_5
  Counter #(.width(16), .max('hffff), .ongoal("wrap"), .trigger("rising"), .behavior("new")) counter_5 (
    .count(and_9_out), .Q(\插入气泡数 ), .clk(CLK), .clr(RST));  // open: load, D, carry, preset, down
  Multiplexer #(.select(1), .width(32), .disabled("Z"), .enable("false")) multiplexer_8 (
    .in0(MemData), .in1(HalfMemData), .out(multiplexer_8_out), .sel(ex_mem_1_lh_2));
  not not_6 (not_6_out, halt);
  and and_10 (and_10_out, ~halt, stall);  // AND_Gate
  MEM_WB mem_wb_1 (
    .JALR(ex_mem_1_jalr_2), .JAL(ex_mem_1_jal_2), .MemToReg(ex_mem_1_memtoreg_2),
    .RegWrite(ex_mem_1_regwrite_2), .halt(ex_mem_1_halt_2), .AluResult({ex_mem_1_aluresult_2, BitSel}),
    .ReadData(multiplexer_8_out), .IR(MEM_IR), .PC(M_PC), .PC_4(ex_mem_1_pc_4_2), .rd(ex_mem_1_rd_2),
    .JALR_2(mem_wb_1_jalr_2), .JAL_2(mem_wb_1_jal_2), .MemToReg_2(mem_wb_1_memtoreg_2),
    .RegWrite_2(RegWrite), .halt_2(mem_wb_1_halt_2), .AluResult_2(mem_wb_1_aluresult_2),
    .ReadData_2(mem_wb_1_readdata_2), .IR_2(WB_IR), .PC_2(WB_PC), .PC_4_2(mem_wb_1_pc_4_2), .rd_2(WB_Rd),
    .reset(RST), .en(not_6_out), .CLK(CLK));
  Counter #(.width(16), .max('hffff), .ongoal("wrap"), .trigger("rising"), .behavior("new")) counter_6 (
    .count(and_10_out), .Q(\LoadUse次数 ), .clk(CLK), .clr(RST));  // open: load, D, carry, preset, down
  D_Flip_Flop #(.trigger("rising"), .Pre_Clr_Positions("ABOVE_BELOW"), .NegatePresetClear("false"), .enable("true"), .NewFFLayout("true")) d_ff_2 (
    .clk(mem_wb_1_halt_2), .D(1'b1), .Q(halt), .en(1'b1), .reset(Go));  // open: Qn, preset
  or or_5 (or_5_out, mem_wb_1_jal_2, mem_wb_1_jalr_2);
  Multiplexer #(.select(1), .width(32), .disabled("Z"), .enable("false")) multiplexer_9 (
    .in0(mem_wb_1_aluresult_2), .in1(mem_wb_1_readdata_2), .out(multiplexer_9_out), .sel(mem_wb_1_memtoreg_2));
  Multiplexer #(.select(1), .width(32), .disabled("Z"), .enable("false")) multiplexer_10 (
    .in0(multiplexer_9_out), .in1(mem_wb_1_pc_4_2), .out(RDin), .sel(or_5_out));

  // Other names for the same wires on the sheet: MEM_PC[31:0] = M_PC

  // Notes on the sheet:
  //   中断源
  //   时空图监测，可删除
  //   中断等待指示
  //   stall
  //   数码管输出
  //   指令存储器
  //   contents of rom_1 (hex, n*v repeats v):
  //   100493 100006f 100493 200913 300993 100006f 100493 200913 300993 100006f 100493 200913 300993
  //   100006f 100493 200913 300993 29c000ef 100413 100493 1f49493 900533 2200893 73 24d493 48463 fedff06f
  //   900533 2200893 73 100493 249493 900533 2200893 73 48463 fedff06f 100493 1f49493 900533 2200893 73
  //   4034d493 900533 2200893 73 4044d493 900533 2200893 73 4044d493 900533 2200893 73 4044d493 900533
  //   2200893 73 4044d493 900533 2200893 73 4044d493 900533 2200893 73 4044d493 900533 2200893 73 4044d493
  //   900533 2200893 73 100413 1f41993 41f9d993 433 c00913 300b13 140413 f47413 800293 100313 499993
  //   89e9b3 1300533 2200893 73 406282b3 fe0294e3 140413 f00f93 1f47433 1c41413 800293 100313 49d993
  //   89e9b3 1300533 2200893 73 406282b3 fe0294e3 1c45413 406b0b33 b0463 f95ff06f 2b3 fff2c293 829293
  //   ff2e293 500533 2200893 73 fff00413 493 84a023 140413 448493 84a023 140413 448493 84a023 140413
  //   448493 84a023 140413 448493 84a023 140413 448493 84a023 140413 448493 84a023 140413 448493 84a023
  //   140413 448493 84a023 140413 448493 84a023 140413 448493 84a023 140413 448493 84a023 140413 448493
  //   84a023 140413 448493 84a023 140413 448493 84a023 140413 448493 84a023 140413 448493 140413 433
  //   3c00493 42983 4aa03 149a2b3 28663 134a023 1442023 ffc48493 fe9412e3 800533 2200893 73 440413 3c00493
  //   fc9416e3 a00893 73 413 140413 800533 2200893 73 240413 800533 2200893 73 340413 800533 2200893 73
  //   440413 800533 2200893 73 540413 800533 2200893 73 640413 800533 2200893 73 740413 800533 2200893 73
  //   840413 800533 2200893 2200893 73 8067
  //   指令探针
  //   指令字
  //   IR
  //   I型指令立即数 
  //   S型指令立即数 
  //   B型指令立即数 
  //   J型指令立即数 
  //   控制位
  //   RS1Used
  //   Beq
  //   JAL
  //   JALR
  //   Bne
  //   URET
  //   Lh
  //   Bge
  //   ecall
  //   流水调试日志用
  //   暂停节拍，不能为0
  //   RS2Used
  //   ecall
  //   MemToReg
  //   MemWrite
  //   AluOP
  //   AluSrcB
  //   RegWrite
  //   S_type
  //   戳工具置1进入计数暂停模式，ctrl+k时钟自动运行到对应节拍暂停
  //   ctrl+k关闭时钟连续运行，将控制位置零，进入单步调试模式调试
  //   Bge
  //   Lh
  //   URET
  //   JALR
  //   JAL
  //   imm1
  //   imm2
  //   rd 
  //   IR 
  //   PC 
  //   PC+4 
  //   可计数暂停的时钟源
  //   flush
  //   Beq
  //   Bne
  //   AluOP
  //   AluSrcB
  //   ecall
  //   R1
  //   R2
  //   MemToReg
  //   MemWrite
  //   RegWrite
  //   BranchTaken
  //   JumpAddr
  //   为方便自动评测，需要输出流水线各段保存的PC值，注意是PC不是PC+4，另外ID段寄存器写入信息，Mem段内存写入信息也要输出
  //   EX.RegWrite
  //   ecall
  //   EX.rd
  //   AluResult
  //   WriteData
  //   rd 
  //   IR 
  //   PC 
  //   PC+4 
  //   Lh
  //   JALR
  //   JAL
  //   MemToReg
  //   MemWrite
  //   RegWrite
  //   halt
  //   MEM.RegWrite
  //   数据存储器
  //   MEM.rd
  //   JALR
  //   JAL
  //   MemToReg
  //   RegWrite
  //   halt
  //   AluResult
  //   Lh
  //   ReadData
  //   rd 
  //   IR 
  //   PC 
  //   PC+4 
  //   JAL
  //   JALR
endmodule
module \重定向流水线  (
  output RegWrite,
  output MemWrite,
  output [31:0] IF_PC,
  output [31:0] ID_PC,
  output [31:0] EX_PC,
  output [31:0] M_PC,
  output [31:0] WB_PC,
  output [31:0] RDin,
  output [31:0] MDin,
  output [31:0] LedData
);

  wire and_1_out, and_2_out, and_3_out, and_4_out, and_5_out, and_6_out, and_7_out, and_8_out, and_9_out,
       and_10_out, BranchCount, CLK, clock_1_out, comparator_1_eq, comparator_1_lt, comparator_2_eq,
       d_ff_1_q, Equal, EX_JAL, EX_JALR, ex_mem_1_halt_2, ex_mem_1_jal_2, ex_mem_1_jalr_2, ex_mem_1_lh_2,
       ex_mem_1_memtoreg_2, ex_mem_1_regwrite_2, flush, Ge, Go, halt, id_ex_1_alusrcb_2, id_ex_1_beq_2,
       id_ex_1_bge_2, id_ex_1_bne_2, id_ex_1_ecall_2, id_ex_1_lh_2, id_ex_1_memtoreg_2, id_ex_1_memwrite_2,
       id_ex_1_regwrite_2, ID_JAL, IR1, IR2, IR3, JumpCount, Less, mem_wb_1_halt_2, mem_wb_1_jal_2,
       mem_wb_1_jalr_2, mem_wb_1_memtoreg_2, nand_1_out, not_1_out, not_2_out, not_3_out, not_4_out,
       not_5_out, not_6_out, or_2_out, or_5_out, RST, S_type, stall, W1, W2, W3, \单周期硬布线控制器_1_alu_src ,
       \单周期硬布线控制器_1_beq , \单周期硬布线控制器_1_bge , \单周期硬布线控制器_1_bne , \单周期硬布线控制器_1_ecall , \单周期硬布线控制器_1_jalr ,
       \单周期硬布线控制器_1_lh , \单周期硬布线控制器_1_memtoreg , \单周期硬布线控制器_1_memwrite , \单周期硬布线控制器_1_regwrite ,
       \单周期硬布线控制器_1_rs1used , \单周期硬布线控制器_1_rs2used , \单周期硬布线控制器_1_uret ;
  wire [1:0] BitSel, RS1Forward, RS2Forward, \重定向处理逻辑_1_rs1forward , \重定向处理逻辑_1_rs2forward ;
  wire [1:1] or_1_out;
  wire [3:0] id_ex_1_aluop_2, \单周期硬布线控制器_1_alu_op ;
  wire [4:0] ex_mem_1_rd_2, id_ex_1_rd_2, multiplexer_2_out, multiplexer_3_out, WB_Rd;
  wire [12:0] CNT_num;
  wire [15:0] \LoadUse次数 , multiplexer_9_out, \总周期数 , \插入气泡数 , \无条件分支数 , \条件分支成功数 ;
  wire [31:0] adder_2_out, bit_extender_1_out, bit_extender_2_out, bit_extender_3_out, bit_extender_4_out,
       EX_AluResult, EX_IR, ex_mem_1_pc_4_2, HalfMemData, id_ex_1_imm1_2, id_ex_1_imm2_2, id_ex_1_pc_4_2,
       id_ex_1_r1_2, id_ex_1_r2_2, ID_IR, if_id_1_pc_4_2, IF_IR, IF_PC_4, MEM_IR, mem_wb_1_aluresult_2,
       mem_wb_1_pc_4_2, mem_wb_1_readdata_2, MemData, multiplexer_1_out, multiplexer_4_out,
       multiplexer_5_out, multiplexer_6_out, multiplexer_7_out, multiplexer_8_out, multiplexer_10_out,
       multiplexer_11_out, regifile_1_r1, regifile_1_r2, shifter_1_out, WB_IR;
  wire [31:2] MEM_AluResult;

  Button \u_总复位  (.out(RST));
  Button _1 (.out(IR1));
  Button _2 (.out(IR2));
  Button _3 (.out(IR3));
  // Probe on \总周期数 
  // Probe on \总周期数 
  \重定向处理逻辑  \u_重定向处理逻辑_1  (
    .IR(ID_IR), .RS1Used(\单周期硬布线控制器_1_rs1used ), .EX_RegWrite(id_ex_1_regwrite_2), .EX_rd(id_ex_1_rd_2),
    .RS2Used(\单周期硬布线控制器_1_rs2used ), .MEM_RegWrite(ex_mem_1_regwrite_2), .MEM_rd(ex_mem_1_rd_2),
    .BranchTaken(or_2_out), .ecall(\单周期硬布线控制器_1_ecall ), .EX_MemToReg(id_ex_1_memtoreg_2), .stall(stall),
    .flush(flush), .RS1Forward(\重定向处理逻辑_1_rs1forward ), .RS2Forward(\重定向处理逻辑_1_rs2forward ));
  Button \u_继续运行  (.out(Go));
  LED #(.active("true")) led_1 (.in(W1));
  LED #(.active("true")) led_2 (.in(W2));
  LED #(.active("true")) led_3 (.in(W3));
  Hex_Digit_Display hex_digit_display_1 (.value(LedData[31:28]));  // open: dp
  // Probe on IF_PC[19:0]
  // RiscV_Probe riscv_probe_1: pin names not known; wires that end beside it: IF_IR
  Hex_Digit_Display hex_digit_display_2 (.value(LedData[27:24]));  // open: dp
  Hex_Digit_Display hex_digit_display_3 (.value(LedData[23:20]));  // open: dp
  // Probe on ID_PC[19:0]
  // RiscV_Probe riscv_probe_2: pin names not known; wires that end beside it: ID_IR
  and and_1 (and_1_out, ~stall, ~halt);  // AND_Gate
  Multiplexer #(.select(2), .width(32), .disabled("Z"), .enable("false")) multiplexer_1 (
    .in0(IF_PC_4), .in1(EX_AluResult), .in2(adder_2_out), .out(multiplexer_1_out),
    .sel({or_1_out[1], EX_JALR}));  // open: in3
  Hex_Digit_Display hex_digit_display_4 (.value(LedData[19:16]));  // open: dp
  Hex_Digit_Display hex_digit_display_5 (.value(LedData[15:12]));  // open: dp
  Register #(.width(32), .trigger("rising"), .Select("low")) PC (
    .D(multiplexer_1_out), .en(and_1_out), .Q(IF_PC), .clk(CLK), .clr(RST));
  Hex_Digit_Display hex_digit_display_6 (.value(LedData[7:4]));  // open: dp
  Hex_Digit_Display hex_digit_display_7 (.value(LedData[11:8]));  // open: dp
  // Probe on EX_PC[19:0]
  // RiscV_Probe riscv_probe_3: pin names not known; wires that end beside it: EX_IR
  Hex_Digit_Display hex_digit_display_8 (.value(LedData[3:0]));  // open: dp
  ROM #(.addrWidth(10), .dataWidth(32), .Select("high")) rom_1 (.addr(IF_PC[11:2]), .data(IF_IR));
  Adder #(.width(32)) adder_1 (.a(IF_PC), .b(32'h4), .out(IF_PC_4));  // open: cin, cout
  // Probe on \总周期数 
  // Probe on M_PC[19:0]
  // RiscV_Probe riscv_probe_4: pin names not known; wires that end beside it: MEM_IR
  // RiscV_Probe riscv_probe_5: pin names not known; wires that end beside it: IF_IR
  // Probe on \总周期数 
  // Probe on \无条件分支数 
  // Probe on \条件分支成功数 
  // Probe on \插入气泡数 
  // Probe on \LoadUse次数 
  IF_ID if_id_1 (
    .IR(IF_IR), .IR_2(ID_IR), .PC_2(ID_PC), .reset(RST), .en(and_1_out), .CLK(CLK), .PC_4(IF_PC_4),
    .PC_4_2(if_id_1_pc_4_2), .PC(IF_PC), .flush(or_2_out));  // open: PredictJump, PredictJump_2
  // Probe on IF_PC[11:0]
  // Probe on WB_PC[19:0]
  // RiscV_Probe riscv_probe_6: pin names not known; wires that end beside it: WB_IR
  // Probe on EX_PC[11:0]
  // Probe on ID_PC[11:0]
  \单周期硬布线控制器  \u_单周期硬布线控制器_1  (
    .Funct({ID_IR[30], ID_IR[25], ID_IR[14:12]}), .OP(ID_IR[6:2]), .ALU_OP(\单周期硬布线控制器_1_alu_op ),
    .MemToReg(\单周期硬布线控制器_1_memtoreg ), .MemWrite(\单周期硬布线控制器_1_memwrite ), .ALU_SRC(\单周期硬布线控制器_1_alu_src ),
    .RegWrite(\单周期硬布线控制器_1_regwrite ), .ecall(\单周期硬布线控制器_1_ecall ), .S_type(S_type),
    .Jalr(\单周期硬布线控制器_1_jalr ), .Beq(\单周期硬布线控制器_1_beq ), .JAL(ID_JAL), .Bne(\单周期硬布线控制器_1_bne ),
    .in_3(ID_IR[21]), .uret(\单周期硬布线控制器_1_uret ), .Lh(\单周期硬布线控制器_1_lh ), .Bge(\单周期硬布线控制器_1_bge ),
    .RS1Used(\单周期硬布线控制器_1_rs1used ), .RS2Used(\单周期硬布线控制器_1_rs2used ));  // open: CSR
  Multiplexer #(.select(1), .width(5), .disabled("Z"), .enable("false")) multiplexer_2 (
    .in0(ID_IR[19:15]), .in1(5'b10001), .out(multiplexer_2_out), .sel(\单周期硬布线控制器_1_ecall ));
  Multiplexer #(.select(1), .width(5), .disabled("Z"), .enable("false")) multiplexer_3 (
    .in0(ID_IR[24:20]), .in1(5'b01010), .out(multiplexer_3_out), .sel(\单周期硬布线控制器_1_ecall ));
  // Probe on M_PC[11:0]
  D_Flip_Flop #(.trigger("high"), .Pre_Clr_Positions("LEGACY"), .NegatePresetClear("false"), .enable("true"), .NewFFLayout("false")) d_ff_1 (.Q(d_ff_1_q));  // open: clk, D, Qn, preset, en, reset
  // Probe on 13'hc
  assign bit_extender_1_out = {{20{ID_IR[31]}}, ID_IR[31:20]};  // Bit_Extender bit_extender_1
  assign bit_extender_2_out = {{20{ID_IR[31]}}, {ID_IR[31:25], ID_IR[11:7]}};  // Bit_Extender bit_extender_2
  assign bit_extender_3_out = {{20{ID_IR[31]}}, {ID_IR[31], ID_IR[7], ID_IR[30:25], ID_IR[11:8]}};  // Bit_Extender bit_extender_3
  assign bit_extender_4_out = {{12{ID_IR[31]}}, {ID_IR[31], ID_IR[19:12], ID_IR[20], ID_IR[30:21]}};  // Bit_Extender bit_extender_4
  // Probe on WB_PC[11:0]
  Comparator #(.width(13), .mode("twosComplement")) comparator_1 (
    .a(CNT_num), .b(13'hc), .eq(comparator_1_eq), .lt(comparator_1_lt));  // open: gt
  Clock #(.highDuration(1), .lowDuration(1)) clock_1 (.out(clock_1_out));
  not not_1 (not_1_out, CLK);
  Multiplexer #(.select(1), .width(32), .disabled("Z"), .enable("false")) multiplexer_4 (
    .in0(bit_extender_1_out), .in1(bit_extender_2_out), .out(multiplexer_4_out), .sel(S_type));
  Multiplexer #(.select(1), .width(32), .disabled("Z"), .enable("false")) multiplexer_5 (
    .in0(bit_extender_3_out), .in1(bit_extender_4_out), .out(multiplexer_5_out), .sel(ID_JAL));
  nand nand_1 (nand_1_out, d_ff_1_q, comparator_1_eq);
  Counter #(.width(13), .max('h1fff), .ongoal("stay"), .trigger("rising"), .behavior("old")) counter_1 (
    .count(comparator_1_lt), .Q(CNT_num), .clk(clock_1_out));  // open: load, D, carry, clr, preset
  Regifile regifile_1 (
    .Din(RDin), .Clk(not_1_out), .R1(regifile_1_r1), .R2(regifile_1_r2), .WE(RegWrite), .W_num(WB_Rd),
    .R1_num(multiplexer_2_out), .R2_num(multiplexer_3_out));
  not not_2 (not_2_out, halt);
  assign CLK = nand_1_out ? clock_1_out : 1'bz;  // Controlled_Buffer controlled_buffer_1
  ID_EX id_ex_1 (
    .Bge(\单周期硬布线控制器_1_bge ), .Lh(\单周期硬布线控制器_1_lh ), .URET(\单周期硬布线控制器_1_uret ), .JALR(\单周期硬布线控制器_1_jalr ),
    .JAL(ID_JAL), .Beq(\单周期硬布线控制器_1_beq ), .Bne(\单周期硬布线控制器_1_bne ), .MemToReg(\单周期硬布线控制器_1_memtoreg ),
    .MemWrite(\单周期硬布线控制器_1_memwrite ), .AluOP(\单周期硬布线控制器_1_alu_op ), .AluSrcB(\单周期硬布线控制器_1_alu_src ),
    .RegWrite(\单周期硬布线控制器_1_regwrite ), .Bge_2(id_ex_1_bge_2), .Lh_2(id_ex_1_lh_2), .JALR_2(EX_JALR),
    .JAL_2(EX_JAL), .Beq_2(id_ex_1_beq_2), .Bne_2(id_ex_1_bne_2), .MemToReg_2(id_ex_1_memtoreg_2),
    .MemWrite_2(id_ex_1_memwrite_2), .AluOP_2(id_ex_1_aluop_2), .AluSrcB_2(id_ex_1_alusrcb_2),
    .RegWrite_2(id_ex_1_regwrite_2), .reset(RST), .en(not_2_out), .CLK(CLK), .ecall(\单周期硬布线控制器_1_ecall ),
    .ecall_2(id_ex_1_ecall_2), .R1_2(id_ex_1_r1_2), .R2(regifile_1_r2), .R2_2(id_ex_1_r2_2),
    .imm1(multiplexer_4_out), .imm1_2(id_ex_1_imm1_2), .imm2(multiplexer_5_out), .imm2_2(id_ex_1_imm2_2),
    .IR(ID_IR), .PC(ID_PC), .PC_2(EX_PC), .PC_4(if_id_1_pc_4_2), .PC_4_2(id_ex_1_pc_4_2), .R1(regifile_1_r1),
    .IR_2(EX_IR), .rd(ID_IR[11:7]), .rd_2(id_ex_1_rd_2), .flush(flush), .RS1Forward(\重定向处理逻辑_1_rs1forward ),
    .RS1Forward_2(RS1Forward), .RS2Forward(\重定向处理逻辑_1_rs2forward ), .RS2Forward_2(RS2Forward));  // open: URET_2, PredictJump, PredictJump_2
  Pull_Resistor #(.pull(1)) pull_resistor_1 (.node(CLK));
  or or_1 (or_1_out[1], EX_JAL, and_2_out, and_3_out, and_4_out);
  and and_2 (and_2_out, Ge, id_ex_1_bge_2);
  Shifter #(.width(32), .shift("ll")) shifter_1 (.in(id_ex_1_imm2_2), .\dist (5'b00001), .out(shifter_1_out));
  or or_2 (or_2_out, or_1_out[1], EX_JALR);
  and and_3 (and_3_out, id_ex_1_beq_2, Equal);
  and and_4 (and_4_out, ~Equal, id_ex_1_bne_2);  // AND_Gate
  Multiplexer #(.select(2), .width(32), .disabled("Z"), .enable("false")) multiplexer_6 (
    .in0(id_ex_1_r2_2), .in1(RDin), .in2({MEM_AluResult, BitSel}), .out(multiplexer_6_out), .sel(RS2Forward));  // open: in3
  Adder #(.width(32)) adder_2 (.a(shifter_1_out), .b(EX_PC), .out(adder_2_out));  // open: cin, cout
  not not_3 (not_3_out, halt);
  Counter #(.width(16), .max('hffff), .ongoal("wrap"), .trigger("rising"), .behavior("new")) counter_2 (
    .count(not_3_out), .Q(\总周期数 ), .clk(CLK), .clr(RST));  // open: load, D, carry, preset, down
  or or_3 (BranchCount, and_2_out, and_4_out, and_3_out);
  or or_4 (JumpCount, EX_JALR, EX_JAL);
  Multiplexer #(.select(2), .width(32), .disabled("Z"), .enable("false")) multiplexer_7 (
    .in0(id_ex_1_r1_2), .in1(RDin), .in2({MEM_AluResult, BitSel}), .out(multiplexer_7_out), .sel(RS1Forward));  // open: in3
  Multiplexer #(.select(1), .width(32), .disabled("Z"), .enable("false")) multiplexer_8 (
    .in0(multiplexer_6_out), .in1(id_ex_1_imm1_2), .out(multiplexer_8_out), .sel(id_ex_1_alusrcb_2));
  ALU alu_1 (
    .X(multiplexer_7_out), .Y(multiplexer_8_out), .AluOP(id_ex_1_aluop_2), .Equal(Equal),
    .Result(EX_AluResult), .out_4(Ge), .out_6(Less));  // open: Result_2
  Comparator #(.width(32), .mode("twosComplement")) comparator_2 (
    .a(multiplexer_7_out), .b(32'h22), .eq(comparator_2_eq));  // open: gt, lt
  and and_5 (and_5_out, ~halt, JumpCount);  // AND_Gate
  Counter #(.width(16), .max('hffff), .ongoal("wrap"), .trigger("rising"), .behavior("new")) counter_3 (
    .count(and_5_out), .Q(\无条件分支数 ), .clk(CLK), .clr(RST));  // open: load, D, carry, preset, down
  and and_6 (and_6_out, id_ex_1_ecall_2, ~comparator_2_eq);  // AND_Gate
  and and_7 (and_7_out, comparator_2_eq, id_ex_1_ecall_2);
  Register #(.width(32), .trigger("rising"), .Select("low")) register_1 (
    .D(multiplexer_6_out), .en(and_7_out), .Q(LedData), .clk(CLK), .clr(RST));
  not not_4 (not_4_out, halt);
  and and_8 (and_8_out, ~halt, BranchCount);  // AND_Gate
  EX_MEM ex_mem_1 (
    .Lh(id_ex_1_lh_2), .JALR(EX_JALR), .JAL(EX_JAL), .MemToReg(id_ex_1_memtoreg_2),
    .MemWrite(id_ex_1_memwrite_2), .RegWrite(id_ex_1_regwrite_2), .halt(and_6_out), .AluResult(EX_AluResult),
    .WriteData(multiplexer_6_out), .IR(EX_IR), .PC(EX_PC), .PC_4(id_ex_1_pc_4_2), .rd(id_ex_1_rd_2),
    .Lh_2(ex_mem_1_lh_2), .JALR_2(ex_mem_1_jalr_2), .JAL_2(ex_mem_1_jal_2), .MemToReg_2(ex_mem_1_memtoreg_2),
    .MemWrite_2(MemWrite), .RegWrite_2(ex_mem_1_regwrite_2), .halt_2(ex_mem_1_halt_2),
    .AluResult_2({MEM_AluResult, BitSel}), .WriteData_2(MDin), .IR_2(MEM_IR), .PC_2(M_PC),
    .PC_4_2(ex_mem_1_pc_4_2), .rd_2(ex_mem_1_rd_2), .reset(RST), .en(not_4_out), .CLK(CLK));
  Counter #(.width(16), .max('hffff), .ongoal("wrap"), .trigger("rising"), .behavior("new")) counter_4 (
    .count(and_8_out), .Q(\条件分支成功数 ), .clk(CLK), .clr(RST));  // open: load, D, carry, preset, down
  Multiplexer #(.select(1), .width(16), .disabled("Z"), .enable("false")) multiplexer_9 (
    .in0(MemData[15:0]), .in1(MemData[31:16]), .out(multiplexer_9_out), .sel(BitSel[1]));
  and and_9 (and_9_out, ~halt, flush);  // AND_Gate
  RAM #(.addrWidth(10), .dataWidth(32), .bus("separate"), .Select("high")) ram_1 (
    .addr(MEM_AluResult[11:2]), .din(MDin), .data(MemData), .str(MemWrite), .clk(CLK), .ld(not_5_out),
    .clr(RST));  // open: sel
  not not_5 (not_5_out, MemWrite);
  assign HalfMemData = {{16{multiplexer_9_out[15]}}, multiplexer_9_out};  // Bit_Extender bit_extender_5
  Counter #(.width(16), .max('hffff), .ongoal("wrap"), .trigger("rising"), .behavior("new")) counter_5 (
    .count(and_9_out), .Q(\插入气泡数 ), .clk(CLK), .clr(RST));  // open: load, D, carry, preset, down
  Multiplexer #(.select(1), .width(32), .disabled("Z"), .enable("false")) multiplexer_10 (
    .in0(MemData), .in1(HalfMemData), .out(multiplexer_10_out), .sel(ex_mem_1_lh_2));
  not not_6 (not_6_out, halt);
  and and_10 (and_10_out, ~halt, stall);  // AND_Gate
  MEM_WB mem_wb_1 (
    .JALR(ex_mem_1_jalr_2), .JAL(ex_mem_1_jal_2), .MemToReg(ex_mem_1_memtoreg_2),
    .RegWrite(ex_mem_1_regwrite_2), .halt(ex_mem_1_halt_2), .AluResult({MEM_AluResult, BitSel}),
    .ReadData(multiplexer_10_out), .IR(MEM_IR), .PC(M_PC), .PC_4(ex_mem_1_pc_4_2), .rd(ex_mem_1_rd_2),
    .JALR_2(mem_wb_1_jalr_2), .JAL_2(mem_wb_1_jal_2), .MemToReg_2(mem_wb_1_memtoreg_2),
    .RegWrite_2(RegWrite), .halt_2(mem_wb_1_halt_2), .AluResult_2(mem_wb_1_aluresult_2),
    .ReadData_2(mem_wb_1_readdata_2), .IR_2(WB_IR), .PC_2(WB_PC), .PC_4_2(mem_wb_1_pc_4_2), .rd_2(WB_Rd),
    .reset(RST), .en(not_6_out), .CLK(CLK));
  Counter #(.width(16), .max('hffff), .ongoal("wrap"), .trigger("rising"), .behavior("new")) counter_6 (
    .count(and_10_out), .Q(\LoadUse次数 ), .clk(CLK), .clr(RST));  // open: load, D, carry, preset, down
  D_Flip_Flop #(.trigger("rising"), .Pre_Clr_Positions("ABOVE_BELOW"), .NegatePresetClear("false"), .enable("true"), .NewFFLayout("true")) d_ff_2 (
    .clk(mem_wb_1_halt_2), .D(1'b1), .Q(halt), .en(1'b1), .reset(Go));  // open: Qn, preset
  or or_5 (or_5_out, mem_wb_1_jal_2, mem_wb_1_jalr_2);
  Multiplexer #(.select(1), .width(32), .disabled("Z"), .enable("false")) multiplexer_11 (
    .in0(mem_wb_1_aluresult_2), .in1(mem_wb_1_readdata_2), .out(multiplexer_11_out), .sel(mem_wb_1_memtoreg_2));
  Multiplexer #(.select(1), .width(32), .disabled("Z"), .enable("false")) multiplexer_12 (
    .in0(multiplexer_11_out), .in1(mem_wb_1_pc_4_2), .out(RDin), .sel(or_5_out));

  // Other names for the same wires on the sheet: MEM_AluResult[1:0] = BitSel; MEM_PC[31:0] = M_PC

  // Notes on the sheet:
  //   中断源
  //   时空图监测，可删除
  //   中断等待指示
  //   stall
  //   数码管输出
  //   指令存储器
  //   contents of rom_1 (hex, n*v repeats v):
  //   100493 100006f 100493 200913 300993 100006f 100493 200913 300993 100006f 100493 200913 300993
  //   100006f 100493 200913 300993 29c000ef 100413 100493 1f49493 900533 2200893 73 24d493 48463 fedff06f
  //   900533 2200893 73 100493 249493 900533 2200893 73 48463 fedff06f 100493 1f49493 900533 2200893 73
  //   4034d493 900533 2200893 73 4044d493 900533 2200893 73 4044d493 900533 2200893 73 4044d493 900533
  //   2200893 73 4044d493 900533 2200893 73 4044d493 900533 2200893 73 4044d493 900533 2200893 73 4044d493
  //   900533 2200893 73 100413 1f41993 41f9d993 433 c00913 300b13 140413 f47413 800293 100313 499993
  //   89e9b3 1300533 2200893 73 406282b3 fe0294e3 140413 f00f93 1f47433 1c41413 800293 100313 49d993
  //   89e9b3 1300533 2200893 73 406282b3 fe0294e3 1c45413 406b0b33 b0463 f95ff06f 2b3 fff2c293 829293
  //   ff2e293 500533 2200893 73 fff00413 493 84a023 140413 448493 84a023 140413 448493 84a023 140413
  //   448493 84a023 140413 448493 84a023 140413 448493 84a023 140413 448493 84a023 140413 448493 84a023
  //   140413 448493 84a023 140413 448493 84a023 140413 448493 84a023 140413 448493 84a023 140413 448493
  //   84a023 140413 448493 84a023 140413 448493 84a023 140413 448493 84a023 140413 448493 140413 433
  //   3c00493 42983 4aa03 149a2b3 28663 134a023 1442023 ffc48493 fe9412e3 800533 2200893 73 440413 3c00493
  //   fc9416e3 a00893 73 413 140413 800533 2200893 73 240413 800533 2200893 73 340413 800533 2200893 73
  //   440413 800533 2200893 73 540413 800533 2200893 73 640413 800533 2200893 73 740413 800533 2200893 73
  //   840413 800533 2200893 2200893 73 8067
  //   指令探针
  //   指令字
  //   IR
  //   I型指令立即数 
  //   S型指令立即数 
  //   B型指令立即数 
  //   J型指令立即数 
  //   控制位
  //   RS1Used
  //   Beq
  //   JAL
  //   JALR
  //   Bne
  //   URET
  //   Lh
  //   Bge
  //   ecall
  //   流水调试日志用
  //   暂停节拍，不能为0
  //   RS2Used
  //   ecall
  //   MemToReg
  //   MemWrite
  //   AluOP
  //   AluSrcB
  //   RegWrite
  //   S_type
  //   戳工具置1进入计数暂停模式，ctrl+k时钟自动运行到对应节拍暂停
  //   ctrl+k关闭时钟连续运行，将控制位置零，进入单步调试模式调试
  //   RS1Forward
  //   imm1
  //   imm2
  //   rd 
  //   IR 
  //   PC 
  //   PC+4 
  //   可计数暂停的时钟源
  //   RS2Forward
  //   flush
  //   Bge
  //   Lh
  //   URET
  //   JALR
  //   JAL
  //   Beq
  //   Bne
  //   AluOP
  //   AluSrcB
  //   ecall
  //   R1
  //   R2
  //   MemToReg
  //   MemWrite
  //   RegWrite
  //   BranchTaken
  //   JumpAddr
  //   为方便自动评测，需要输出流水线各段保存的PC值，注意是PC不是PC+4，另外ID段寄存器写入信息，Mem段内存写入信息也要输出
  //   EX.RegWrite
  //   ecall
  //   EX.rd
  //   MemToReg
  //   AluResult
  //   WriteData
  //   rd 
  //   IR 
  //   PC 
  //   PC+4 
  //   Lh
  //   JALR
  //   JAL
  //   MemToReg
  //   MemWrite
  //   RegWrite
  //   halt
  //   MEM.RegWrite
  //   数据存储器
  //   MEM.rd
  //   JALR
  //   JAL
  //   MemToReg
  //   RegWrite
  //   halt
  //   AluResult
  //   Lh
  //   ReadData
  //   rd 
  //   IR 
  //   PC 
  //   PC+4 
  //   JAL
  //   JALR
endmodule

module \中断按键参考电路  (
  input  \同步清零信号 ,
  output \与中断屏蔽位与 
);

  wire \_1号中断_out , and_1_out, clock_1_out, d_ff_1_q, or_1_out, or_2_out;

  Clock #(.highDuration(1), .lowDuration(1)) clock_1 (.out(clock_1_out));
  Button \_1号中断  (.out(\_1号中断_out ));
  or or_1 (or_1_out, \与中断屏蔽位与 , d_ff_1_q);
  LED #(.active("true")) \_1号中断等待指示灯  (.in(or_1_out));
  D_Flip_Flop #(.trigger("rising"), .Pre_Clr_Positions("LEGACY"), .NegatePresetClear("false"), .enable("true"), .NewFFLayout("false")) d_ff_1 (
    .clk(\_1号中断_out ), .D(1'b1), .Q(d_ff_1_q), .reset(\与中断屏蔽位与 ));  // open: Qn, preset, en
  or or_2 (or_2_out, d_ff_1_q, \与中断屏蔽位与 );
  and and_1 (and_1_out, or_2_out, ~\同步清零信号 );  // AND_Gate
  D_Flip_Flop #(.trigger("rising"), .Pre_Clr_Positions("LEGACY"), .NegatePresetClear("false"), .enable("true"), .NewFFLayout("false")) IR1 (
    .clk(clock_1_out), .D(and_1_out), .Q(\与中断屏蔽位与 ));  // open: Qn, preset, en, reset

  // Notes on the sheet:
  //   中断信号采样参考电路
  //   Reset 
endmodule

module \单周期_单级中断  (
  input  IR1,
  input  IR2,
  input  IR3,
  output RegWrite,
  output MemWrite,
  output [31:0] PC,
  output [31:0] IR,
  output [31:0] RDin,
  output [31:0] MDin,
  output [31:0] LedData
);

  wire AluSrcB, and_1_out, and_2_out, and_3_out, and_4_out, and_5_out, and_6_out, and_8_out, and_9_out, Beq,
       Bge, Bne, Branch, CLK, clock_1_out, comparator_1_eq, comparator_2_eq, comparator_3_eq,
       comparator_4_eq, comparator_5_eq, comparator_6_eq, comparator_7_eq, comparator_7_lt, d_ff_1_q,
       d_ff_2_q, d_ff_3_q, d_ff_5_q, ecall, Equal, Ge, Go, halt, IE, Intr, IR1_q, IR1_t, IR1Reset, IR2_q,
       IR2_t, IR2Reset, IR3_q, IR3_t, IR3Reset, IRA, IRB, IRC, JAL, JALR, Less, Lh, MemToReg, nand_1_out,
       not_1_out, not_2_out, not_3_out, not_4_out, or_5_out, or_6_out, or_7_out, or_8_out, or_12_out,
       or_13_out, priority_encoder_2_gs, RST, S_type, URET, W1, W2, W3;
  wire [1:0] IRIndex, priority_encoder_1_out, register_2_q;
  wire [3:0] AluOP;
  wire [4:0] multiplexer_2_out, multiplexer_3_out;
  wire [12:0] CNT_num;
  wire [15:0] multiplexer_10_out, \总周期数 ;
  wire [31:0] adder_2_out, adder_3_out, AluResult, bit_extender_1_out, bit_extender_2_out,
       bit_extender_3_out, bit_extender_4_out, EPC, HalfMemData, MemData, multiplexer_4_out,
       multiplexer_5_out, multiplexer_6_out, multiplexer_7_out, multiplexer_9_out, multiplexer_11_out, PC_4,
       PCNext, PCNorm, R1Data, shifter_1_out, shifter_2_out;

  Button \u_继续运行  (.out(Go));
  Button _1 ();  // open: out
  Button _2 ();  // open: out
  Button _3 ();  // open: out
  Button \u_总复位  (.out(RST));
  LED #(.active("true")) led_1 (.in(W1));
  LED #(.active("true")) led_2 (.in(W2));
  LED #(.active("true")) led_3 (.in(W3));
  Hex_Digit_Display hex_digit_display_1 (.value(LedData[31:28]));  // open: dp
  and and_1 (and_1_out, Beq, Equal);
  and and_2 (and_2_out, ~Equal, Bne);  // AND_Gate
  and and_3 (and_3_out, Bge, Ge);
  Priority_Encoder #(.select(2), .disabled("Z")) priority_encoder_1 (
    .in0(1'b1), .in1(JALR), .in2(JAL), .in3(Branch), .out(priority_encoder_1_out));  // open: gs, en_out, en_in
  Multiplexer #(.select(2), .width(32), .disabled("Z"), .enable("false")) multiplexer_1 (
    .in0(PC_4), .in1(AluResult), .in2(adder_3_out), .in3(adder_2_out), .out(PCNorm),
    .sel(priority_encoder_1_out));
  or or_1 (W1, IR1_q, d_ff_1_q);
  LED #(.active("true")) \_1号中断等待指示灯  (.in(W1));
  LED #(.active("true")) \_2号中断等待指示灯  (.in(W2));
  or or_2 (W2, IR2_q, d_ff_2_q);
  or or_3 (W3, IR3_q, d_ff_3_q);
  LED #(.active("true")) \_3号中断等待指示灯  (.in(W3));
  Hex_Digit_Display hex_digit_display_2 (.value(LedData[27:24]));  // open: dp
  Hex_Digit_Display hex_digit_display_3 (.value(LedData[23:20]));  // open: dp
  or or_4 (Branch, and_1_out, and_2_out, and_3_out);
  Register #(.width(32), .trigger("rising"), .Select("low")) u_PC (
    .D(PCNext), .en(not_1_out), .Q(PC), .clk(CLK), .clr(RST));
  not not_1 (not_1_out, halt);
  D_Flip_Flop #(.trigger("rising"), .Pre_Clr_Positions("LEGACY"), .NegatePresetClear("false"), .enable("true"), .NewFFLayout("false")) d_ff_1 (
    .clk(IR1_t), .D(1'b1), .Q(d_ff_1_q), .reset(IR1_q));  // open: Qn, preset, en
  D_Flip_Flop #(.trigger("rising"), .Pre_Clr_Positions("LEGACY"), .NegatePresetClear("false"), .enable("true"), .NewFFLayout("false")) d_ff_2 (
    .clk(IR2_t), .D(1'b1), .Q(d_ff_2_q), .reset(IR2_q));  // open: Qn, preset, en
  D_Flip_Flop #(.trigger("rising"), .Pre_Clr_Positions("LEGACY"), .NegatePresetClear("false"), .enable("true"), .NewFFLayout("false")) d_ff_3 (
    .clk(IR3_t), .D(1'b1), .Q(d_ff_3_q), .reset(IR3_q));  // open: Qn, preset, en
  Hex_Digit_Display hex_digit_display_4 (.value(LedData[15:12]));  // open: dp
  Hex_Digit_Display hex_digit_display_5 (.value(LedData[19:16]));  // open: dp
  or or_5 (or_5_out, d_ff_1_q, IR1_q);
  or or_6 (or_6_out, d_ff_2_q, IR2_q);
  or or_7 (or_7_out, d_ff_3_q, IR3_q);
  Comparator #(.width(16), .mode("twosComplement")) comparator_1 (
    .a(16'h23b), .b(\总周期数 ), .eq(comparator_1_eq));  // open: gt, lt
  Comparator #(.width(16), .mode("twosComplement")) comparator_2 (
    .a(\总周期数 ), .b(16'h1), .eq(comparator_2_eq));  // open: gt, lt
  Comparator #(.width(16), .mode("twosComplement")) comparator_3 (
    .a(\总周期数 ), .b(16'h4), .eq(comparator_3_eq));  // open: gt, lt
  Comparator #(.width(16), .mode("twosComplement")) comparator_4 (
    .a(\总周期数 ), .b(16'h7), .eq(comparator_4_eq));  // open: gt, lt
  Hex_Digit_Display hex_digit_display_6 (.value(LedData[11:8]));  // open: dp
  Hex_Digit_Display hex_digit_display_7 (.value(LedData[7:4]));  // open: dp
  // Probe on \总周期数 
  // RiscV_Probe riscv_probe_1: pin names not known; wires that end beside it: IR
  ROM #(.addrWidth(10), .dataWidth(32), .Select("high")) rom_1 (.addr(PC[11:2]), .data(IR));
  Adder #(.width(32)) adder_1 (.a(PC), .b(32'h4), .out(PC_4));  // open: cin, cout
  and and_4 (and_4_out, or_5_out, ~IR1Reset);  // AND_Gate
  and and_5 (and_5_out, or_6_out, ~IR2Reset);  // AND_Gate
  and and_6 (and_6_out, or_7_out, ~IR3Reset);  // AND_Gate
  or or_8 (or_8_out, comparator_1_eq, comparator_2_eq);
  Pull_Resistor #(.pull(0)) pull_resistor_1 (.node(IRA));
  assign IRA = or_8_out ? ~CLK : 1'bz;  // Controlled_Inverter controlled_inverter_1
  Pull_Resistor #(.pull(0)) pull_resistor_2 (.node(IRB));
  assign IRB = comparator_3_eq ? ~CLK : 1'bz;  // Controlled_Inverter controlled_inverter_2
  Pull_Resistor #(.pull(0)) pull_resistor_3 (.node(IRC));
  assign IRC = comparator_4_eq ? ~CLK : 1'bz;  // Controlled_Inverter controlled_inverter_3
  Hex_Digit_Display hex_digit_display_8 (.value(LedData[3:0]));  // open: dp
  D_Flip_Flop #(.trigger("rising"), .Pre_Clr_Positions("LEGACY"), .NegatePresetClear("false"), .enable("true"), .NewFFLayout("false")) u_IR1 (
    .clk(CLK), .D(and_4_out), .Q(IR1_q), .reset(RST));  // open: Qn, preset, en
  D_Flip_Flop #(.trigger("rising"), .Pre_Clr_Positions("LEGACY"), .NegatePresetClear("false"), .enable("true"), .NewFFLayout("false")) u_IR2 (
    .clk(CLK), .D(and_5_out), .Q(IR2_q), .reset(RST));  // open: Qn, preset, en
  D_Flip_Flop #(.trigger("rising"), .Pre_Clr_Positions("LEGACY"), .NegatePresetClear("false"), .enable("true"), .NewFFLayout("false")) u_IR3 (
    .clk(CLK), .D(and_6_out), .Q(IR3_q), .reset(RST));  // open: Qn, preset, en
  \单周期硬布线控制器  \u_单周期硬布线控制器_1  (
    .Funct({IR[30], IR[25], IR[14:12]}), .OP(IR[6:2]), .ALU_OP(AluOP), .MemToReg(MemToReg),
    .MemWrite(MemWrite), .ALU_SRC(AluSrcB), .RegWrite(RegWrite), .ecall(ecall), .S_type(S_type), .Jalr(JALR),
    .Beq(Beq), .JAL(JAL), .Bne(Bne), .in_3(IR[21]), .uret(URET), .Lh(Lh), .Bge(Bge));  // open: RS1Used, RS2Used, CSR
  Multiplexer #(.select(1), .width(5), .disabled("Z"), .enable("false")) multiplexer_2 (
    .in0(IR[19:15]), .in1(5'b10001), .out(multiplexer_2_out), .sel(ecall));
  Multiplexer #(.select(1), .width(5), .disabled("Z"), .enable("false")) multiplexer_3 (
    .in0(IR[24:20]), .in1(5'b01010), .out(multiplexer_3_out), .sel(ecall));
  Priority_Encoder #(.select(2), .disabled("Z")) priority_encoder_2 (
    .in1(IR1_q), .in2(IR2_q), .in3(IR3_q), .out(IRIndex), .gs(priority_encoder_2_gs));  // open: in0, en_out, en_in
  or or_9 (IR1_t, IR1, IRA);
  assign bit_extender_1_out = {{20{IR[31]}}, IR[31:20]};  // Bit_Extender bit_extender_1
  assign bit_extender_2_out = {{20{IR[31]}}, {IR[31:25], IR[11:7]}};  // Bit_Extender bit_extender_2
  assign bit_extender_3_out = {{20{IR[31]}}, {IR[31], IR[7], IR[30:25], IR[11:8]}};  // Bit_Extender bit_extender_3
  assign bit_extender_4_out = {{12{IR[31]}}, {IR[31], IR[19:12], IR[20], IR[30:21]}};  // Bit_Extender bit_extender_4
  and and_7 (Intr, priority_encoder_2_gs, IE);
  or or_10 (IR2_t, IR2, IRB);
  Multiplexer #(.select(1), .width(32), .disabled("Z"), .enable("false")) multiplexer_4 (
    .in0(bit_extender_1_out), .in1(bit_extender_2_out), .out(multiplexer_4_out), .sel(S_type));
  Shifter #(.width(32), .shift("ll")) shifter_1 (.in(bit_extender_3_out), .\dist (5'b00001), .out(shifter_1_out));
  Shifter #(.width(32), .shift("ll")) shifter_2 (.in(bit_extender_4_out), .\dist (5'b00001), .out(shifter_2_out));
  Multiplexer #(.select(2), .width(32), .disabled("Z"), .enable("false")) multiplexer_5 (
    .in1(32'h30ac), .in2(32'h3150), .in3(32'h31f4), .out(multiplexer_5_out), .sel(IRIndex));  // open: in0
  Regifile regifile_1 (
    .Din(RDin), .Clk(CLK), .R1(R1Data), .R2(MDin), .WE(RegWrite), .W_num(IR[11:7]),
    .R1_num(multiplexer_2_out), .R2_num(multiplexer_3_out));
  Multiplexer #(.select(1), .width(32), .disabled("Z"), .enable("false")) multiplexer_6 (
    .in0(PCNorm), .in1(multiplexer_5_out), .out(multiplexer_6_out), .sel(Intr));
  or or_11 (IR3_t, IR3, IRC);
  Multiplexer #(.select(1), .width(32), .disabled("Z"), .enable("false")) multiplexer_7 (
    .in0(MDin), .in1(multiplexer_4_out), .out(multiplexer_7_out), .sel(AluSrcB));
  Adder #(.width(32)) adder_2 (.a(shifter_1_out), .b(PC), .out(adder_2_out));  // open: cin, cout
  Adder #(.width(32)) adder_3 (.a(shifter_2_out), .b(PC), .out(adder_3_out));  // open: cin, cout
  not not_2 (not_2_out, halt);
  Counter #(.width(16), .max('hffff), .ongoal("wrap"), .trigger("rising"), .behavior("new")) counter_1 (
    .count(not_2_out), .Q(\总周期数 ), .clk(CLK));  // open: load, D, carry, clr, preset, down
  ALU alu_1 (
    .X(R1Data), .Y(multiplexer_7_out), .AluOP(AluOP), .Equal(Equal), .Result(AluResult), .out_4(Ge),
    .out_6(Less));  // open: Result_2
  Comparator #(.width(32), .mode("twosComplement")) comparator_5 (
    .a(R1Data), .b(32'h22), .eq(comparator_5_eq));  // open: gt, lt
  Multiplexer #(.select(1), .width(32), .disabled("Z"), .enable("false")) multiplexer_8 (
    .in0(multiplexer_6_out), .in1(EPC), .out(PCNext), .sel(URET));
  and and_8 (and_8_out, ecall, ~comparator_5_eq);  // AND_Gate
  and and_9 (and_9_out, comparator_5_eq, ecall);
  D_Flip_Flop #(.trigger("falling"), .Pre_Clr_Positions("ABOVE_BELOW"), .NegatePresetClear("false"), .enable("true"), .NewFFLayout("true")) d_ff_4 (
    .clk(CLK), .D(and_8_out), .Q(halt), .en(ecall), .reset(Go));  // open: Qn, preset
  Register #(.width(32), .trigger("rising"), .Select("low")) register_1 (
    .D(MDin), .en(and_9_out), .Q(LedData), .clk(CLK), .clr(RST));
  Register #(.width(32), .trigger("rising"), .Select("low")) u_EPC (
    .D(PCNorm), .en(Intr), .Q(EPC), .clk(CLK), .clr(RST));
  Comparator #(.width(16), .mode("twosComplement")) comparator_6 (
    .a(\总周期数 ), .b({16{1'b0}}), .eq(comparator_6_eq));  // open: gt, lt
  Register #(.width(2), .trigger("rising"), .Select("low")) register_2 (
    .D(IRIndex), .en(Intr), .Q(register_2_q), .clk(CLK), .clr(RST));
  not not_3 (not_3_out, MemWrite);
  Register #(.width(1), .trigger("rising"), .Select("low")) u_IE (
    .D(not_4_out), .en(or_12_out), .Q(IE), .clk(CLK), .clr(RST));
  not not_4 (not_4_out, Intr);
  or or_12 (or_12_out, Intr, URET, comparator_6_eq);
  Demultiplexer #(.select(2), .width(1), .tristate("false"), .disabled("Z"), .enable("false")) demultiplexer_1 (
    .out1(IR1Reset), .out2(IR2Reset), .out3(IR3Reset), .in(URET), .sel(register_2_q));  // open: out0
  RAM #(.addrWidth(10), .dataWidth(32), .bus("separate"), .Select("high")) ram_1 (
    .addr(AluResult[11:2]), .din(MDin), .data(MemData), .str(MemWrite), .clk(CLK), .ld(not_3_out));  // open: sel, clr
  D_Flip_Flop #(.trigger("high"), .Pre_Clr_Positions("LEGACY"), .NegatePresetClear("false"), .enable("true"), .NewFFLayout("false")) d_ff_5 (.Q(d_ff_5_q));  // open: clk, D, Qn, preset, en, reset
  // Probe on 13'hc
  Multiplexer #(.select(1), .width(32), .disabled("Z"), .enable("false")) multiplexer_9 (
    .in0(MemData), .in1(HalfMemData), .out(multiplexer_9_out), .sel(Lh));
  Multiplexer #(.select(1), .width(16), .disabled("Z"), .enable("false")) multiplexer_10 (
    .in0(MemData[15:0]), .in1(MemData[31:16]), .out(multiplexer_10_out), .sel(AluResult[1]));
  Comparator #(.width(13), .mode("twosComplement")) comparator_7 (
    .a(CNT_num), .b(13'hc), .eq(comparator_7_eq), .lt(comparator_7_lt));  // open: gt
  Clock #(.highDuration(1), .lowDuration(1)) clock_1 (.out(clock_1_out));
  Multiplexer #(.select(1), .width(32), .disabled("Z"), .enable("false")) multiplexer_11 (
    .in0(AluResult), .in1(multiplexer_9_out), .out(multiplexer_11_out), .sel(MemToReg));
  assign HalfMemData = {{16{multiplexer_10_out[15]}}, multiplexer_10_out};  // Bit_Extender bit_extender_5
  Counter #(.width(13), .max('h1fff), .ongoal("stay"), .trigger("rising"), .behavior("old")) counter_2 (
    .count(comparator_7_lt), .Q(CNT_num), .clk(clock_1_out));  // open: load, D, carry, clr, preset
  or or_13 (or_13_out, JAL, JALR);
  nand nand_1 (nand_1_out, d_ff_5_q, comparator_7_eq);
  Multiplexer #(.select(1), .width(32), .disabled("Z"), .enable("false")) multiplexer_12 (
    .in0(multiplexer_11_out), .in1(PC_4), .out(RDin), .sel(or_13_out));
  assign CLK = nand_1_out ? clock_1_out : 1'bz;  // Controlled_Buffer controlled_buffer_1
  Pull_Resistor #(.pull(1)) pull_resistor_4 (.node(CLK));

  // Other names for the same wires on the sheet: BitSel[1:0] = AluResult[1:0]

  // Notes on the sheet:
  //   中断源
  //   中断等待指示
  //   总复位信号应将除ROM以外所有存储组件全部清零
  //   单级中断测试信号模拟器
  //   数码管输出
  //   数码管输出应该用寄存器锁存，否则显示数据只能一闪而过
  //   指令探针
  //   指令存储器
  //   contents of rom_1 (hex, n*v repeats v):
  //   7d000113 100413 1f41993 41f9d993 433 c00913 800b13 140413 f47413 800293 100313 499993 89e9b3 1300533
  //   2200893 73 406282b3 fe0294e3 140413 f00f93 1f47433 1c41413 800293 100313 49d993 89e9b3 1300533
  //   2200893 73 406282b3 fe0294e3 1c45413 406b0b33 b0463 f95ff06f 2b3 fff2c293 1029293 fff2e293 500533
  //   2200893 73 f5dff06f 1112023 410113 a12023 410113 812023 410113 1312023 410113 1412023 410113 1512023
  //   410113 1612023 410113 100b13 300a13 100a93 1600433 441413 14469b3 1300533 2200893 73 fe0416e3
  //   415a0a33 fe0a10e3 ffc10113 12b03 ffc10113 12a83 ffc10113 12a03 ffc10113 12983 ffc10113 12403
  //   ffc10113 12503 ffc10113 12883 200073 1112023 410113 a12023 410113 812023 410113 1312023 410113
  //   1412023 410113 1512023 410113 1612023 410113 200b13 300a13 100a93 1600433 441413 14469b3 1300533
  //   2200893 73 fe0416e3 415a0a33 fe0a10e3 ffc10113 12b03 ffc10113 12a83 ffc10113 12a03 ffc10113 12983
  //   ffc10113 12403 ffc10113 12503 ffc10113 12883 200073 1112023 410113 a12023 410113 812023 410113
  //   1312023 410113 1412023 410113 1512023 410113 1612023 410113 300b13 300a13 100a93 1600433 441413
  //   14469b3 1300533 2200893 73 fe0416e3 415a0a33 fe0a10e3 ffc10113 12b03 ffc10113 12a83 ffc10113 12a03
  //   ffc10113 12983 ffc10113 12403 ffc10113 12503 ffc10113 12883 200073
  //   指令字
  //   JAL
  //   JALR
  //   URET
  //   ecall
  //   I型指令立即数 
  //   S型指令立即数 
  //   B型指令立即数 
  //   J型指令立即数 
  //   Beq
  //   Bne
  //   MemToReg
  //   MemWrite
  //   AluOP
  //   AluSrcB
  //   RegWrite
  //   S_type
  //   为方便自动评测，需要输出PC，IR，寄存器堆写如数据RDin
  //   RAM写使能MemWrite、RAM写入数据MDin等信号
  //   数据存储器
  //   控制位
  //   暂停节拍，不能为0
  //   戳工具置1进入计数暂停模式，ctrl+k时钟自动运行到对应节拍暂停
  //   ctrl+k关闭时钟连续运行，将控制位置零，进入单步调试模式调试
  //   可计数暂停的时钟源
endmodule

module \单周期_多级中断  (
  input  IR1,
  input  IR2,
  input  IR3,
  output RegWrite,
  output MemWrite,
  output [31:0] PC,
  output [31:0] IR,
  output [31:0] RDin,
  output [31:0] MDin,
  output [31:0] LedData
);

  wire AluSrcB, and_1_out, and_2_out, and_3_out, and_4_out, and_5_out, and_6_out, and_8_out, and_9_out,
       and_10_out, and_13_out, and_14_out, and_15_out, and_16_out, and_17_out, Beq, Bge, Bne, Branch, CLK,
       clock_1_out, comparator_1_eq, comparator_2_eq, comparator_3_eq, comparator_4_eq, comparator_5_eq,
       comparator_6_eq, comparator_7_eq, comparator_8_eq, comparator_9_eq, comparator_10_eq,
       comparator_10_lt, CSR, CSRRCI, CSRRSI, d_ff_1_q, d_ff_2_q, d_ff_3_q, d_ff_5_q, decoder_1_out1,
       decoder_1_out2, decoder_1_out3, decoder_2_out0, decoder_2_out1, decoder_2_out2, ecall, Equal, Ge, Go,
       halt, IE, Intr, IR1_q, IR1_t, IR1Reset, IR2_q, IR2_t, IR2Reset, IR3_q, IR3_t, IR3Reset, IRA, IRB, IRC,
       JAL, JALR, Less, Lh, MemToReg, nand_1_out, not_1_out, not_2_out, not_3_out, or_5_out, or_6_out,
       or_7_out, or_8_out, or_9_out, or_13_out, or_14_out, or_15_out, or_16_out, PriorIntr,
       priority_encoder_2_gs, RST, S_type, URET, W1, W2, W3;
  wire [1:0] adder_4_out, IntrCount, IRIndex, IRIndex0_q, IRIndex1_q, IRIndex2_q, IRIndexCur,
       multiplexer_10_out, priority_encoder_1_out;
  wire [3:0] AluOP;
  wire [4:0] multiplexer_2_out, multiplexer_3_out;
  wire [12:0] CNT_num;
  wire [15:0] multiplexer_12_out, \总周期数 ;
  wire [31:0] adder_2_out, adder_3_out, AluResult, bit_extender_1_out, bit_extender_2_out,
       bit_extender_3_out, bit_extender_4_out, EPC, EPC1_q, EPC2_q, EPC3_q, HalfMemData, MemData,
       multiplexer_4_out, multiplexer_5_out, multiplexer_6_out, multiplexer_7_out, multiplexer_11_out,
       multiplexer_13_out, PC_4, PCNext, PCNorm, R1Data, shifter_1_out, shifter_2_out;

  Button \u_继续运行  (.out(Go));
  Button _1 ();  // open: out
  Button _2 ();  // open: out
  Button _3 ();  // open: out
  Button \u_总复位  (.out(RST));
  LED #(.active("true")) led_1 (.in(W1));
  LED #(.active("true")) led_2 (.in(W2));
  LED #(.active("true")) led_3 (.in(W3));
  Hex_Digit_Display hex_digit_display_1 (.value(LedData[31:28]));  // open: dp
  Hex_Digit_Display hex_digit_display_2 (.value(LedData[23:20]));  // open: dp
  Hex_Digit_Display hex_digit_display_3 (.value(LedData[27:24]));  // open: dp
  Multiplexer #(.select(2), .width(32), .disabled("Z"), .enable("false")) multiplexer_1 (
    .in0(PC_4), .in1(AluResult), .in2(adder_3_out), .in3(adder_2_out), .out(PCNorm),
    .sel(priority_encoder_1_out));
  Hex_Digit_Display hex_digit_display_4 (.value(LedData[19:16]));  // open: dp
  Hex_Digit_Display hex_digit_display_5 (.value(LedData[15:12]));  // open: dp
  and and_1 (and_1_out, Beq, Equal);
  and and_2 (and_2_out, ~Equal, Bne);  // AND_Gate
  and and_3 (and_3_out, Bge, Ge);
  Priority_Encoder #(.select(2), .disabled("Z")) priority_encoder_1 (
    .in0(1'b1), .in1(JALR), .in2(JAL), .in3(Branch), .out(priority_encoder_1_out));  // open: gs, en_out, en_in
  not not_1 (not_1_out, halt);
  or or_1 (W1, IR1_q, d_ff_1_q);
  LED #(.active("true")) \_1号中断等待指示灯  (.in(W1));
  LED #(.active("true")) \_2号中断等待指示灯  (.in(W2));
  or or_2 (W2, IR2_q, d_ff_2_q);
  or or_3 (W3, IR3_q, d_ff_3_q);
  LED #(.active("true")) \_3号中断等待指示灯  (.in(W3));
  Hex_Digit_Display hex_digit_display_6 (.value(LedData[7:4]));  // open: dp
  Hex_Digit_Display hex_digit_display_7 (.value(LedData[11:8]));  // open: dp
  // Probe on \总周期数 
  or or_4 (Branch, and_1_out, and_2_out, and_3_out);
  Register #(.width(32), .trigger("rising"), .Select("low")) u_PC (
    .D(PCNext), .en(not_1_out), .Q(PC), .clk(CLK), .clr(RST));
  D_Flip_Flop #(.trigger("rising"), .Pre_Clr_Positions("LEGACY"), .NegatePresetClear("false"), .enable("true"), .NewFFLayout("false")) d_ff_1 (
    .clk(IR1_t), .D(1'b1), .Q(d_ff_1_q), .reset(IR1_q));  // open: Qn, preset, en
  D_Flip_Flop #(.trigger("rising"), .Pre_Clr_Positions("LEGACY"), .NegatePresetClear("false"), .enable("true"), .NewFFLayout("false")) d_ff_2 (
    .clk(IR2_t), .D(1'b1), .Q(d_ff_2_q), .reset(IR2_q));  // open: Qn, preset, en
  D_Flip_Flop #(.trigger("rising"), .Pre_Clr_Positions("LEGACY"), .NegatePresetClear("false"), .enable("true"), .NewFFLayout("false")) d_ff_3 (
    .clk(IR3_t), .D(1'b1), .Q(d_ff_3_q), .reset(IR3_q));  // open: Qn, preset, en
  Hex_Digit_Display hex_digit_display_8 (.value(LedData[3:0]));  // open: dp
  or or_5 (or_5_out, d_ff_1_q, IR1_q);
  or or_6 (or_6_out, d_ff_2_q, IR2_q);
  or or_7 (or_7_out, d_ff_3_q, IR3_q);
  Comparator #(.width(16), .mode("twosComplement")) comparator_1 (
    .a(16'h258), .b(\总周期数 ), .eq(comparator_1_eq));  // open: gt, lt
  Comparator #(.width(16), .mode("twosComplement")) comparator_2 (
    .a(\总周期数 ), .b(16'h1), .eq(comparator_2_eq));  // open: gt, lt
  Comparator #(.width(16), .mode("twosComplement")) comparator_3 (
    .a(\总周期数 ), .b(16'h4), .eq(comparator_3_eq));  // open: gt, lt
  Comparator #(.width(16), .mode("twosComplement")) comparator_4 (
    .a(\总周期数 ), .b(16'h7), .eq(comparator_4_eq));  // open: gt, lt
  or or_8 (or_8_out, comparator_4_eq, comparator_5_eq);
  Comparator #(.width(16), .mode("twosComplement")) comparator_5 (
    .a(\总周期数 ), .b(16'h241), .eq(comparator_5_eq));  // open: gt, lt
  // RiscV_Probe riscv_probe_1: pin names not known; wires that end beside it: IR
  ROM #(.addrWidth(10), .dataWidth(32), .Select("high")) rom_1 (.addr(PC[11:2]), .data(IR));
  Adder #(.width(32)) adder_1 (.a(PC), .b(32'h4), .out(PC_4));  // open: cin, cout
  and and_4 (and_4_out, or_5_out, ~IR1Reset);  // AND_Gate
  and and_5 (and_5_out, or_6_out, ~IR2Reset);  // AND_Gate
  and and_6 (and_6_out, or_7_out, ~IR3Reset);  // AND_Gate
  or or_9 (or_9_out, comparator_1_eq, comparator_2_eq);
  Pull_Resistor #(.pull(0)) pull_resistor_1 (.node(IRA));
  assign IRA = or_9_out ? ~CLK : 1'bz;  // Controlled_Inverter controlled_inverter_1
  Pull_Resistor #(.pull(0)) pull_resistor_2 (.node(IRB));
  assign IRB = comparator_3_eq ? ~CLK : 1'bz;  // Controlled_Inverter controlled_inverter_2
  Pull_Resistor #(.pull(0)) pull_resistor_3 (.node(IRC));
  assign IRC = or_8_out ? ~CLK : 1'bz;  // Controlled_Inverter controlled_inverter_3
  or or_10 (IR1_t, IR1, IRA);
  D_Flip_Flop #(.trigger("rising"), .Pre_Clr_Positions("LEGACY"), .NegatePresetClear("false"), .enable("true"), .NewFFLayout("false")) u_IR1 (
    .clk(CLK), .D(and_4_out), .Q(IR1_q), .reset(RST));  // open: Qn, preset, en
  D_Flip_Flop #(.trigger("rising"), .Pre_Clr_Positions("LEGACY"), .NegatePresetClear("false"), .enable("true"), .NewFFLayout("false")) u_IR2 (
    .clk(CLK), .D(and_5_out), .Q(IR2_q), .reset(RST));  // open: Qn, preset, en
  D_Flip_Flop #(.trigger("rising"), .Pre_Clr_Positions("LEGACY"), .NegatePresetClear("false"), .enable("true"), .NewFFLayout("false")) u_IR3 (
    .clk(CLK), .D(and_6_out), .Q(IR3_q), .reset(RST));  // open: Qn, preset, en
  or or_11 (IR2_t, IR2, IRB);
  \单周期硬布线控制器  \u_单周期硬布线控制器_1  (
    .Funct({IR[30], IR[25], IR[14:12]}), .OP(IR[6:2]), .ALU_OP(AluOP), .MemToReg(MemToReg),
    .MemWrite(MemWrite), .ALU_SRC(AluSrcB), .RegWrite(RegWrite), .ecall(ecall), .S_type(S_type), .Jalr(JALR),
    .Beq(Beq), .JAL(JAL), .Bne(Bne), .in_3(IR[21]), .uret(URET), .Lh(Lh), .Bge(Bge), .CSR(CSR));  // open: RS1Used, RS2Used
  Multiplexer #(.select(1), .width(5), .disabled("Z"), .enable("false")) multiplexer_2 (
    .in0(IR[19:15]), .in1(5'b10001), .out(multiplexer_2_out), .sel(ecall));
  Multiplexer #(.select(1), .width(5), .disabled("Z"), .enable("false")) multiplexer_3 (
    .in0(IR[24:20]), .in1(5'b01010), .out(multiplexer_3_out), .sel(ecall));
  Priority_Encoder #(.select(2), .disabled("Z")) priority_encoder_2 (
    .in1(IR1_q), .in2(IR2_q), .in3(IR3_q), .out(IRIndex), .gs(priority_encoder_2_gs));  // open: in0, en_out, en_in
  assign bit_extender_1_out = {{20{IR[31]}}, IR[31:20]};  // Bit_Extender bit_extender_1
  assign bit_extender_2_out = {{20{IR[31]}}, {IR[31:25], IR[11:7]}};  // Bit_Extender bit_extender_2
  assign bit_extender_3_out = {{20{IR[31]}}, {IR[31], IR[7], IR[30:25], IR[11:8]}};  // Bit_Extender bit_extender_3
  assign bit_extender_4_out = {{12{IR[31]}}, {IR[31], IR[19:12], IR[20], IR[30:21]}};  // Bit_Extender bit_extender_4
  Decoder #(.select(2), .tristate("false"), .disabled("Z"), .enable("false")) decoder_1 (
    .out1(decoder_1_out1), .out2(decoder_1_out2), .out3(decoder_1_out3), .sel(IRIndex));  // open: out0
  or or_12 (IR3_t, IR3, IRC);
  Multiplexer #(.select(1), .width(32), .disabled("Z"), .enable("false")) multiplexer_4 (
    .in0(bit_extender_1_out), .in1(bit_extender_2_out), .out(multiplexer_4_out), .sel(S_type));
  Shifter #(.width(32), .shift("ll")) shifter_1 (.in(bit_extender_3_out), .\dist (5'b00001), .out(shifter_1_out));
  Shifter #(.width(32), .shift("ll")) shifter_2 (.in(bit_extender_4_out), .\dist (5'b00001), .out(shifter_2_out));
  Multiplexer #(.select(2), .width(32), .disabled("Z"), .enable("false")) multiplexer_5 (
    .in1(32'h30ac), .in2(32'h3158), .in3(32'h3204), .out(multiplexer_5_out), .sel(IRIndex));  // open: in0
  and and_7 (Intr, priority_encoder_2_gs, IE, PriorIntr);
  Comparator #(.width(3), .mode("twosComplement")) comparator_6 (
    .a(3'b110), .b(IR[14:12]), .eq(comparator_6_eq));  // open: gt, lt
  Comparator #(.width(3), .mode("twosComplement")) comparator_7 (
    .a(IR[14:12]), .b(3'b111), .eq(comparator_7_eq));  // open: gt, lt
  and and_8 (and_8_out, Intr, decoder_1_out1);
  Pull_Resistor #(.pull(0)) pull_resistor_4 (.node(decoder_1_out1));
  and and_9 (and_9_out, Intr, decoder_1_out2);
  Pull_Resistor #(.pull(0)) pull_resistor_5 (.node(decoder_1_out2));
  and and_10 (and_10_out, Intr, decoder_1_out3);
  Pull_Resistor #(.pull(0)) pull_resistor_6 (.node(decoder_1_out3));
  Regifile regifile_1 (
    .Din(RDin), .Clk(CLK), .R1(R1Data), .R2(MDin), .WE(RegWrite), .W_num(IR[11:7]),
    .R1_num(multiplexer_2_out), .R2_num(multiplexer_3_out));
  Multiplexer #(.select(1), .width(32), .disabled("Z"), .enable("false")) multiplexer_6 (
    .in0(PCNorm), .in1(multiplexer_5_out), .out(multiplexer_6_out), .sel(Intr));
  and and_11 (CSRRSI, comparator_6_eq, CSR);
  and and_12 (CSRRCI, CSR, comparator_7_eq);
  Register #(.width(32), .trigger("rising"), .Select("low")) EPC1 (
    .D(PCNorm), .en(and_8_out), .Q(EPC1_q), .clk(CLK), .clr(RST));
  Register #(.width(32), .trigger("rising"), .Select("low")) EPC2 (
    .D(PCNorm), .en(and_9_out), .Q(EPC2_q), .clk(CLK), .clr(RST));
  Register #(.width(32), .trigger("rising"), .Select("low")) EPC3 (
    .D(PCNorm), .en(and_10_out), .Q(EPC3_q), .clk(CLK), .clr(RST));
  Multiplexer #(.select(1), .width(32), .disabled("Z"), .enable("false")) multiplexer_7 (
    .in0(MDin), .in1(multiplexer_4_out), .out(multiplexer_7_out), .sel(AluSrcB));
  Adder #(.width(32)) adder_2 (.a(shifter_1_out), .b(PC), .out(adder_2_out));  // open: cin, cout
  Adder #(.width(32)) adder_3 (.a(shifter_2_out), .b(PC), .out(adder_3_out));  // open: cin, cout
  Multiplexer #(.select(1), .width(32), .disabled("Z"), .enable("false")) multiplexer_8 (
    .in0(multiplexer_6_out), .in1(EPC), .out(PCNext), .sel(URET));
  not not_2 (not_2_out, halt);
  Counter #(.width(16), .max('hffff), .ongoal("wrap"), .trigger("rising"), .behavior("new")) counter_1 (
    .count(not_2_out), .Q(\总周期数 ), .clk(CLK));  // open: load, D, carry, clr, preset, down
  ALU alu_1 (
    .X(R1Data), .Y(multiplexer_7_out), .AluOP(AluOP), .Equal(Equal), .Result(AluResult), .out_4(Ge),
    .out_6(Less));  // open: Result_2
  Comparator #(.width(32), .mode("twosComplement")) comparator_8 (
    .a(R1Data), .b(32'h22), .eq(comparator_8_eq));  // open: gt, lt
  Multiplexer #(.select(2), .width(32), .disabled("Z"), .enable("false")) multiplexer_9 (
    .in1(EPC1_q), .in2(EPC2_q), .in3(EPC3_q), .out(EPC), .sel(IRIndexCur));  // open: in0
  and and_13 (and_13_out, ecall, ~comparator_8_eq);  // AND_Gate
  and and_14 (and_14_out, comparator_8_eq, ecall);
  D_Flip_Flop #(.trigger("falling"), .Pre_Clr_Positions("ABOVE_BELOW"), .NegatePresetClear("false"), .enable("true"), .NewFFLayout("true")) d_ff_4 (
    .clk(CLK), .D(and_13_out), .Q(halt), .en(ecall), .reset(Go));  // open: Qn, preset
  Register #(.width(32), .trigger("rising"), .Select("low")) register_1 (
    .D(MDin), .en(and_14_out), .Q(LedData), .clk(CLK), .clr(RST));
  Comparator #(.width(16), .mode("twosComplement")) comparator_9 (
    .a(\总周期数 ), .b({16{1'b0}}), .eq(comparator_9_eq));  // open: gt, lt
  Demultiplexer #(.select(2), .width(1), .tristate("false"), .disabled("Z"), .enable("false")) demultiplexer_1 (
    .out1(IR1Reset), .out2(IR2Reset), .out3(IR3Reset), .in(URET), .sel(IRIndex));  // open: out0
  Multiplexer #(.select(1), .width(2), .disabled("Z"), .enable("false")) multiplexer_10 (
    .in0(2'b11), .in1(2'b01), .out(multiplexer_10_out), .sel(Intr));
  or or_13 (or_13_out, CSRRSI, ~Intr);  // OR_Gate
  Adder #(.width(2)) adder_4 (.a(IntrCount), .b(multiplexer_10_out), .out(adder_4_out));  // open: cin, cout
  or or_14 (or_14_out, Intr, URET);
  D_Flip_Flop #(.trigger("high"), .Pre_Clr_Positions("LEGACY"), .NegatePresetClear("false"), .enable("true"), .NewFFLayout("false")) d_ff_5 (.Q(d_ff_5_q));  // open: clk, D, Qn, preset, en, reset
  // Probe on 13'hce
  RAM #(.addrWidth(10), .dataWidth(32), .bus("separate"), .Select("high")) ram_1 (
    .addr(AluResult[11:2]), .din(MDin), .data(MemData), .str(MemWrite), .clk(CLK), .ld(not_3_out));  // open: sel, clr
  not not_3 (not_3_out, MemWrite);
  or or_15 (or_15_out, Intr, URET, comparator_9_eq, CSRRCI, CSRRSI);
  Pull_Resistor #(.pull(0)) pull_resistor_7 (.node(IR1Reset));
  Decoder #(.select(2), .tristate("false"), .disabled("Z"), .enable("false")) decoder_2 (
    .out0(decoder_2_out0), .out1(decoder_2_out1), .out2(decoder_2_out2), .sel(IntrCount));  // open: out3
  Register #(.width(2), .trigger("rising"), .Select("low")) register_2 (
    .D(adder_4_out), .en(or_14_out), .Q(IntrCount), .clk(CLK), .clr(RST));
  Comparator #(.width(13), .mode("twosComplement")) comparator_10 (
    .a(CNT_num), .b(13'hce), .eq(comparator_10_eq), .lt(comparator_10_lt));  // open: gt
  Clock #(.highDuration(1), .lowDuration(1)) clock_1 (.out(clock_1_out));
  Register #(.width(1), .trigger("rising"), .Select("low")) u_IE (
    .D(or_13_out), .en(or_15_out), .Q(IE), .clk(CLK), .clr(RST));
  Pull_Resistor #(.pull(0)) pull_resistor_8 (.node(IR2Reset));
  Counter #(.width(13), .max('h1fff), .ongoal("stay"), .trigger("rising"), .behavior("old")) counter_2 (
    .count(comparator_10_lt), .Q(CNT_num), .clk(clock_1_out));  // open: load, D, carry, clr, preset
  Multiplexer #(.select(1), .width(32), .disabled("Z"), .enable("false")) multiplexer_11 (
    .in0(MemData), .in1(HalfMemData), .out(multiplexer_11_out), .sel(Lh));
  Multiplexer #(.select(1), .width(16), .disabled("Z"), .enable("false")) multiplexer_12 (
    .in0(MemData[15:0]), .in1(MemData[31:16]), .out(multiplexer_12_out), .sel(AluResult[1]));
  Pull_Resistor #(.pull(0)) pull_resistor_9 (.node(IR3Reset));
  and and_15 (and_15_out, Intr, decoder_2_out0);
  and and_16 (and_16_out, Intr, decoder_2_out1);
  and and_17 (and_17_out, Intr, decoder_2_out2);
  nand nand_1 (nand_1_out, d_ff_5_q, comparator_10_eq);
  Multiplexer #(.select(1), .width(32), .disabled("Z"), .enable("false")) multiplexer_13 (
    .in0(AluResult), .in1(multiplexer_11_out), .out(multiplexer_13_out), .sel(MemToReg));
  assign HalfMemData = {{16{multiplexer_12_out[15]}}, multiplexer_12_out};  // Bit_Extender bit_extender_5
  Register #(.width(2), .trigger("rising"), .Select("low")) IRIndex0 (
    .D(IRIndex), .en(and_15_out), .Q(IRIndex0_q), .clk(CLK), .clr(RST));
  Register #(.width(2), .trigger("rising"), .Select("low")) IRIndex1 (
    .D(IRIndex), .en(and_16_out), .Q(IRIndex1_q), .clk(CLK), .clr(RST));
  Register #(.width(2), .trigger("rising"), .Select("low")) IRIndex2 (
    .D(IRIndex), .en(and_17_out), .Q(IRIndex2_q), .clk(CLK), .clr(RST));
  assign CLK = nand_1_out ? clock_1_out : 1'bz;  // Controlled_Buffer controlled_buffer_1
  Pull_Resistor #(.pull(1)) pull_resistor_10 (.node(CLK));
  or or_16 (or_16_out, JAL, JALR);
  Multiplexer #(.select(1), .width(32), .disabled("Z"), .enable("false")) multiplexer_14 (
    .in0(multiplexer_13_out), .in1(PC_4), .out(RDin), .sel(or_16_out));
  Multiplexer #(.select(2), .width(2), .disabled("Z"), .enable("false")) multiplexer_15 (
    .in1(IRIndex0_q), .in2(IRIndex1_q), .in3(IRIndex2_q), .out(IRIndexCur), .sel(IntrCount));  // open: in0
  Comparator #(.width(2), .mode("unsigned")) comparator_11 (
    .a(IRIndexCur), .b(IRIndex), .lt(PriorIntr));  // open: gt, eq
  Pull_Resistor #(.pull(1)) pull_resistor_11 (.node(PriorIntr));

  // Other names for the same wires on the sheet: funct3[2:0] = IR[14:12]; BitSel[1:0] = AluResult[1:0]

  // Notes on the sheet:
  //   中断源
  //   中断等待指示
  //   总复位信号应将除ROM以外所有存储组件全部清零
  //   数码管输出
  //   数码管输出应该用寄存器锁存，否则显示数据只能一闪而过
  //   多级中断测试信号模拟器
  //   指令存储器
  //   指令探针
  //   contents of rom_1 (hex, n*v repeats v):
  //   7d000113 100413 1f41993 41f9d993 433 c00913 800b13 140413 f47413 800293 100313 499993 89e9b3 1300533
  //   2200893 73 406282b3 fe0294e3 140413 f00f93 1f47433 1c41413 800293 100313 49d993 89e9b3 1300533
  //   2200893 73 406282b3 fe0294e3 1c45413 406b0b33 b0463 f95ff06f 2b3 fff2c293 1029293 fff2e293 500533
  //   2200893 73 f5dff06f 1112023 410113 a12023 410113 812023 410113 1312023 410113 1412023 410113 1512023
  //   410113 1612023 410113 40e073 100b13 300a13 100a93 1600433 441413 14469b3 1300533 2200893 73 fe0416e3
  //   415a0a33 fe0a10e3 40f073 ffc10113 12b03 ffc10113 12a83 ffc10113 12a03 ffc10113 12983 ffc10113 12403
  //   ffc10113 12503 ffc10113 12883 200073 1112023 410113 a12023 410113 812023 410113 1312023 410113
  //   1412023 410113 1512023 410113 1612023 410113 40e073 200b13 300a13 100a93 1600433 441413 14469b3
  //   1300533 2200893 73 fe0416e3 415a0a33 fe0a10e3 40f073 ffc10113 12b03 ffc10113 12a83 ffc10113 12a03
  //   ffc10113 12983 ffc10113 12403 ffc10113 12503 ffc10113 12883 200073 1112023 410113 a12023 410113
  //   812023 410113 1312023 410113 1412023 410113 1512023 410113 1612023 410113 40e073 300b13 300a13
  //   100a93 1600433 441413 14469b3 1300533 2200893 73 fe0416e3 415a0a33 fe0a10e3 40f073 ffc10113 12b03
  //   ffc10113 12a83 ffc10113 12a03 ffc10113 12983 ffc10113 12403 ffc10113 12503 ffc10113 12883 200073
  //   JAL
  //   JALR
  //   指令字
  //   I型指令立即数 
  //   S型指令立即数 
  //   B型指令立即数 
  //   Beq
  //   Bne
  //   URET
  //   ecall
  //   J型指令立即数 
  //   MemToReg
  //   MemWrite
  //   AluOP
  //   AluSrcB
  //   RegWrite
  //   CSR
  //   S_type
  //   为方便自动评测，需要输出PC，IR，寄存器堆写如数据RDin
  //   RAM写使能MemWrite、RAM写入数据MDin等信号
  //   控制位
  //   暂停节拍，不能为0
  //   数据存储器
  //   戳工具置1进入计数暂停模式，ctrl+k时钟自动运行到对应节拍暂停
  //   ctrl+k关闭时钟连续运行，将控制位置零，进入单步调试模式调试
  //   可计数暂停的时钟源
endmodule

module \动态分支预测  (
  output RegWrite,
  output MemWrite,
  output [31:0] IF_PC,
  output [31:0] ID_PC,
  output [31:0] EX_PC,
  output [31:0] M_PC,
  output [31:0] WB_PC,
  output [31:0] RDin,
  output [31:0] MDin,
  output [31:0] LedData
);

  wire and_1_out, and_2_out, and_3_out, and_4_out, and_5_out, and_6_out, and_7_out, and_8_out, and_9_out,
       and_10_out, Branch, BranchCount, BranchTaken, CLK, clock_1_out, comparator_1_eq, comparator_1_lt,
       comparator_2_eq, d_ff_1_q, Equal, EX_Branch, EX_JAL, EX_JALR, ex_mem_1_halt_2, ex_mem_1_jal_2,
       ex_mem_1_jalr_2, ex_mem_1_lh_2, ex_mem_1_memtoreg_2, ex_mem_1_regwrite_2, EX_PredictJump, flush, Ge,
       Go, halt, id_ex_1_alusrcb_2, id_ex_1_beq_2, id_ex_1_bge_2, id_ex_1_bne_2, id_ex_1_ecall_2,
       id_ex_1_lh_2, id_ex_1_memtoreg_2, id_ex_1_memwrite_2, id_ex_1_regwrite_2, ID_JAL,
       if_id_1_predictjump_2, IF_PredictJump, IR1, IR2, IR3, JumpCount, Less, mem_wb_1_halt_2,
       mem_wb_1_jal_2, mem_wb_1_jalr_2, mem_wb_1_memtoreg_2, nand_1_out, not_1_out, not_2_out, not_3_out,
       not_4_out, not_5_out, not_6_out, or_8_out, PredictError, RST, S_type, stall, W1, W2, W3,
       \单周期硬布线控制器_1_alu_src , \单周期硬布线控制器_1_beq , \单周期硬布线控制器_1_bge , \单周期硬布线控制器_1_bne , \单周期硬布线控制器_1_ecall ,
       \单周期硬布线控制器_1_jalr , \单周期硬布线控制器_1_lh , \单周期硬布线控制器_1_memtoreg , \单周期硬布线控制器_1_memwrite ,
       \单周期硬布线控制器_1_regwrite , \单周期硬布线控制器_1_rs1used , \单周期硬布线控制器_1_rs2used , \单周期硬布线控制器_1_uret ;
  wire [1:0] BitSel, RS1Forward, RS2Forward, \重定向处理逻辑_1_rs1forward , \重定向处理逻辑_1_rs2forward ;
  wire [1:1] or_3_out;
  wire [3:0] id_ex_1_aluop_2, \单周期硬布线控制器_1_alu_op ;
  wire [4:0] ex_mem_1_rd_2, id_ex_1_rd_2, multiplexer_6_out, multiplexer_7_out, WB_Rd;
  wire [12:0] CNT_num;
  wire [15:0] \LoadUse次数 , multiplexer_13_out, \总周期数 , \插入气泡数 , \无条件分支数 , \条件分支成功数 ;
  wire [31:0] adder_1_out, bhb_1_jumpaddr, bit_extender_1_out, bit_extender_2_out, bit_extender_3_out,
       bit_extender_4_out, EX_AluResult, EX_IR, ex_mem_1_pc_4_2, HalfMemData, id_ex_1_imm1_2, id_ex_1_imm2_2,
       id_ex_1_pc_4_2, id_ex_1_r1_2, id_ex_1_r2_2, ID_IR, if_id_1_pc_4_2, IF_IR, IF_PC_4, JumpAddr, MEM_IR,
       mem_wb_1_aluresult_2, mem_wb_1_pc_4_2, mem_wb_1_readdata_2, MemData, multiplexer_1_out,
       multiplexer_2_out, multiplexer_3_out, multiplexer_4_out, multiplexer_8_out, multiplexer_9_out,
       multiplexer_10_out, multiplexer_11_out, multiplexer_12_out, multiplexer_14_out, multiplexer_15_out,
       PredictAddr, regifile_1_r1, regifile_1_r2, shifter_1_out, WB_IR;
  wire [31:2] MEM_AluResult;

  Button \u_总复位  (.out(RST));
  Button _1 (.out(IR1));
  Button _2 (.out(IR2));
  Button _3 (.out(IR3));
  // Probe on \总周期数 
  // Probe on \总周期数 
  Button \u_继续运行  (.out(Go));
  LED #(.active("true")) led_1 (.in(W1));
  LED #(.active("true")) led_2 (.in(W2));
  LED #(.active("true")) led_3 (.in(W3));
  \重定向处理逻辑  \u_重定向处理逻辑_1  (
    .IR(ID_IR), .RS1Used(\单周期硬布线控制器_1_rs1used ), .EX_RegWrite(id_ex_1_regwrite_2), .EX_rd(id_ex_1_rd_2),
    .RS2Used(\单周期硬布线控制器_1_rs2used ), .MEM_RegWrite(ex_mem_1_regwrite_2), .MEM_rd(ex_mem_1_rd_2),
    .BranchTaken(BranchTaken), .ecall(\单周期硬布线控制器_1_ecall ), .EX_MemToReg(id_ex_1_memtoreg_2), .stall(stall),
    .RS1Forward(\重定向处理逻辑_1_rs1forward ), .RS2Forward(\重定向处理逻辑_1_rs2forward ));  // open: flush
  Adder #(.width(32)) adder_1 (.a(EX_PC), .b(32'h4), .out(adder_1_out));  // open: cin, cout
  Hex_Digit_Display hex_digit_display_1 (.value(LedData[31:28]));  // open: dp
  // Probe on IF_PC[19:0]
  // RiscV_Probe riscv_probe_1: pin names not known; wires that end beside it: IF_IR
  Multiplexer #(.select(2), .width(32), .disabled("Z"), .enable("false")) multiplexer_1 (
    .in0(adder_1_out), .in1(EX_AluResult), .in2(JumpAddr), .out(multiplexer_1_out),
    .sel({or_3_out[1], EX_JALR}));  // open: in3
  Hex_Digit_Display hex_digit_display_2 (.value(LedData[23:20]));  // open: dp
  Hex_Digit_Display hex_digit_display_3 (.value(LedData[27:24]));  // open: dp
  // Probe on ID_PC[19:0]
  // RiscV_Probe riscv_probe_2: pin names not known; wires that end beside it: ID_IR
  Multiplexer #(.select(2), .width(32), .disabled("Z"), .enable("false")) multiplexer_2 (
    .in0(IF_PC), .in1(EX_AluResult), .in2(JumpAddr), .out(multiplexer_2_out), .sel({EX_JAL, EX_JALR}));  // open: in3
  Hex_Digit_Display hex_digit_display_4 (.value(LedData[15:12]));  // open: dp
  Hex_Digit_Display hex_digit_display_5 (.value(LedData[19:16]));  // open: dp
  and and_1 (and_1_out, ~stall, ~halt);  // AND_Gate
  Multiplexer #(.select(1), .width(32), .disabled("Z"), .enable("false")) multiplexer_3 (
    .in0(PredictAddr), .in1(multiplexer_1_out), .out(multiplexer_3_out), .sel(PredictError));
  Multiplexer #(.select(1), .width(32), .disabled("Z"), .enable("false")) multiplexer_4 (
    .in0(multiplexer_2_out), .in1(JumpAddr), .out(multiplexer_4_out), .sel(Branch));
  Hex_Digit_Display hex_digit_display_6 (.value(LedData[7:4]));  // open: dp
  Hex_Digit_Display hex_digit_display_7 (.value(LedData[11:8]));  // open: dp
  // Probe on EX_PC[19:0]
  // RiscV_Probe riscv_probe_3: pin names not known; wires that end beside it: EX_IR
  Register #(.width(32), .trigger("rising"), .Select("low")) PC (
    .D(multiplexer_3_out), .en(and_1_out), .Q(IF_PC), .clk(CLK), .clr(RST));
  Hex_Digit_Display hex_digit_display_8 (.value(LedData[3:0]));  // open: dp
  BHB bhb_1 (
    .PC(IF_PC), .EX_PC(EX_PC), .EX_BranchAddr(multiplexer_4_out), .JumpAddr(bhb_1_jumpaddr), .CLK(CLK),
    .EX_Branch(EX_Branch), .EX_BranchTaken(BranchTaken), .PredictJump(IF_PredictJump));
  Multiplexer #(.select(1), .width(32), .disabled("Z"), .enable("false")) multiplexer_5 (
    .in0(IF_PC_4), .in1(bhb_1_jumpaddr), .out(PredictAddr), .sel(IF_PredictJump));
  // Probe on \总周期数 
  // Probe on M_PC[19:0]
  // RiscV_Probe riscv_probe_4: pin names not known; wires that end beside it: MEM_IR
  Adder #(.width(32)) adder_2 (.a(IF_PC), .b(32'h4), .out(IF_PC_4));  // open: cin, cout
  // Probe on \总周期数 
  // Probe on \无条件分支数 
  // Probe on \条件分支成功数 
  // Probe on \插入气泡数 
  // Probe on \LoadUse次数 
  // RiscV_Probe riscv_probe_5: pin names not known; wires that end beside it: IF_IR
  ROM #(.addrWidth(10), .dataWidth(32), .Select("high")) rom_1 (.addr(IF_PC[11:2]), .data(IF_IR));
  // Probe on IF_PC[11:0]
  // Probe on WB_PC[19:0]
  // RiscV_Probe riscv_probe_6: pin names not known; wires that end beside it: WB_IR
  // Probe on ID_PC[11:0]
  // Probe on EX_PC[11:0]
  IF_ID if_id_1 (
    .IR(IF_IR), .IR_2(ID_IR), .PC_2(ID_PC), .reset(RST), .en(and_1_out), .CLK(CLK), .PC_4(IF_PC_4),
    .PC_4_2(if_id_1_pc_4_2), .PC(IF_PC), .flush(PredictError), .PredictJump(IF_PredictJump),
    .PredictJump_2(if_id_1_predictjump_2));
  // Probe on M_PC[11:0]
  D_Flip_Flop #(.trigger("high"), .Pre_Clr_Positions("LEGACY"), .NegatePresetClear("false"), .enable("true"), .NewFFLayout("false")) d_ff_1 (.Q(d_ff_1_q));  // open: clk, D, Qn, preset, en, reset
  // Probe on 13'h600
  Multiplexer #(.select(1), .width(5), .disabled("Z"), .enable("false")) multiplexer_6 (
    .in0(ID_IR[19:15]), .in1(5'b10001), .out(multiplexer_6_out), .sel(\单周期硬布线控制器_1_ecall ));
  Multiplexer #(.select(1), .width(5), .disabled("Z"), .enable("false")) multiplexer_7 (
    .in0(ID_IR[24:20]), .in1(5'b01010), .out(multiplexer_7_out), .sel(\单周期硬布线控制器_1_ecall ));
  // Probe on WB_PC[11:0]
  Comparator #(.width(13), .mode("twosComplement")) comparator_1 (
    .a(CNT_num), .b(13'h600), .eq(comparator_1_eq), .lt(comparator_1_lt));  // open: gt
  Clock #(.highDuration(1), .lowDuration(1)) clock_1 (.out(clock_1_out));
  \单周期硬布线控制器  \u_单周期硬布线控制器_1  (
    .Funct({ID_IR[30], ID_IR[25], ID_IR[14:12]}), .OP(ID_IR[6:2]), .ALU_OP(\单周期硬布线控制器_1_alu_op ),
    .MemToReg(\单周期硬布线控制器_1_memtoreg ), .MemWrite(\单周期硬布线控制器_1_memwrite ), .ALU_SRC(\单周期硬布线控制器_1_alu_src ),
    .RegWrite(\单周期硬布线控制器_1_regwrite ), .ecall(\单周期硬布线控制器_1_ecall ), .S_type(S_type),
    .Jalr(\单周期硬布线控制器_1_jalr ), .Beq(\单周期硬布线控制器_1_beq ), .JAL(ID_JAL), .Bne(\单周期硬布线控制器_1_bne ),
    .in_3(ID_IR[21]), .uret(\单周期硬布线控制器_1_uret ), .Lh(\单周期硬布线控制器_1_lh ), .Bge(\单周期硬布线控制器_1_bge ),
    .RS1Used(\单周期硬布线控制器_1_rs1used ), .RS2Used(\单周期硬布线控制器_1_rs2used ));  // open: CSR
  nand nand_1 (nand_1_out, d_ff_1_q, comparator_1_eq);
  Counter #(.width(13), .max('h1fff), .ongoal("stay"), .trigger("rising"), .behavior("old")) counter_1 (
    .count(comparator_1_lt), .Q(CNT_num), .clk(clock_1_out));  // open: load, D, carry, clr, preset
  xor xor_1 (PredictError, BranchTaken, EX_PredictJump);
  assign bit_extender_1_out = {{20{ID_IR[31]}}, ID_IR[31:20]};  // Bit_Extender bit_extender_1
  Multiplexer #(.select(1), .width(32), .disabled("Z"), .enable("false")) multiplexer_8 (
    .in0(bit_extender_1_out), .in1(bit_extender_2_out), .out(multiplexer_8_out), .sel(S_type));
  assign bit_extender_2_out = {{20{ID_IR[31]}}, {ID_IR[31:25], ID_IR[11:7]}};  // Bit_Extender bit_extender_2
  assign bit_extender_3_out = {{20{ID_IR[31]}}, {ID_IR[31], ID_IR[7], ID_IR[30:25], ID_IR[11:8]}};  // Bit_Extender bit_extender_3
  Multiplexer #(.select(1), .width(32), .disabled("Z"), .enable("false")) multiplexer_9 (
    .in0(bit_extender_3_out), .in1(bit_extender_4_out), .out(multiplexer_9_out), .sel(ID_JAL));
  assign bit_extender_4_out = {{12{ID_IR[31]}}, {ID_IR[31], ID_IR[19:12], ID_IR[20], ID_IR[30:21]}};  // Bit_Extender bit_extender_4
  assign CLK = nand_1_out ? clock_1_out : 1'bz;  // Controlled_Buffer controlled_buffer_1
  or or_1 (flush, PredictError, stall);
  not not_1 (not_1_out, CLK);
  Regifile regifile_1 (
    .Din(RDin), .Clk(not_1_out), .R1(regifile_1_r1), .R2(regifile_1_r2), .WE(RegWrite), .W_num(WB_Rd),
    .R1_num(multiplexer_6_out), .R2_num(multiplexer_7_out));
  Pull_Resistor #(.pull(1)) pull_resistor_1 (.node(CLK));
  not not_2 (not_2_out, halt);
  ID_EX id_ex_1 (
    .Bge(\单周期硬布线控制器_1_bge ), .Lh(\单周期硬布线控制器_1_lh ), .URET(\单周期硬布线控制器_1_uret ), .JALR(\单周期硬布线控制器_1_jalr ),
    .JAL(ID_JAL), .Beq(\单周期硬布线控制器_1_beq ), .Bne(\单周期硬布线控制器_1_bne ), .MemToReg(\单周期硬布线控制器_1_memtoreg ),
    .MemWrite(\单周期硬布线控制器_1_memwrite ), .AluOP(\单周期硬布线控制器_1_alu_op ), .AluSrcB(\单周期硬布线控制器_1_alu_src ),
    .RegWrite(\单周期硬布线控制器_1_regwrite ), .Bge_2(id_ex_1_bge_2), .Lh_2(id_ex_1_lh_2), .JALR_2(EX_JALR),
    .JAL_2(EX_JAL), .Beq_2(id_ex_1_beq_2), .Bne_2(id_ex_1_bne_2), .MemToReg_2(id_ex_1_memtoreg_2),
    .MemWrite_2(id_ex_1_memwrite_2), .AluOP_2(id_ex_1_aluop_2), .AluSrcB_2(id_ex_1_alusrcb_2),
    .RegWrite_2(id_ex_1_regwrite_2), .reset(RST), .en(not_2_out), .CLK(CLK), .ecall(\单周期硬布线控制器_1_ecall ),
    .ecall_2(id_ex_1_ecall_2), .R1_2(id_ex_1_r1_2), .R2(regifile_1_r2), .R2_2(id_ex_1_r2_2),
    .imm1(multiplexer_8_out), .imm1_2(id_ex_1_imm1_2), .imm2(multiplexer_9_out), .imm2_2(id_ex_1_imm2_2),
    .IR(ID_IR), .PC(ID_PC), .PC_2(EX_PC), .PC_4(if_id_1_pc_4_2), .PC_4_2(id_ex_1_pc_4_2), .R1(regifile_1_r1),
    .IR_2(EX_IR), .rd(ID_IR[11:7]), .rd_2(id_ex_1_rd_2), .flush(flush), .RS1Forward(\重定向处理逻辑_1_rs1forward ),
    .RS1Forward_2(RS1Forward), .RS2Forward(\重定向处理逻辑_1_rs2forward ), .RS2Forward_2(RS2Forward),
    .PredictJump(if_id_1_predictjump_2), .PredictJump_2(EX_PredictJump));  // open: URET_2
  and and_2 (and_2_out, Ge, id_ex_1_bge_2);
  Shifter #(.width(32), .shift("ll")) shifter_1 (.in(id_ex_1_imm2_2), .\dist (5'b00001), .out(shifter_1_out));
  not not_3 (not_3_out, halt);
  Counter #(.width(16), .max('hffff), .ongoal("wrap"), .trigger("rising"), .behavior("new")) counter_2 (
    .count(not_3_out), .Q(\总周期数 ), .clk(CLK), .clr(RST));  // open: load, D, carry, preset, down
  or or_2 (BranchTaken, or_3_out[1], EX_JALR);
  or or_3 (or_3_out[1], EX_JAL, and_2_out, and_4_out, and_3_out);
  and and_3 (and_3_out, ~Equal, id_ex_1_bne_2);  // AND_Gate
  and and_4 (and_4_out, id_ex_1_beq_2, Equal);
  Multiplexer #(.select(2), .width(32), .disabled("Z"), .enable("false")) multiplexer_10 (
    .in0(id_ex_1_r2_2), .in1(RDin), .in2({MEM_AluResult, BitSel}), .out(multiplexer_10_out), .sel(RS2Forward));  // open: in3
  Adder #(.width(32)) adder_3 (.a(shifter_1_out), .b(EX_PC), .out(JumpAddr));  // open: cin, cout
  or or_4 (BranchCount, and_2_out, and_3_out, and_4_out);
  or or_5 (JumpCount, EX_JALR, EX_JAL);
  Multiplexer #(.select(2), .width(32), .disabled("Z"), .enable("false")) multiplexer_11 (
    .in0(id_ex_1_r1_2), .in1(RDin), .in2({MEM_AluResult, BitSel}), .out(multiplexer_11_out), .sel(RS1Forward));  // open: in3
  Multiplexer #(.select(1), .width(32), .disabled("Z"), .enable("false")) multiplexer_12 (
    .in0(multiplexer_10_out), .in1(id_ex_1_imm1_2), .out(multiplexer_12_out), .sel(id_ex_1_alusrcb_2));
  or or_6 (Branch, id_ex_1_bne_2, id_ex_1_bge_2, id_ex_1_beq_2);
  and and_5 (and_5_out, ~halt, JumpCount);  // AND_Gate
  Counter #(.width(16), .max('hffff), .ongoal("wrap"), .trigger("rising"), .behavior("new")) counter_3 (
    .count(and_5_out), .Q(\无条件分支数 ), .clk(CLK), .clr(RST));  // open: load, D, carry, preset, down
  or or_7 (EX_Branch, Branch, EX_JAL, EX_JALR);
  ALU alu_1 (
    .X(multiplexer_11_out), .Y(multiplexer_12_out), .AluOP(id_ex_1_aluop_2), .Equal(Equal),
    .Result(EX_AluResult), .out_4(Ge), .out_6(Less));  // open: Result_2
  Comparator #(.width(32), .mode("twosComplement")) comparator_2 (
    .a(multiplexer_11_out), .b(32'h22), .eq(comparator_2_eq));  // open: gt, lt
  and and_6 (and_6_out, id_ex_1_ecall_2, ~comparator_2_eq);  // AND_Gate
  and and_7 (and_7_out, comparator_2_eq, id_ex_1_ecall_2);
  Register #(.width(32), .trigger("rising"), .Select("low")) register_1 (
    .D(multiplexer_10_out), .en(and_7_out), .Q(LedData), .clk(CLK), .clr(RST));
  and and_8 (and_8_out, ~halt, BranchCount);  // AND_Gate
  not not_4 (not_4_out, halt);
  Counter #(.width(16), .max('hffff), .ongoal("wrap"), .trigger("rising"), .behavior("new")) counter_4 (
    .count(and_8_out), .Q(\条件分支成功数 ), .clk(CLK), .clr(RST));  // open: load, D, carry, preset, down
  EX_MEM ex_mem_1 (
    .Lh(id_ex_1_lh_2), .JALR(EX_JALR), .JAL(EX_JAL), .MemToReg(id_ex_1_memtoreg_2),
    .MemWrite(id_ex_1_memwrite_2), .RegWrite(id_ex_1_regwrite_2), .halt(and_6_out), .AluResult(EX_AluResult),
    .WriteData(multiplexer_10_out), .IR(EX_IR), .PC(EX_PC), .PC_4(id_ex_1_pc_4_2), .rd(id_ex_1_rd_2),
    .Lh_2(ex_mem_1_lh_2), .JALR_2(ex_mem_1_jalr_2), .JAL_2(ex_mem_1_jal_2), .MemToReg_2(ex_mem_1_memtoreg_2),
    .MemWrite_2(MemWrite), .RegWrite_2(ex_mem_1_regwrite_2), .halt_2(ex_mem_1_halt_2),
    .AluResult_2({MEM_AluResult, BitSel}), .WriteData_2(MDin), .IR_2(MEM_IR), .PC_2(M_PC),
    .PC_4_2(ex_mem_1_pc_4_2), .rd_2(ex_mem_1_rd_2), .reset(RST), .en(not_4_out), .CLK(CLK));
  and and_9 (and_9_out, ~halt, flush);  // AND_Gate
  Counter #(.width(16), .max('hffff), .ongoal("wrap"), .trigger("rising"), .behavior("new")) counter_5 (
    .count(and_9_out), .Q(\插入气泡数 ), .clk(CLK), .clr(RST));  // open: load, D, carry, preset, down
  not not_5 (not_5_out, MemWrite);
  Multiplexer #(.select(1), .width(16), .disabled("Z"), .enable("false")) multiplexer_13 (
    .in0(MemData[15:0]), .in1(MemData[31:16]), .out(multiplexer_13_out), .sel(BitSel[1]));
  RAM #(.addrWidth(10), .dataWidth(32), .bus("separate"), .Select("high")) ram_1 (
    .addr(MEM_AluResult[11:2]), .din(MDin), .data(MemData), .str(MemWrite), .clk(CLK), .ld(not_5_out),
    .clr(RST));  // open: sel
  assign HalfMemData = {{16{multiplexer_13_out[15]}}, multiplexer_13_out};  // Bit_Extender bit_extender_5
  and and_10 (and_10_out, ~halt, stall);  // AND_Gate
  Multiplexer #(.select(1), .width(32), .disabled("Z"), .enable("false")) multiplexer_14 (
    .in0(MemData), .in1(HalfMemData), .out(multiplexer_14_out), .sel(ex_mem_1_lh_2));
  Counter #(.width(16), .max('hffff), .ongoal("wrap"), .trigger("rising"), .behavior("new")) counter_6 (
    .count(and_10_out), .Q(\LoadUse次数 ), .clk(CLK), .clr(RST));  // open: load, D, carry, preset, down
  not not_6 (not_6_out, halt);
  MEM_WB mem_wb_1 (
    .JALR(ex_mem_1_jalr_2), .JAL(ex_mem_1_jal_2), .MemToReg(ex_mem_1_memtoreg_2),
    .RegWrite(ex_mem_1_regwrite_2), .halt(ex_mem_1_halt_2), .AluResult({MEM_AluResult, BitSel}),
    .ReadData(multiplexer_14_out), .IR(MEM_IR), .PC(M_PC), .PC_4(ex_mem_1_pc_4_2), .rd(ex_mem_1_rd_2),
    .JALR_2(mem_wb_1_jalr_2), .JAL_2(mem_wb_1_jal_2), .MemToReg_2(mem_wb_1_memtoreg_2),
    .RegWrite_2(RegWrite), .halt_2(mem_wb_1_halt_2), .AluResult_2(mem_wb_1_aluresult_2),
    .ReadData_2(mem_wb_1_readdata_2), .IR_2(WB_IR), .PC_2(WB_PC), .PC_4_2(mem_wb_1_pc_4_2), .rd_2(WB_Rd),
    .reset(RST), .en(not_6_out), .CLK(CLK));
  D_Flip_Flop #(.trigger("rising"), .Pre_Clr_Positions("ABOVE_BELOW"), .NegatePresetClear("false"), .enable("true"), .NewFFLayout("true")) d_ff_2 (
    .clk(mem_wb_1_halt_2), .D(1'b1), .Q(halt), .en(1'b1), .reset(Go));  // open: Qn, preset
  Multiplexer #(.select(1), .width(32), .disabled("Z"), .enable("false")) multiplexer_15 (
    .in0(mem_wb_1_aluresult_2), .in1(mem_wb_1_readdata_2), .out(multiplexer_15_out), .sel(mem_wb_1_memtoreg_2));
  or or_8 (or_8_out, mem_wb_1_jal_2, mem_wb_1_jalr_2);
  Multiplexer #(.select(1), .width(32), .disabled("Z"), .enable("false")) multiplexer_16 (
    .in0(multiplexer_15_out), .in1(mem_wb_1_pc_4_2), .out(RDin), .sel(or_8_out));

  // Other names for the same wires on the sheet: MEM_AluResult[1:0] = BitSel; MEM_PC[31:0] = M_PC

  // Notes on the sheet:
  //   中断源
  //   时空图监测，可删除
  //   中断等待指示
  //   数码管输出
  //   stall
  //   指令存储器
  //   指令探针
  //   指令字
  //   contents of rom_1 (hex, n*v repeats v):
  //   100493 100006f 100493 200913 300993 100006f 100493 200913 300993 100006f 100493 200913 300993
  //   100006f 100493 200913 300993 29c000ef 100413 100493 1f49493 900533 2200893 73 24d493 48463 fedff06f
  //   900533 2200893 73 100493 249493 900533 2200893 73 48463 fedff06f 100493 1f49493 900533 2200893 73
  //   4034d493 900533 2200893 73 4044d493 900533 2200893 73 4044d493 900533 2200893 73 4044d493 900533
  //   2200893 73 4044d493 900533 2200893 73 4044d493 900533 2200893 73 4044d493 900533 2200893 73 4044d493
  //   900533 2200893 73 100413 1f41993 41f9d993 433 c00913 300b13 140413 f47413 800293 100313 499993
  //   89e9b3 1300533 2200893 73 406282b3 fe0294e3 140413 f00f93 1f47433 1c41413 800293 100313 49d993
  //   89e9b3 1300533 2200893 73 406282b3 fe0294e3 1c45413 406b0b33 b0463 f95ff06f 2b3 fff2c293 829293
  //   ff2e293 500533 2200893 73 fff00413 493 84a023 140413 448493 84a023 140413 448493 84a023 140413
  //   448493 84a023 140413 448493 84a023 140413 448493 84a023 140413 448493 84a023 140413 448493 84a023
  //   140413 448493 84a023 140413 448493 84a023 140413 448493 84a023 140413 448493 84a023 140413 448493
  //   84a023 140413 448493 84a023 140413 448493 84a023 140413 448493 84a023 140413 448493 140413 433
  //   3c00493 42983 4aa03 149a2b3 28663 134a023 1442023 ffc48493 fe9412e3 800533 2200893 73 440413 3c00493
  //   fc9416e3 a00893 73 413 140413 800533 2200893 73 240413 800533 2200893 73 340413 800533 2200893 73
  //   440413 800533 2200893 73 540413 800533 2200893 73 640413 800533 2200893 73 740413 800533 2200893 73
  //   840413 800533 2200893 2200893 73 8067
  //   PredictJump
  //   控制位
  //   IR
  //   流水调试日志用
  //   暂停节拍，不能为0
  //   RS1Used
  //   JAL
  //   JALR
  //   URET
  //   Lh
  //   Bge
  //   ecall
  //   I型指令立即数 
  //   S型指令立即数 
  //   B型指令立即数 
  //   J型指令立即数 
  //   戳工具置1进入计数暂停模式，ctrl+k时钟自动运行到对应节拍暂停
  //   ctrl+k关闭时钟连续运行，将控制位置零，进入单步调试模式调试
  //   RS2Used
  //   Beq
  //   Bne
  //   MemToReg
  //   MemWrite
  //   AluOP
  //   AluSrcB
  //   RegWrite
  //   S_type
  //   ecall
  //   可计数暂停的时钟源
  //   RS1Forward
  //   PredictJump
  //   RS2Forward
  //   flush
  //   imm1
  //   imm2
  //   rd 
  //   IR 
  //   PC 
  //   PC+4 
  //   Bge
  //   Lh
  //   URET
  //   JALR
  //   JAL
  //   Beq
  //   Bne
  //   MemToReg
  //   MemWrite
  //   AluOP
  //   AluSrcB
  //   RegWrite
  //   ecall
  //   R1
  //   R2
  //   BranchTaken
  //   为方便自动评测，需要输出流水线各段保存的PC值，注意是PC不是PC+4，另外ID段寄存器写入信息，Mem段内存写入信息也要输出
  //   JumpAddr
  //   EX.RegWrite
  //   ecall
  //   EX.rd
  //   MemToReg
  //   AluResult
  //   WriteData
  //   rd 
  //   IR 
  //   PC 
  //   PC+4 
  //   Lh
  //   JALR
  //   JAL
  //   MemToReg
  //   MemWrite
  //   RegWrite
  //   halt
  //   MEM.RegWrite
  //   数据存储器
  //   MEM.rd
  //   MemToReg
  //   Lh
  //   ReadData
  //   JALR
  //   JAL
  //   RegWrite
  //   halt
  //   AluResult
  //   rd 
  //   IR 
  //   PC 
  //   PC+4 
  //   JAL
  //   JALR
endmodule

module \封装正确性测试  (
);

  wire IR1, IR2, IR3, MemW, RegW;
  wire [31:0] EX_PC, ID_PC, IF_PC, IR, LED, MDin, MDinr, MEM_PC, PC, RDin, RDinr, WB_PC;

  \单周期RISC_V  \u_单周期risc_v_1  (
    .IR1(IR1), .IR2(IR2), .IR3(IR3), .RegWrite(RegW), .MemWrite(MemW), .PC(PC), .IR(IR), .RDin(RDin),
    .MDin(MDin), .LedData(LED));
  \气泡流水线  \u_气泡流水线_1  (
    .RegWrite(RegW), .MemWrite(MemW), .IF_PC(IF_PC), .ID_PC(ID_PC), .EX_PC(EX_PC), .M_PC(MEM_PC),
    .WB_PC(WB_PC), .RDin(RDinr), .MDin(MDinr), .LedData(LED));
  \单周期_单级中断  \u_单周期_单级中断_1  (
    .IR1(IR1), .IR2(IR2), .IR3(IR3), .RegWrite(RegW), .MemWrite(MemW), .PC(PC), .IR(IR), .RDin(RDin),
    .MDin(MDin), .LedData(LED));
  \理想流水线  \u_理想流水线_1  (
    .RegWrite(RegW), .MemWrite(MemW), .IF_PC(IF_PC), .ID_PC(ID_PC), .EX_PC(EX_PC), .M_PC(MEM_PC),
    .WB_PC(WB_PC), .RDin(RDinr), .MDin(MDinr), .LedData(LED));
  \重定向流水线  \u_重定向流水线_1  (
    .RegWrite(RegW), .MemWrite(MemW), .IF_PC(IF_PC), .ID_PC(ID_PC), .EX_PC(EX_PC), .M_PC(MEM_PC),
    .WB_PC(WB_PC), .RDin(RDinr), .MDin(MDinr), .LedData(LED));
  \单周期_多级中断  \u_单周期_多级中断_1  (
    .IR1(IR1), .IR2(IR2), .IR3(IR3), .RegWrite(RegW), .MemWrite(MemW), .PC(PC), .IR(IR), .RDin(RDin),
    .MDin(MDin), .LedData(LED));

  // Notes on the sheet:
  //   单周期封装测试
  //   气泡流水封装测试
  //   单周期+单级中断封装测试
  //   请检查上面封装有无位宽不匹配，引脚标签是否和连接的标签相对应，否则无法在educoder平台上正确测试
  //   理想流水封装测试
  //   重定向流水封装测试
  //   单周期+多级中断封装测试
endmodule

module IF_ID (
  input  [31:0] IR,
  input  [31:0] PC,
  input  [31:0] PC_4,
  input  PredictJump,
  input  en,
  input  CLK,
  input  reset,
  input  flush,
  output [31:0] IR_2,
  output [31:0] PC_2,
  output [31:0] PC_4_2,
  output PredictJump_2
);

  wire multiplexer_4_out, or_1_out;
  wire [31:0] multiplexer_1_out, multiplexer_2_out, multiplexer_3_out;

  Multiplexer #(.select(1), .width(32), .disabled("Z"), .enable("false")) multiplexer_1 (
    .in0(IR), .in1({32{1'b0}}), .out(multiplexer_1_out), .sel(or_1_out));
  Multiplexer #(.select(1), .width(32), .disabled("Z"), .enable("false")) multiplexer_2 (
    .in0(PC), .in1({32{1'b0}}), .out(multiplexer_2_out), .sel(or_1_out));
  Multiplexer #(.select(1), .width(32), .disabled("Z"), .enable("false")) multiplexer_3 (
    .in0(PC_4), .in1({32{1'b0}}), .out(multiplexer_3_out), .sel(or_1_out));
  Multiplexer #(.select(1), .width(1), .disabled("Z"), .enable("false")) multiplexer_4 (
    .in0(PredictJump), .in1(1'b0), .out(multiplexer_4_out), .sel(or_1_out));
  or or_1 (or_1_out, reset, flush);
  Register #(.width(32), .trigger("rising"), .Select("low")) register_1 (
    .D(multiplexer_1_out), .en(en), .Q(IR_2), .clk(CLK));  // open: clr
  Register #(.width(32), .trigger("rising"), .Select("low")) register_2 (
    .D(multiplexer_2_out), .en(en), .Q(PC_2), .clk(CLK));  // open: clr
  Register #(.width(32), .trigger("rising"), .Select("low")) register_3 (
    .D(multiplexer_3_out), .en(en), .Q(PC_4_2), .clk(CLK));  // open: clr
  Register #(.width(1), .trigger("rising"), .Select("low")) register_4 (
    .D(multiplexer_4_out), .en(en), .Q(PredictJump_2), .clk(CLK));  // open: clr
endmodule

module ID_EX (
  input  [1:0] RS1Forward,
  input  [1:0] RS2Forward,
  input  PredictJump,
  input  Bge,
  input  Lh,
  input  URET,
  input  JALR,
  input  JAL,
  input  Beq,
  input  Bne,
  input  MemToReg,
  input  MemWrite,
  input  [3:0] AluOP,
  input  AluSrcB,
  input  RegWrite,
  input  ecall,
  input  [31:0] R1,
  input  [31:0] R2,
  input  [31:0] imm1,
  input  [31:0] imm2,
  input  [31:0] IR,
  input  [31:0] PC,
  input  [31:0] PC_4,
  input  [4:0] rd,
  input  en,
  input  CLK,
  input  reset,
  input  flush,
  output [1:0] RS1Forward_2,
  output [1:0] RS2Forward_2,
  output PredictJump_2,
  output Bge_2,
  output Lh_2,
  output URET_2,
  output JALR_2,
  output JAL_2,
  output Beq_2,
  output Bne_2,
  output MemToReg_2,
  output MemWrite_2,
  output [3:0] AluOP_2,
  output AluSrcB_2,
  output RegWrite_2,
  output ecall_2,
  output [31:0] R1_2,
  output [31:0] R2_2,
  output [31:0] imm1_2,
  output [31:0] imm2_2,
  output [31:0] IR_2,
  output [31:0] PC_2,
  output [31:0] PC_4_2,
  output [4:0] rd_2
);

  wire multiplexer_3_out, multiplexer_4_out, multiplexer_5_out, multiplexer_6_out, multiplexer_7_out,
       multiplexer_8_out, multiplexer_9_out, multiplexer_10_out, multiplexer_11_out, multiplexer_12_out,
       multiplexer_14_out, multiplexer_15_out, multiplexer_16_out, or_1_out;
  wire [1:0] multiplexer_1_out, multiplexer_2_out;
  wire [3:0] multiplexer_13_out;
  wire [4:0] multiplexer_24_out;
  wire [31:0] multiplexer_17_out, multiplexer_18_out, multiplexer_19_out, multiplexer_20_out,
       multiplexer_21_out, multiplexer_22_out, multiplexer_23_out;

  Multiplexer #(.select(1), .width(2), .disabled("Z"), .enable("false")) multiplexer_1 (
    .in0(RS1Forward), .in1(2'b00), .out(multiplexer_1_out), .sel(or_1_out));
  Multiplexer #(.select(1), .width(2), .disabled("Z"), .enable("false")) multiplexer_2 (
    .in0(RS2Forward), .in1(2'b00), .out(multiplexer_2_out), .sel(or_1_out));
  Multiplexer #(.select(1), .width(1), .disabled("Z"), .enable("false")) multiplexer_3 (
    .in0(PredictJump), .in1(1'b0), .out(multiplexer_3_out), .sel(or_1_out));
  Multiplexer #(.select(1), .width(1), .disabled("Z"), .enable("false")) multiplexer_4 (
    .in0(Bge), .in1(1'b0), .out(multiplexer_4_out), .sel(or_1_out));
  Multiplexer #(.select(1), .width(1), .disabled("Z"), .enable("false")) multiplexer_5 (
    .in0(Lh), .in1(1'b0), .out(multiplexer_5_out), .sel(or_1_out));
  Multiplexer #(.select(1), .width(1), .disabled("Z"), .enable("false")) multiplexer_6 (
    .in0(URET), .in1(1'b0), .out(multiplexer_6_out), .sel(or_1_out));
  Multiplexer #(.select(1), .width(1), .disabled("Z"), .enable("false")) multiplexer_7 (
    .in0(JALR), .in1(1'b0), .out(multiplexer_7_out), .sel(or_1_out));
  Multiplexer #(.select(1), .width(1), .disabled("Z"), .enable("false")) multiplexer_8 (
    .in0(JAL), .in1(1'b0), .out(multiplexer_8_out), .sel(or_1_out));
  Multiplexer #(.select(1), .width(1), .disabled("Z"), .enable("false")) multiplexer_9 (
    .in0(Beq), .in1(1'b0), .out(multiplexer_9_out), .sel(or_1_out));
  Multiplexer #(.select(1), .width(1), .disabled("Z"), .enable("false")) multiplexer_10 (
    .in0(Bne), .in1(1'b0), .out(multiplexer_10_out), .sel(or_1_out));
  Multiplexer #(.select(1), .width(1), .disabled("Z"), .enable("false")) multiplexer_11 (
    .in0(MemToReg), .in1(1'b0), .out(multiplexer_11_out), .sel(or_1_out));
  Multiplexer #(.select(1), .width(1), .disabled("Z"), .enable("false")) multiplexer_12 (
    .in0(MemWrite), .in1(1'b0), .out(multiplexer_12_out), .sel(or_1_out));
  Multiplexer #(.select(1), .width(4), .disabled("Z"), .enable("false")) multiplexer_13 (
    .in0(AluOP), .in1(4'b0000), .out(multiplexer_13_out), .sel(or_1_out));
  Multiplexer #(.select(1), .width(1), .disabled("Z"), .enable("false")) multiplexer_14 (
    .in0(AluSrcB), .in1(1'b0), .out(multiplexer_14_out), .sel(or_1_out));
  Multiplexer #(.select(1), .width(1), .disabled("Z"), .enable("false")) multiplexer_15 (
    .in0(RegWrite), .in1(1'b0), .out(multiplexer_15_out), .sel(or_1_out));
  Multiplexer #(.select(1), .width(1), .disabled("Z"), .enable("false")) multiplexer_16 (
    .in0(ecall), .in1(1'b0), .out(multiplexer_16_out), .sel(or_1_out));
  Multiplexer #(.select(1), .width(32), .disabled("Z"), .enable("false")) multiplexer_17 (
    .in0(R1), .in1({32{1'b0}}), .out(multiplexer_17_out), .sel(or_1_out));
  Multiplexer #(.select(1), .width(32), .disabled("Z"), .enable("false")) multiplexer_18 (
    .in0(R2), .in1({32{1'b0}}), .out(multiplexer_18_out), .sel(or_1_out));
  Multiplexer #(.select(1), .width(32), .disabled("Z"), .enable("false")) multiplexer_19 (
    .in0(imm1), .in1({32{1'b0}}), .out(multiplexer_19_out), .sel(or_1_out));
  Multiplexer #(.select(1), .width(32), .disabled("Z"), .enable("false")) multiplexer_20 (
    .in0(imm2), .in1({32{1'b0}}), .out(multiplexer_20_out), .sel(or_1_out));
  Multiplexer #(.select(1), .width(32), .disabled("Z"), .enable("false")) multiplexer_21 (
    .in0(IR), .in1({32{1'b0}}), .out(multiplexer_21_out), .sel(or_1_out));
  Multiplexer #(.select(1), .width(32), .disabled("Z"), .enable("false")) multiplexer_22 (
    .in0(PC), .in1({32{1'b0}}), .out(multiplexer_22_out), .sel(or_1_out));
  Multiplexer #(.select(1), .width(32), .disabled("Z"), .enable("false")) multiplexer_23 (
    .in0(PC_4), .in1({32{1'b0}}), .out(multiplexer_23_out), .sel(or_1_out));
  Multiplexer #(.select(1), .width(5), .disabled("Z"), .enable("false")) multiplexer_24 (
    .in0(rd), .in1({5{1'b0}}), .out(multiplexer_24_out), .sel(or_1_out));
  or or_1 (or_1_out, reset, flush);
  Register #(.width(2), .trigger("rising"), .Select("low")) register_1 (
    .D(multiplexer_1_out), .en(en), .Q(RS1Forward_2), .clk(CLK));  // open: clr
  Register #(.width(2), .trigger("rising"), .Select("low")) register_2 (
    .D(multiplexer_2_out), .en(en), .Q(RS2Forward_2), .clk(CLK));  // open: clr
  Register #(.width(1), .trigger("rising"), .Select("low")) register_3 (
    .D(multiplexer_3_out), .en(en), .Q(PredictJump_2), .clk(CLK));  // open: clr
  Register #(.width(1), .trigger("rising"), .Select("low")) register_4 (
    .D(multiplexer_4_out), .en(en), .Q(Bge_2), .clk(CLK));  // open: clr
  Register #(.width(1), .trigger("rising"), .Select("low")) register_5 (
    .D(multiplexer_5_out), .en(en), .Q(Lh_2), .clk(CLK));  // open: clr
  Register #(.width(1), .trigger("rising"), .Select("low")) register_6 (
    .D(multiplexer_6_out), .en(en), .Q(URET_2), .clk(CLK));  // open: clr
  Register #(.width(1), .trigger("rising"), .Select("low")) register_7 (
    .D(multiplexer_7_out), .en(en), .Q(JALR_2), .clk(CLK));  // open: clr
  Register #(.width(1), .trigger("rising"), .Select("low")) register_8 (
    .D(multiplexer_8_out), .en(en), .Q(JAL_2), .clk(CLK));  // open: clr
  Register #(.width(1), .trigger("rising"), .Select("low")) register_9 (
    .D(multiplexer_9_out), .en(en), .Q(Beq_2), .clk(CLK));  // open: clr
  Register #(.width(1), .trigger("rising"), .Select("low")) register_10 (
    .D(multiplexer_10_out), .en(en), .Q(Bne_2), .clk(CLK));  // open: clr
  Register #(.width(1), .trigger("rising"), .Select("low")) register_11 (
    .D(multiplexer_11_out), .en(en), .Q(MemToReg_2), .clk(CLK));  // open: clr
  Register #(.width(1), .trigger("rising"), .Select("low")) register_12 (
    .D(multiplexer_12_out), .en(en), .Q(MemWrite_2), .clk(CLK));  // open: clr
  Register #(.width(4), .trigger("rising"), .Select("low")) register_13 (
    .D(multiplexer_13_out), .en(en), .Q(AluOP_2), .clk(CLK));  // open: clr
  Register #(.width(1), .trigger("rising"), .Select("low")) register_14 (
    .D(multiplexer_14_out), .en(en), .Q(AluSrcB_2), .clk(CLK));  // open: clr
  Register #(.width(1), .trigger("rising"), .Select("low")) register_15 (
    .D(multiplexer_15_out), .en(en), .Q(RegWrite_2), .clk(CLK));  // open: clr
  Register #(.width(1), .trigger("rising"), .Select("low")) register_16 (
    .D(multiplexer_16_out), .en(en), .Q(ecall_2), .clk(CLK));  // open: clr
  Register #(.width(32), .trigger("rising"), .Select("low")) register_17 (
    .D(multiplexer_17_out), .en(en), .Q(R1_2), .clk(CLK));  // open: clr
  Register #(.width(32), .trigger("rising"), .Select("low")) register_18 (
    .D(multiplexer_18_out), .en(en), .Q(R2_2), .clk(CLK));  // open: clr
  Register #(.width(32), .trigger("rising"), .Select("low")) register_19 (
    .D(multiplexer_19_out), .en(en), .Q(imm1_2), .clk(CLK));  // open: clr
  Register #(.width(32), .trigger("rising"), .Select("low")) register_20 (
    .D(multiplexer_20_out), .en(en), .Q(imm2_2), .clk(CLK));  // open: clr
  Register #(.width(32), .trigger("rising"), .Select("low")) register_21 (
    .D(multiplexer_21_out), .en(en), .Q(IR_2), .clk(CLK));  // open: clr
  Register #(.width(32), .trigger("rising"), .Select("low")) register_22 (
    .D(multiplexer_22_out), .en(en), .Q(PC_2), .clk(CLK));  // open: clr
  Register #(.width(32), .trigger("rising"), .Select("low")) register_23 (
    .D(multiplexer_23_out), .en(en), .Q(PC_4_2), .clk(CLK));  // open: clr
  Register #(.width(5), .trigger("rising"), .Select("low")) register_24 (
    .D(multiplexer_24_out), .en(en), .Q(rd_2), .clk(CLK));  // open: clr
endmodule

module EX_MEM (
  input  Lh,
  input  JALR,
  input  JAL,
  input  MemToReg,
  input  MemWrite,
  input  RegWrite,
  input  halt,
  input  [31:0] AluResult,
  input  [31:0] WriteData,
  input  [31:0] IR,
  input  [31:0] PC,
  input  [31:0] PC_4,
  input  [4:0] rd,
  input  reset,
  input  en,
  input  CLK,
  output Lh_2,
  output JALR_2,
  output JAL_2,
  output MemToReg_2,
  output MemWrite_2,
  output RegWrite_2,
  output halt_2,
  output [31:0] AluResult_2,
  output [31:0] WriteData_2,
  output [31:0] IR_2,
  output [31:0] PC_2,
  output [31:0] PC_4_2,
  output [4:0] rd_2
);

  wire multiplexer_1_out, multiplexer_2_out, multiplexer_3_out, multiplexer_4_out, multiplexer_5_out,
       multiplexer_6_out, multiplexer_7_out;
  wire [4:0] multiplexer_13_out;
  wire [31:0] multiplexer_8_out, multiplexer_9_out, multiplexer_10_out, multiplexer_11_out,
       multiplexer_12_out;

  Multiplexer #(.select(1), .width(1), .disabled("Z"), .enable("false")) multiplexer_1 (
    .in0(Lh), .in1(1'b0), .out(multiplexer_1_out), .sel(reset));
  Multiplexer #(.select(1), .width(1), .disabled("Z"), .enable("false")) multiplexer_2 (
    .in0(JALR), .in1(1'b0), .out(multiplexer_2_out), .sel(reset));
  Multiplexer #(.select(1), .width(1), .disabled("Z"), .enable("false")) multiplexer_3 (
    .in0(JAL), .in1(1'b0), .out(multiplexer_3_out), .sel(reset));
  Multiplexer #(.select(1), .width(1), .disabled("Z"), .enable("false")) multiplexer_4 (
    .in0(MemToReg), .in1(1'b0), .out(multiplexer_4_out), .sel(reset));
  Multiplexer #(.select(1), .width(1), .disabled("Z"), .enable("false")) multiplexer_5 (
    .in0(MemWrite), .in1(1'b0), .out(multiplexer_5_out), .sel(reset));
  Multiplexer #(.select(1), .width(1), .disabled("Z"), .enable("false")) multiplexer_6 (
    .in0(RegWrite), .in1(1'b0), .out(multiplexer_6_out), .sel(reset));
  Multiplexer #(.select(1), .width(1), .disabled("Z"), .enable("false")) multiplexer_7 (
    .in0(halt), .in1(1'b0), .out(multiplexer_7_out), .sel(reset));
  Multiplexer #(.select(1), .width(32), .disabled("Z"), .enable("false")) multiplexer_8 (
    .in0(AluResult), .in1({32{1'b0}}), .out(multiplexer_8_out), .sel(reset));
  Multiplexer #(.select(1), .width(32), .disabled("Z"), .enable("false")) multiplexer_9 (
    .in0(WriteData), .in1({32{1'b0}}), .out(multiplexer_9_out), .sel(reset));
  Multiplexer #(.select(1), .width(32), .disabled("Z"), .enable("false")) multiplexer_10 (
    .in0(IR), .in1({32{1'b0}}), .out(multiplexer_10_out), .sel(reset));
  Multiplexer #(.select(1), .width(32), .disabled("Z"), .enable("false")) multiplexer_11 (
    .in0(PC), .in1({32{1'b0}}), .out(multiplexer_11_out), .sel(reset));
  Multiplexer #(.select(1), .width(32), .disabled("Z"), .enable("false")) multiplexer_12 (
    .in0(PC_4), .in1({32{1'b0}}), .out(multiplexer_12_out), .sel(reset));
  Multiplexer #(.select(1), .width(5), .disabled("Z"), .enable("false")) multiplexer_13 (
    .in0(rd), .in1({5{1'b0}}), .out(multiplexer_13_out), .sel(reset));
  Register #(.width(1), .trigger("rising"), .Select("low")) register_1 (
    .D(multiplexer_1_out), .en(en), .Q(Lh_2), .clk(CLK));  // open: clr
  Register #(.width(1), .trigger("rising"), .Select("low")) register_2 (
    .D(multiplexer_2_out), .en(en), .Q(JALR_2), .clk(CLK));  // open: clr
  Register #(.width(1), .trigger("rising"), .Select("low")) register_3 (
    .D(multiplexer_3_out), .en(en), .Q(JAL_2), .clk(CLK));  // open: clr
  Register #(.width(1), .trigger("rising"), .Select("low")) register_4 (
    .D(multiplexer_4_out), .en(en), .Q(MemToReg_2), .clk(CLK));  // open: clr
  Register #(.width(1), .trigger("rising"), .Select("low")) register_5 (
    .D(multiplexer_5_out), .en(en), .Q(MemWrite_2), .clk(CLK));  // open: clr
  Register #(.width(1), .trigger("rising"), .Select("low")) register_6 (
    .D(multiplexer_6_out), .en(en), .Q(RegWrite_2), .clk(CLK));  // open: clr
  Register #(.width(1), .trigger("rising"), .Select("low")) register_7 (
    .D(multiplexer_7_out), .en(en), .Q(halt_2), .clk(CLK));  // open: clr
  Register #(.width(32), .trigger("rising"), .Select("low")) register_8 (
    .D(multiplexer_8_out), .en(en), .Q(AluResult_2), .clk(CLK));  // open: clr
  Register #(.width(32), .trigger("rising"), .Select("low")) register_9 (
    .D(multiplexer_9_out), .en(en), .Q(WriteData_2), .clk(CLK));  // open: clr
  Register #(.width(32), .trigger("rising"), .Select("low")) register_10 (
    .D(multiplexer_10_out), .en(en), .Q(IR_2), .clk(CLK));  // open: clr
  Register #(.width(32), .trigger("rising"), .Select("low")) register_11 (
    .D(multiplexer_11_out), .en(en), .Q(PC_2), .clk(CLK));  // open: clr
  Register #(.width(32), .trigger("rising"), .Select("low")) register_12 (
    .D(multiplexer_12_out), .en(en), .Q(PC_4_2), .clk(CLK));  // open: clr
  Register #(.width(5), .trigger("rising"), .Select("low")) register_13 (
    .D(multiplexer_13_out), .en(en), .Q(rd_2), .clk(CLK));  // open: clr
endmodule

module MEM_WB (
  input  JALR,
  input  JAL,
  input  MemToReg,
  input  RegWrite,
  input  halt,
  input  [31:0] AluResult,
  input  [31:0] ReadData,
  input  [31:0] IR,
  input  [31:0] PC,
  input  [31:0] PC_4,
  input  [4:0] rd,
  input  reset,
  input  en,
  input  CLK,
  output JALR_2,
  output JAL_2,
  output MemToReg_2,
  output RegWrite_2,
  output halt_2,
  output [31:0] AluResult_2,
  output [31:0] ReadData_2,
  output [31:0] IR_2,
  output [31:0] PC_2,
  output [31:0] PC_4_2,
  output [4:0] rd_2
);

  wire multiplexer_1_out, multiplexer_2_out, multiplexer_3_out, multiplexer_4_out, multiplexer_5_out;
  wire [4:0] multiplexer_11_out;
  wire [31:0] multiplexer_6_out, multiplexer_7_out, multiplexer_8_out, multiplexer_9_out, multiplexer_10_out;

  Multiplexer #(.select(1), .width(1), .disabled("Z"), .enable("false")) multiplexer_1 (
    .in0(JALR), .in1(1'b0), .out(multiplexer_1_out), .sel(reset));
  Multiplexer #(.select(1), .width(1), .disabled("Z"), .enable("false")) multiplexer_2 (
    .in0(JAL), .in1(1'b0), .out(multiplexer_2_out), .sel(reset));
  Multiplexer #(.select(1), .width(1), .disabled("Z"), .enable("false")) multiplexer_3 (
    .in0(MemToReg), .in1(1'b0), .out(multiplexer_3_out), .sel(reset));
  Multiplexer #(.select(1), .width(1), .disabled("Z"), .enable("false")) multiplexer_4 (
    .in0(RegWrite), .in1(1'b0), .out(multiplexer_4_out), .sel(reset));
  Multiplexer #(.select(1), .width(1), .disabled("Z"), .enable("false")) multiplexer_5 (
    .in0(halt), .in1(1'b0), .out(multiplexer_5_out), .sel(reset));
  Multiplexer #(.select(1), .width(32), .disabled("Z"), .enable("false")) multiplexer_6 (
    .in0(AluResult), .in1({32{1'b0}}), .out(multiplexer_6_out), .sel(reset));
  Multiplexer #(.select(1), .width(32), .disabled("Z"), .enable("false")) multiplexer_7 (
    .in0(ReadData), .in1({32{1'b0}}), .out(multiplexer_7_out), .sel(reset));
  Multiplexer #(.select(1), .width(32), .disabled("Z"), .enable("false")) multiplexer_8 (
    .in0(IR), .in1({32{1'b0}}), .out(multiplexer_8_out), .sel(reset));
  Multiplexer #(.select(1), .width(32), .disabled("Z"), .enable("false")) multiplexer_9 (
    .in0(PC), .in1({32{1'b0}}), .out(multiplexer_9_out), .sel(reset));
  Multiplexer #(.select(1), .width(32), .disabled("Z"), .enable("false")) multiplexer_10 (
    .in0(PC_4), .in1({32{1'b0}}), .out(multiplexer_10_out), .sel(reset));
  Multiplexer #(.select(1), .width(5), .disabled("Z"), .enable("false")) multiplexer_11 (
    .in0(rd), .in1({5{1'b0}}), .out(multiplexer_11_out), .sel(reset));
  Register #(.width(1), .trigger("rising"), .Select("low")) register_1 (
    .D(multiplexer_1_out), .en(en), .Q(JALR_2), .clk(CLK));  // open: clr
  Register #(.width(1), .trigger("rising"), .Select("low")) register_2 (
    .D(multiplexer_2_out), .en(en), .Q(JAL_2), .clk(CLK));  // open: clr
  Register #(.width(1), .trigger("rising"), .Select("low")) register_3 (
    .D(multiplexer_3_out), .en(en), .Q(MemToReg_2), .clk(CLK));  // open: clr
  Register #(.width(1), .trigger("rising"), .Select("low")) register_4 (
    .D(multiplexer_4_out), .en(en), .Q(RegWrite_2), .clk(CLK));  // open: clr
  Register #(.width(1), .trigger("rising"), .Select("low")) register_5 (
    .D(multiplexer_5_out), .en(en), .Q(halt_2), .clk(CLK));  // open: clr
  Register #(.width(32), .trigger("rising"), .Select("low")) register_6 (
    .D(multiplexer_6_out), .en(en), .Q(AluResult_2), .clk(CLK));  // open: clr
  Register #(.width(32), .trigger("rising"), .Select("low")) register_7 (
    .D(multiplexer_7_out), .en(en), .Q(ReadData_2), .clk(CLK));  // open: clr
  Register #(.width(32), .trigger("rising"), .Select("low")) register_8 (
    .D(multiplexer_8_out), .en(en), .Q(IR_2), .clk(CLK));  // open: clr
  Register #(.width(32), .trigger("rising"), .Select("low")) register_9 (
    .D(multiplexer_9_out), .en(en), .Q(PC_2), .clk(CLK));  // open: clr
  Register #(.width(32), .trigger("rising"), .Select("low")) register_10 (
    .D(multiplexer_10_out), .en(en), .Q(PC_4_2), .clk(CLK));  // open: clr
  Register #(.width(5), .trigger("rising"), .Select("low")) register_11 (
    .D(multiplexer_11_out), .en(en), .Q(rd_2), .clk(CLK));  // open: clr
endmodule

module \气泡处理逻辑  (
  input  [31:0] IR,
  input  RS1Used,
  input  EX_RegWrite,
  input  [4:0] EX_rd,
  input  RS2Used,
  input  MEM_RegWrite,
  input  [4:0] MEM_rd,
  input  BranchTaken,
  input  ecall,
  output stall,
  output flush
);

  wire and_1_out, and_2_out, and_3_out, and_4_out, and_5_out, and_6_out, comparator_1_eq, comparator_2_eq,
       comparator_3_eq, comparator_4_eq, comparator_5_eq, comparator_6_eq, comparator_7_eq, comparator_8_eq,
       comparator_9_eq, comparator_10_eq, comparator_11_eq, comparator_12_eq, or_1_out, or_2_out;

  Comparator #(.width(5), .mode("twosComplement")) comparator_1 (
    .a(5'b10001), .b(EX_rd), .eq(comparator_1_eq));  // open: gt, lt
  Comparator #(.width(5), .mode("twosComplement")) comparator_2 (
    .a(EX_rd), .b(5'b01010), .eq(comparator_2_eq));  // open: gt, lt
  Comparator #(.width(5), .mode("twosComplement")) comparator_3 (
    .a(5'b10001), .b(MEM_rd), .eq(comparator_3_eq));  // open: gt, lt
  Comparator #(.width(5), .mode("twosComplement")) comparator_4 (
    .a(MEM_rd), .b(5'b01010), .eq(comparator_4_eq));  // open: gt, lt
  Comparator #(.width(5), .mode("twosComplement")) comparator_5 (
    .a({5{1'b0}}), .b(IR[19:15]), .eq(comparator_5_eq));  // open: gt, lt
  Comparator #(.width(5), .mode("twosComplement")) comparator_6 (
    .a(IR[19:15]), .b(EX_rd), .eq(comparator_6_eq));  // open: gt, lt
  Comparator #(.width(5), .mode("twosComplement")) comparator_7 (
    .a({5{1'b0}}), .b(IR[24:20]), .eq(comparator_7_eq));  // open: gt, lt
  Comparator #(.width(5), .mode("twosComplement")) comparator_8 (
    .a(IR[24:20]), .b(EX_rd), .eq(comparator_8_eq));  // open: gt, lt
  Comparator #(.width(5), .mode("twosComplement")) comparator_9 (
    .a({5{1'b0}}), .b(IR[19:15]), .eq(comparator_9_eq));  // open: gt, lt
  Comparator #(.width(5), .mode("twosComplement")) comparator_10 (
    .a(IR[19:15]), .b(MEM_rd), .eq(comparator_10_eq));  // open: gt, lt
  Comparator #(.width(5), .mode("twosComplement")) comparator_11 (
    .a({5{1'b0}}), .b(IR[24:20]), .eq(comparator_11_eq));  // open: gt, lt
  Comparator #(.width(5), .mode("twosComplement")) comparator_12 (
    .a(IR[24:20]), .b(MEM_rd), .eq(comparator_12_eq));  // open: gt, lt
  or or_1 (or_1_out, comparator_1_eq, comparator_2_eq);
  or or_2 (or_2_out, comparator_3_eq, comparator_4_eq);
  and and_1 (and_1_out, RS1Used, ~comparator_5_eq, comparator_6_eq, EX_RegWrite);  // AND_Gate
  and and_2 (and_2_out, RS2Used, ~comparator_7_eq, comparator_8_eq, EX_RegWrite);  // AND_Gate
  and and_3 (and_3_out, RS1Used, ~comparator_9_eq, comparator_10_eq, MEM_RegWrite);  // AND_Gate
  and and_4 (and_4_out, RS2Used, ~comparator_11_eq, comparator_12_eq, MEM_RegWrite);  // AND_Gate
  and and_5 (and_5_out, or_1_out, ecall);
  and and_6 (and_6_out, ecall, or_2_out);
  or or_3 (stall, and_1_out, and_2_out, and_3_out, and_4_out, and_5_out, and_6_out);
  or or_4 (flush, stall, BranchTaken);

  // Other names for the same wires on the sheet: DataHazzard = stall; RS1[4:0] = IR[19:15]; RS2[4:0] = IR[24:20]
endmodule
module \重定向处理逻辑  (
  input  [31:0] IR,
  input  RS1Used,
  input  EX_RegWrite,
  input  [4:0] EX_rd,
  input  RS2Used,
  input  MEM_RegWrite,
  input  [4:0] MEM_rd,
  input  BranchTaken,
  input  ecall,
  input  EX_MemToReg,
  output stall,
  output flush,
  output [1:0] RS1Forward,
  output [1:0] RS2Forward
);

  wire and_1_out, and_2_out, and_3_out, and_4_out, and_5_out, and_6_out, and_8_out, and_9_out, and_10_out,
       and_11_out, comparator_1_eq, comparator_2_eq, comparator_3_eq, comparator_4_eq, comparator_5_eq,
       comparator_6_eq, comparator_7_eq, comparator_8_eq, comparator_9_eq, comparator_10_eq,
       comparator_11_eq, comparator_12_eq, comparator_13_eq, comparator_14_eq, comparator_15_eq,
       comparator_16_eq, or_3_out, or_6_out;

  Comparator #(.width(5), .mode("twosComplement")) comparator_1 (
    .a({5{1'b0}}), .b(IR[19:15]), .eq(comparator_1_eq));  // open: gt, lt
  Comparator #(.width(5), .mode("twosComplement")) comparator_2 (
    .a(IR[19:15]), .b(EX_rd), .eq(comparator_2_eq));  // open: gt, lt
  Comparator #(.width(5), .mode("twosComplement")) comparator_3 (
    .a({5{1'b0}}), .b(IR[19:15]), .eq(comparator_3_eq));  // open: gt, lt
  Comparator #(.width(5), .mode("twosComplement")) comparator_4 (
    .a(IR[19:15]), .b(MEM_rd), .eq(comparator_4_eq));  // open: gt, lt
  Comparator #(.width(5), .mode("twosComplement")) comparator_5 (
    .a({5{1'b0}}), .b(IR[19:15]), .eq(comparator_5_eq));  // open: gt, lt
  Comparator #(.width(5), .mode("twosComplement")) comparator_6 (
    .a(IR[19:15]), .b(EX_rd), .eq(comparator_6_eq));  // open: gt, lt
  Comparator #(.width(5), .mode("twosComplement")) comparator_7 (
    .a({5{1'b0}}), .b(IR[24:20]), .eq(comparator_7_eq));  // open: gt, lt
  Comparator #(.width(5), .mode("twosComplement")) comparator_8 (
    .a(IR[24:20]), .b(EX_rd), .eq(comparator_8_eq));  // open: gt, lt
  Comparator #(.width(5), .mode("twosComplement")) comparator_9 (
    .a(5'b10001), .b(EX_rd), .eq(comparator_9_eq));  // open: gt, lt
  Comparator #(.width(5), .mode("twosComplement")) comparator_10 (
    .a(5'b10001), .b(MEM_rd), .eq(comparator_10_eq));  // open: gt, lt
  and and_1 (and_1_out, RS1Used, ~comparator_5_eq, comparator_6_eq, EX_MemToReg);  // AND_Gate
  and and_2 (and_2_out, RS2Used, ~comparator_7_eq, comparator_8_eq, EX_MemToReg);  // AND_Gate
  and and_3 (and_3_out, ecall, EX_RegWrite, comparator_9_eq);
  and and_4 (and_4_out, RS1Used, ~comparator_1_eq, comparator_2_eq, EX_RegWrite);  // AND_Gate
  and and_5 (and_5_out, RS1Used, ~comparator_3_eq, comparator_4_eq, MEM_RegWrite);  // AND_Gate
  and and_6 (and_6_out, ecall, MEM_RegWrite, comparator_10_eq);
  or or_1 (stall, and_1_out, and_2_out);
  or or_2 (RS1Forward[1], and_3_out, and_4_out);
  or or_3 (or_3_out, and_5_out, and_6_out);
  and and_7 (RS1Forward[0], ~RS1Forward[1], or_3_out);  // AND_Gate
  Comparator #(.width(5), .mode("twosComplement")) comparator_11 (
    .a({5{1'b0}}), .b(IR[24:20]), .eq(comparator_11_eq));  // open: gt, lt
  Comparator #(.width(5), .mode("twosComplement")) comparator_12 (
    .a(IR[24:20]), .b(EX_rd), .eq(comparator_12_eq));  // open: gt, lt
  Comparator #(.width(5), .mode("twosComplement")) comparator_13 (
    .a({5{1'b0}}), .b(IR[24:20]), .eq(comparator_13_eq));  // open: gt, lt
  Comparator #(.width(5), .mode("twosComplement")) comparator_14 (
    .a(IR[24:20]), .b(MEM_rd), .eq(comparator_14_eq));  // open: gt, lt
  Comparator #(.width(5), .mode("twosComplement")) comparator_15 (
    .a(5'b01010), .b(EX_rd), .eq(comparator_15_eq));  // open: gt, lt
  Comparator #(.width(5), .mode("twosComplement")) comparator_16 (
    .a(5'b01010), .b(MEM_rd), .eq(comparator_16_eq));  // open: gt, lt
  or or_4 (flush, stall, BranchTaken);
  and and_8 (and_8_out, ecall, EX_RegWrite, comparator_15_eq);
  and and_9 (and_9_out, RS2Used, ~comparator_11_eq, comparator_12_eq, EX_RegWrite);  // AND_Gate
  and and_10 (and_10_out, RS2Used, ~comparator_13_eq, comparator_14_eq, MEM_RegWrite);  // AND_Gate
  and and_11 (and_11_out, ecall, MEM_RegWrite, comparator_16_eq);
  or or_5 (RS2Forward[1], and_8_out, and_9_out);
  or or_6 (or_6_out, and_10_out, and_11_out);
  and and_12 (RS2Forward[0], ~RS2Forward[1], or_6_out);  // AND_Gate

  // Other names for the same wires on the sheet: RS1[4:0] = IR[19:15]; RS2[4:0] = IR[24:20]; LoadUse = stall
endmodule

module BHB (
  input  [31:0] PC,
  input  [31:0] EX_PC,
  input  [31:0] EX_BranchAddr,
  input  CLK,
  input  EX_Branch,
  input  EX_BranchTaken,
  output [31:0] JumpAddr,
  output PredictJump
);

  wire and_1_out, and_2_out, and_3_out, and_4_out, and_5_out, and_6_out, and_7_out, and_8_out, and_25_out,
       comparator_1_eq, comparator_2_eq, comparator_3_eq, comparator_4_eq, comparator_5_eq, comparator_6_eq,
       comparator_7_eq, comparator_8_eq, comparator_9_eq, comparator_10_eq, comparator_11_eq,
       comparator_12_eq, comparator_13_eq, comparator_14_eq, comparator_15_eq, comparator_16_eq, d_ff_1_q,
       d_ff_2_q, d_ff_3_q, d_ff_4_q, d_ff_5_q, d_ff_6_q, d_ff_7_q, d_ff_8_q, decoder_1_out0, decoder_1_out1,
       decoder_1_out2, decoder_1_out3, decoder_1_out4, decoder_1_out5, decoder_1_out6, decoder_1_out7,
       demultiplexer_1_out0, demultiplexer_1_out1, demultiplexer_1_out2, demultiplexer_1_out3,
       demultiplexer_1_out4, demultiplexer_1_out5, demultiplexer_1_out6, demultiplexer_1_out7, EX_Hit,
       EX_Miss, L0, L1, L2, L3, L4, L5, L6, L7, M0, M1, M2, M3, M4, M5, M6, M7, not_2_out, not_3_out,
       not_4_out, not_5_out, not_6_out, not_7_out, not_8_out, not_9_out, or_1_out, or_2_out, or_3_out,
       or_4_out, or_5_out, or_6_out, or_7_out, or_8_out, or_10_out, or_11_out, or_12_out, or_13_out,
       or_14_out, or_15_out, or_16_out, or_17_out, priority_encoder_1_gs, v0, v1, v2, v3, v4, v5, v6, v7,
       Write0, Write1, Write2, Write3, Write4, Write5, Write6, Write7;
  wire [0:0] controlled_buffer_9_out, controlled_buffer_10_out, controlled_buffer_11_out,
       controlled_buffer_12_out, controlled_buffer_13_out, controlled_buffer_14_out,
       controlled_buffer_15_out, controlled_buffer_16_out;
  wire [1:0] Predict0, Predict1, Predict2, Predict3, Predict4, Predict5, Predict6, Predict7,
       predictfsm_1_low_2, predictfsm_2_low_2, predictfsm_3_low_2, predictfsm_4_low_2, predictfsm_5_low_2,
       predictfsm_6_low_2, predictfsm_7_low_2, predictfsm_8_low_2;
  wire [2:0] max_1_maxid, max_2_maxid, max_3_maxid, max_4_maxid, max_5_maxid, max_6_maxid, max_7_maxid,
       priority_encoder_1_out;
  wire [31:0] C0, C1, C2, C3, C4, C5, C6, C7, max_1_max, max_2_max, max_3_max, max_4_max, max_5_max,
       max_6_max, register_17_q, register_18_q, register_19_q, register_20_q, register_21_q, register_22_q,
       register_23_q, register_24_q, Tag0, Tag1, Tag2, Tag3, Tag4, Tag5, Tag6, Tag7;

  Register #(.width(1), .trigger("rising"), .Select("low")) register_1 (
    .D(1'b1), .en(Write0), .Q(v0), .clk(CLK));  // open: clr
  Register #(.width(1), .trigger("rising"), .Select("low")) register_2 (
    .D(1'b1), .en(Write1), .Q(v1), .clk(CLK));  // open: clr
  Register #(.width(1), .trigger("rising"), .Select("low")) register_3 (
    .D(1'b1), .en(Write2), .Q(v2), .clk(CLK));  // open: clr
  Register #(.width(1), .trigger("rising"), .Select("low")) register_4 (
    .D(1'b1), .en(Write3), .Q(v3), .clk(CLK));  // open: clr
  Register #(.width(1), .trigger("rising"), .Select("low")) register_5 (
    .D(1'b1), .en(Write4), .Q(v4), .clk(CLK));  // open: clr
  Register #(.width(1), .trigger("rising"), .Select("low")) register_6 (
    .D(1'b1), .en(Write5), .Q(v5), .clk(CLK));  // open: clr
  Register #(.width(1), .trigger("rising"), .Select("low")) register_7 (
    .D(1'b1), .en(Write6), .Q(v6), .clk(CLK));  // open: clr
  Register #(.width(1), .trigger("rising"), .Select("low")) register_8 (
    .D(1'b1), .en(Write7), .Q(v7), .clk(CLK));  // open: clr
  Register #(.width(32), .trigger("rising"), .Select("low")) register_9 (
    .D(EX_PC), .en(Write0), .Q(Tag0), .clk(CLK));  // open: clr
  Register #(.width(32), .trigger("rising"), .Select("low")) register_10 (
    .D(EX_PC), .en(Write1), .Q(Tag1), .clk(CLK));  // open: clr
  Register #(.width(32), .trigger("rising"), .Select("low")) register_11 (
    .D(EX_PC), .en(Write2), .Q(Tag2), .clk(CLK));  // open: clr
  Register #(.width(32), .trigger("rising"), .Select("low")) register_12 (
    .D(EX_PC), .en(Write3), .Q(Tag3), .clk(CLK));  // open: clr
  Register #(.width(32), .trigger("rising"), .Select("low")) register_13 (
    .D(EX_PC), .en(Write4), .Q(Tag4), .clk(CLK));  // open: clr
  Register #(.width(32), .trigger("rising"), .Select("low")) register_14 (
    .D(EX_PC), .en(Write5), .Q(Tag5), .clk(CLK));  // open: clr
  Register #(.width(32), .trigger("rising"), .Select("low")) register_15 (
    .D(EX_PC), .en(Write6), .Q(Tag6), .clk(CLK));  // open: clr
  Register #(.width(32), .trigger("rising"), .Select("low")) register_16 (
    .D(EX_PC), .en(Write7), .Q(Tag7), .clk(CLK));  // open: clr
  or or_1 (or_1_out, Write0, L0);
  or or_2 (or_2_out, Write1, L1);
  or or_3 (or_3_out, Write2, L2);
  or or_4 (or_4_out, Write3, L3);
  or or_5 (or_5_out, Write4, L4);
  or or_6 (or_6_out, Write5, L5);
  or or_7 (or_7_out, Write6, L6);
  or or_8 (or_8_out, Write7, L7);
  Counter #(.width(32), .max('hffffffff), .ongoal("wrap"), .trigger("rising"), .behavior("new")) counter_1 (
    .Q(C0), .clk(CLK), .clr(d_ff_1_q));  // open: load, D, count, carry, preset, down
  D_Flip_Flop #(.trigger("rising"), .Pre_Clr_Positions("LEGACY"), .NegatePresetClear("false"), .enable("true"), .NewFFLayout("false")) d_ff_1 (
    .clk(CLK), .D(or_1_out), .Q(d_ff_1_q));  // open: Qn, preset, en, reset
  Counter #(.width(32), .max('hffffffff), .ongoal("wrap"), .trigger("rising"), .behavior("new")) counter_2 (
    .Q(C1), .clk(CLK), .clr(d_ff_2_q));  // open: load, D, count, carry, preset, down
  D_Flip_Flop #(.trigger("rising"), .Pre_Clr_Positions("LEGACY"), .NegatePresetClear("false"), .enable("true"), .NewFFLayout("false")) d_ff_2 (
    .clk(CLK), .D(or_2_out), .Q(d_ff_2_q));  // open: Qn, preset, en, reset
  Counter #(.width(32), .max('hffffffff), .ongoal("wrap"), .trigger("rising"), .behavior("new")) counter_3 (
    .Q(C2), .clk(CLK), .clr(d_ff_3_q));  // open: load, D, count, carry, preset, down
  D_Flip_Flop #(.trigger("rising"), .Pre_Clr_Positions("LEGACY"), .NegatePresetClear("false"), .enable("true"), .NewFFLayout("false")) d_ff_3 (
    .clk(CLK), .D(or_3_out), .Q(d_ff_3_q));  // open: Qn, preset, en, reset
  Counter #(.width(32), .max('hffffffff), .ongoal("wrap"), .trigger("rising"), .behavior("new")) counter_4 (
    .Q(C3), .clk(CLK), .clr(d_ff_4_q));  // open: load, D, count, carry, preset, down
  D_Flip_Flop #(.trigger("rising"), .Pre_Clr_Positions("LEGACY"), .NegatePresetClear("false"), .enable("true"), .NewFFLayout("false")) d_ff_4 (
    .clk(CLK), .D(or_4_out), .Q(d_ff_4_q));  // open: Qn, preset, en, reset
  Counter #(.width(32), .max('hffffffff), .ongoal("wrap"), .trigger("rising"), .behavior("new")) counter_5 (
    .Q(C4), .clk(CLK), .clr(d_ff_5_q));  // open: load, D, count, carry, preset, down
  D_Flip_Flop #(.trigger("rising"), .Pre_Clr_Positions("LEGACY"), .NegatePresetClear("false"), .enable("true"), .NewFFLayout("false")) d_ff_5 (
    .clk(CLK), .D(or_5_out), .Q(d_ff_5_q));  // open: Qn, preset, en, reset
  Counter #(.width(32), .max('hffffffff), .ongoal("wrap"), .trigger("rising"), .behavior("new")) counter_6 (
    .Q(C5), .clk(CLK), .clr(d_ff_6_q));  // open: load, D, count, carry, preset, down
  D_Flip_Flop #(.trigger("rising"), .Pre_Clr_Positions("LEGACY"), .NegatePresetClear("false"), .enable("true"), .NewFFLayout("false")) d_ff_6 (
    .clk(CLK), .D(or_6_out), .Q(d_ff_6_q));  // open: Qn, preset, en, reset
  Counter #(.width(32), .max('hffffffff), .ongoal("wrap"), .trigger("rising"), .behavior("new")) counter_7 (
    .Q(C6), .clk(CLK), .clr(d_ff_7_q));  // open: load, D, count, carry, preset, down
  D_Flip_Flop #(.trigger("rising"), .Pre_Clr_Positions("LEGACY"), .NegatePresetClear("false"), .enable("true"), .NewFFLayout("false")) d_ff_7 (
    .clk(CLK), .D(or_7_out), .Q(d_ff_7_q));  // open: Qn, preset, en, reset
  Counter #(.width(32), .max('hffffffff), .ongoal("wrap"), .trigger("rising"), .behavior("new")) counter_8 (
    .Q(C7), .clk(CLK), .clr(d_ff_8_q));  // open: load, D, count, carry, preset, down
  D_Flip_Flop #(.trigger("rising"), .Pre_Clr_Positions("LEGACY"), .NegatePresetClear("false"), .enable("true"), .NewFFLayout("false")) d_ff_8 (
    .clk(CLK), .D(or_8_out), .Q(d_ff_8_q));  // open: Qn, preset, en, reset
  Register #(.width(32), .trigger("rising"), .Select("low")) register_17 (
    .D(EX_BranchAddr), .en(Write0), .Q(register_17_q), .clk(CLK));  // open: clr
  assign JumpAddr = L0 ? register_17_q : 32'bz;  // Controlled_Buffer controlled_buffer_1
  assign JumpAddr = L1 ? register_18_q : 32'bz;  // Controlled_Buffer controlled_buffer_2
  Register #(.width(32), .trigger("rising"), .Select("low")) register_18 (
    .D(EX_BranchAddr), .en(Write1), .Q(register_18_q), .clk(CLK));  // open: clr
  Register #(.width(32), .trigger("rising"), .Select("low")) register_19 (
    .D(EX_BranchAddr), .en(Write2), .Q(register_19_q), .clk(CLK));  // open: clr
  assign JumpAddr = L2 ? register_19_q : 32'bz;  // Controlled_Buffer controlled_buffer_3
  assign JumpAddr = L3 ? register_20_q : 32'bz;  // Controlled_Buffer controlled_buffer_4
  Register #(.width(32), .trigger("rising"), .Select("low")) register_20 (
    .D(EX_BranchAddr), .en(Write3), .Q(register_20_q), .clk(CLK));  // open: clr
  Register #(.width(32), .trigger("rising"), .Select("low")) register_21 (
    .D(EX_BranchAddr), .en(Write4), .Q(register_21_q), .clk(CLK));  // open: clr
  assign JumpAddr = L4 ? register_21_q : 32'bz;  // Controlled_Buffer controlled_buffer_5
  Register #(.width(32), .trigger("rising"), .Select("low")) register_22 (
    .D(EX_BranchAddr), .en(Write5), .Q(register_22_q), .clk(CLK));  // open: clr
  assign JumpAddr = L5 ? register_22_q : 32'bz;  // Controlled_Buffer controlled_buffer_6
  Register #(.width(32), .trigger("rising"), .Select("low")) register_23 (
    .D(EX_BranchAddr), .en(Write6), .Q(register_23_q), .clk(CLK));  // open: clr
  assign JumpAddr = L6 ? register_23_q : 32'bz;  // Controlled_Buffer controlled_buffer_7
  assign JumpAddr = L7 ? register_24_q : 32'bz;  // Controlled_Buffer controlled_buffer_8
  Register #(.width(32), .trigger("rising"), .Select("low")) register_24 (
    .D(EX_BranchAddr), .en(Write7), .Q(register_24_q), .clk(CLK));  // open: clr
  PredictFSM predictfsm_1 (
    .High(Predict0[1]), .Low(Predict0[0]), .Jump(EX_BranchTaken), .High_2(predictfsm_1_low_2[1]),
    .Low_2(predictfsm_1_low_2[0]));
  PredictFSM predictfsm_2 (
    .High(Predict1[1]), .Low(Predict1[0]), .Jump(EX_BranchTaken), .High_2(predictfsm_2_low_2[1]),
    .Low_2(predictfsm_2_low_2[0]));
  PredictFSM predictfsm_3 (
    .High(Predict2[1]), .Low(Predict2[0]), .Jump(EX_BranchTaken), .High_2(predictfsm_3_low_2[1]),
    .Low_2(predictfsm_3_low_2[0]));
  PredictFSM predictfsm_4 (
    .High(Predict3[1]), .Low(Predict3[0]), .Jump(EX_BranchTaken), .High_2(predictfsm_4_low_2[1]),
    .Low_2(predictfsm_4_low_2[0]));
  PredictFSM predictfsm_5 (
    .High(Predict4[1]), .Low(Predict4[0]), .Jump(EX_BranchTaken), .High_2(predictfsm_5_low_2[1]),
    .Low_2(predictfsm_5_low_2[0]));
  PredictFSM predictfsm_6 (
    .High(Predict5[1]), .Low(Predict5[0]), .Jump(EX_BranchTaken), .High_2(predictfsm_6_low_2[1]),
    .Low_2(predictfsm_6_low_2[0]));
  PredictFSM predictfsm_7 (
    .High(Predict6[1]), .Low(Predict6[0]), .Jump(EX_BranchTaken), .High_2(predictfsm_7_low_2[1]),
    .Low_2(predictfsm_7_low_2[0]));
  PredictFSM predictfsm_8 (
    .High(Predict7[1]), .Low(Predict7[0]), .Jump(EX_BranchTaken), .High_2(predictfsm_8_low_2[1]),
    .Low_2(predictfsm_8_low_2[0]));
  and and_1 (and_1_out, M0, EX_Branch);
  and and_2 (and_2_out, M1, EX_Branch);
  and and_3 (and_3_out, M2, EX_Branch);
  and and_4 (and_4_out, M3, EX_Branch);
  and and_5 (and_5_out, M4, EX_Branch);
  and and_6 (and_6_out, M5, EX_Branch);
  and and_7 (and_7_out, M6, EX_Branch);
  and and_8 (and_8_out, M7, EX_Branch);
  Register #(.width(2), .trigger("rising"), .Select("low")) register_25 (
    .D(predictfsm_1_low_2), .en(and_1_out), .Q(Predict0), .clk(CLK));  // open: clr
  Register #(.width(2), .trigger("rising"), .Select("low")) register_26 (
    .D(predictfsm_2_low_2), .en(and_2_out), .Q(Predict1), .clk(CLK));  // open: clr
  Register #(.width(2), .trigger("rising"), .Select("low")) register_27 (
    .D(predictfsm_3_low_2), .en(and_3_out), .Q(Predict2), .clk(CLK));  // open: clr
  Register #(.width(2), .trigger("rising"), .Select("low")) register_28 (
    .D(predictfsm_4_low_2), .en(and_4_out), .Q(Predict3), .clk(CLK));  // open: clr
  Register #(.width(2), .trigger("rising"), .Select("low")) register_29 (
    .D(predictfsm_5_low_2), .en(and_5_out), .Q(Predict4), .clk(CLK));  // open: clr
  Register #(.width(2), .trigger("rising"), .Select("low")) register_30 (
    .D(predictfsm_6_low_2), .en(and_6_out), .Q(Predict5), .clk(CLK));  // open: clr
  Register #(.width(2), .trigger("rising"), .Select("low")) register_31 (
    .D(predictfsm_7_low_2), .en(and_7_out), .Q(Predict6), .clk(CLK));  // open: clr
  Register #(.width(2), .trigger("rising"), .Select("low")) register_32 (
    .D(predictfsm_8_low_2), .en(and_8_out), .Q(Predict7), .clk(CLK));  // open: clr
  assign {PredictJump, controlled_buffer_9_out[0]} = L0 ? Predict0 : 2'bz;  // Controlled_Buffer controlled_buffer_9
  assign {PredictJump, controlled_buffer_10_out[0]} = L1 ? Predict1 : 2'bz;  // Controlled_Buffer controlled_buffer_10
  assign {PredictJump, controlled_buffer_11_out[0]} = L2 ? Predict2 : 2'bz;  // Controlled_Buffer controlled_buffer_11
  assign {PredictJump, controlled_buffer_12_out[0]} = L3 ? Predict3 : 2'bz;  // Controlled_Buffer controlled_buffer_12
  assign {PredictJump, controlled_buffer_13_out[0]} = L4 ? Predict4 : 2'bz;  // Controlled_Buffer controlled_buffer_13
  assign {PredictJump, controlled_buffer_14_out[0]} = L5 ? Predict5 : 2'bz;  // Controlled_Buffer controlled_buffer_14
  assign {PredictJump, controlled_buffer_15_out[0]} = L6 ? Predict6 : 2'bz;  // Controlled_Buffer controlled_buffer_15
  assign {PredictJump, controlled_buffer_16_out[0]} = L7 ? Predict7 : 2'bz;  // Controlled_Buffer controlled_buffer_16
  Pull_Resistor #(.pull(0)) pull_resistor_1 (.node(PredictJump));
  Comparator #(.width(32), .mode("twosComplement")) comparator_1 (
    .a(EX_PC), .b(Tag0), .eq(comparator_1_eq));  // open: gt, lt
  Comparator #(.width(32), .mode("twosComplement")) comparator_2 (
    .a(EX_PC), .b(Tag1), .eq(comparator_2_eq));  // open: gt, lt
  Comparator #(.width(32), .mode("twosComplement")) comparator_3 (
    .a(EX_PC), .b(Tag2), .eq(comparator_3_eq));  // open: gt, lt
  Comparator #(.width(32), .mode("twosComplement")) comparator_4 (
    .a(EX_PC), .b(Tag3), .eq(comparator_4_eq));  // open: gt, lt
  Comparator #(.width(32), .mode("twosComplement")) comparator_5 (
    .a(EX_PC), .b(Tag4), .eq(comparator_5_eq));  // open: gt, lt
  Comparator #(.width(32), .mode("twosComplement")) comparator_6 (
    .a(EX_PC), .b(Tag5), .eq(comparator_6_eq));  // open: gt, lt
  Comparator #(.width(32), .mode("twosComplement")) comparator_7 (
    .a(EX_PC), .b(Tag6), .eq(comparator_7_eq));  // open: gt, lt
  Comparator #(.width(32), .mode("twosComplement")) comparator_8 (
    .a(EX_PC), .b(Tag7), .eq(comparator_8_eq));  // open: gt, lt
  and and_9 (M0, comparator_1_eq, v0);
  and and_10 (M1, comparator_2_eq, v1);
  and and_11 (M2, comparator_3_eq, v2);
  and and_12 (M3, comparator_4_eq, v3);
  and and_13 (M4, comparator_5_eq, v4);
  and and_14 (M5, comparator_6_eq, v5);
  and and_15 (M6, comparator_7_eq, v6);
  and and_16 (M7, comparator_8_eq, v7);
  or or_9 (EX_Hit, M0, M1, M2, M3, M4, M5, M6, M7);
  Comparator #(.width(32), .mode("twosComplement")) comparator_9 (
    .a(PC), .b(Tag0), .eq(comparator_9_eq));  // open: gt, lt
  Comparator #(.width(32), .mode("twosComplement")) comparator_10 (
    .a(PC), .b(Tag1), .eq(comparator_10_eq));  // open: gt, lt
  Comparator #(.width(32), .mode("twosComplement")) comparator_11 (
    .a(PC), .b(Tag2), .eq(comparator_11_eq));  // open: gt, lt
  Comparator #(.width(32), .mode("twosComplement")) comparator_12 (
    .a(PC), .b(Tag3), .eq(comparator_12_eq));  // open: gt, lt
  Comparator #(.width(32), .mode("twosComplement")) comparator_13 (
    .a(PC), .b(Tag4), .eq(comparator_13_eq));  // open: gt, lt
  Comparator #(.width(32), .mode("twosComplement")) comparator_14 (
    .a(PC), .b(Tag5), .eq(comparator_14_eq));  // open: gt, lt
  Comparator #(.width(32), .mode("twosComplement")) comparator_15 (
    .a(PC), .b(Tag6), .eq(comparator_15_eq));  // open: gt, lt
  Comparator #(.width(32), .mode("twosComplement")) comparator_16 (
    .a(PC), .b(Tag7), .eq(comparator_16_eq));  // open: gt, lt
  not not_1 (EX_Miss, EX_Hit);
  and and_17 (L0, comparator_9_eq, v0);
  and and_18 (L1, comparator_10_eq, v1);
  and and_19 (L2, comparator_11_eq, v2);
  and and_20 (L3, comparator_12_eq, v3);
  and and_21 (L4, comparator_13_eq, v4);
  and and_22 (L5, comparator_14_eq, v5);
  and and_23 (L6, comparator_15_eq, v6);
  and and_24 (L7, comparator_16_eq, v7);
  not not_2 (not_2_out, v0);
  not not_3 (not_3_out, v1);
  not not_4 (not_4_out, v2);
  not not_5 (not_5_out, v3);
  not not_6 (not_6_out, v4);
  not not_7 (not_7_out, v5);
  not not_8 (not_8_out, v6);
  not not_9 (not_9_out, v7);
  MAX max_1 (.X(C0), .XId(3'b000), .Y(C1), .YId(3'b001), .Max(max_1_max), .MaxId(max_1_maxid));
  MAX max_2 (.X(C2), .XId(3'b010), .Y(C3), .YId(3'b011), .Max(max_2_max), .MaxId(max_2_maxid));
  MAX max_3 (.X(C4), .XId(3'b100), .Y(C5), .YId(3'b101), .Max(max_3_max), .MaxId(max_3_maxid));
  MAX max_4 (.X(C6), .XId(3'b110), .Y(C7), .YId(3'b111), .Max(max_4_max), .MaxId(max_4_maxid));
  Priority_Encoder #(.select(3), .disabled("Z")) priority_encoder_1 (
    .in0(not_2_out), .in1(not_3_out), .in2(not_4_out), .in3(not_5_out), .in4(not_6_out), .in5(not_7_out),
    .in6(not_8_out), .in7(not_9_out), .out(priority_encoder_1_out), .gs(priority_encoder_1_gs));  // open: en_out, en_in
  MAX max_5 (.X(max_1_max), .XId(max_1_maxid), .Y(max_2_max), .YId(max_2_maxid), .Max(max_5_max), .MaxId(max_5_maxid));
  MAX max_6 (.X(max_3_max), .XId(max_3_maxid), .Y(max_4_max), .YId(max_4_maxid), .Max(max_6_max), .MaxId(max_6_maxid));
  and and_25 (and_25_out, v0, v1, v2, v3, v4, v5, v6, v7);
  Decoder #(.select(3), .tristate("false"), .disabled(0), .enable("true")) decoder_1 (
    .out0(decoder_1_out0), .out1(decoder_1_out1), .out2(decoder_1_out2), .out3(decoder_1_out3),
    .out4(decoder_1_out4), .out5(decoder_1_out5), .out6(decoder_1_out6), .out7(decoder_1_out7),
    .sel(priority_encoder_1_out), .en(priority_encoder_1_gs));
  Demultiplexer #(.select(3), .width(1), .tristate("false"), .disabled("Z"), .enable("false")) demultiplexer_1 (
    .out0(demultiplexer_1_out0), .out1(demultiplexer_1_out1), .out2(demultiplexer_1_out2),
    .out3(demultiplexer_1_out3), .out4(demultiplexer_1_out4), .out5(demultiplexer_1_out5),
    .out6(demultiplexer_1_out6), .out7(demultiplexer_1_out7), .in(and_25_out), .sel(max_7_maxid));
  MAX max_7 (.X(max_5_max), .XId(max_5_maxid), .Y(max_6_max), .YId(max_6_maxid), .MaxId(max_7_maxid));  // open: Max
  or or_10 (or_10_out, decoder_1_out0, demultiplexer_1_out0);
  or or_11 (or_11_out, decoder_1_out1, demultiplexer_1_out1);
  or or_12 (or_12_out, decoder_1_out2, demultiplexer_1_out2);
  or or_13 (or_13_out, decoder_1_out3, demultiplexer_1_out3);
  or or_14 (or_14_out, decoder_1_out4, demultiplexer_1_out4);
  or or_15 (or_15_out, decoder_1_out5, demultiplexer_1_out5);
  or or_16 (or_16_out, decoder_1_out6, demultiplexer_1_out6);
  or or_17 (or_17_out, decoder_1_out7, demultiplexer_1_out7);
  and and_26 (Write0, or_10_out, EX_Branch, EX_Miss);
  and and_27 (Write1, or_11_out, EX_Branch, EX_Miss);
  and and_28 (Write2, or_12_out, EX_Branch, EX_Miss);
  and and_29 (Write3, or_13_out, EX_Branch, EX_Miss);
  and and_30 (Write4, or_14_out, EX_Branch, EX_Miss);
  and and_31 (Write5, or_15_out, EX_Branch, EX_Miss);
  and and_32 (Write6, or_16_out, EX_Branch, EX_Miss);
  and and_33 (Write7, or_17_out, EX_Branch, EX_Miss);

  // Other names for the same wires on the sheet: Tag[31:0] = EX_PC
endmodule

module MAX (
  input  [31:0] X,
  input  [2:0] XId,
  input  [31:0] Y,
  input  [2:0] YId,
  output [31:0] Max,
  output [2:0] MaxId
);

  wire comparator_1_eq, comparator_1_lt, or_1_out;

  Comparator #(.width(32), .mode("twosComplement")) comparator_1 (
    .a(X), .b(Y), .eq(comparator_1_eq), .lt(comparator_1_lt));  // open: gt
  or or_1 (or_1_out, comparator_1_eq, comparator_1_lt);
  Multiplexer #(.select(1), .width(32), .disabled("Z"), .enable("false")) multiplexer_1 (
    .in0(X), .in1(Y), .out(Max), .sel(or_1_out));
  Multiplexer #(.select(1), .width(3), .disabled("Z"), .enable("false")) multiplexer_2 (
    .in0(XId), .in1(YId), .out(MaxId), .sel(or_1_out));
endmodule

module PredictFSM (
  input  High,
  input  Low,
  input  Jump,
  output High_2,
  output Low_2
);

  wire and_1_out, and_2_out, and_3_out, and_4_out, not_1_out, not_2_out, not_3_out, not_4_out, not_5_out;

  not not_1 (not_1_out, Low);
  not not_2 (not_2_out, High);
  not not_3 (not_3_out, Low);
  not not_4 (not_4_out, Low);
  not not_5 (not_5_out, Jump);
  and and_1 (and_1_out, Low, Jump);
  and and_2 (and_2_out, High, not_1_out);
  and and_3 (and_3_out, not_2_out, not_3_out, Jump);
  and and_4 (and_4_out, High, not_4_out, not_5_out);
  or or_1 (High_2, and_1_out, and_2_out);
  or or_2 (Low_2, and_3_out, and_4_out);
endmodule
